// Logisim project CPU.circ as structural Verilog: 28 circuits, main circuit build_2
module build_2 (
  input  pwr,
  input  reset,
  input  irq,
  input  nmi
);

  wire and_1_out, and_2_out, and_3_out, and_4_out, and_9_out, and_10_out, and_11_out, and_12_out,
       cleaned_build_2_1_r_w_mode, clock_1_out, clock_2_out, clock_3_out, clock_4_out, clock_5_out,
       decoder_1_out11, decoder_1_out15, hight_mem_enable, io_interface_enable, low_mem_activate, not_1_out,
       not_2_out, not_3_out, not_4_out, not_5_out, not_6_out, not_7_out, not_8_out, not_9_out, not_10_out,
       not_11_out, not_12_out, or_1_out, or_2_out, system_memory_enable;
  wire [7:0] cleaned_build_2_1_d_bus_out, controlled_buffer_1_out, controlled_buffer_3_out,
       controlled_buffer_5_out, controlled_buffer_6_out, h_ram_b_1_dout, h_ram_b_2_dout,
       out_devices_1_port_b, ram_1_dout, rom_1_data;
  wire [15:0] controlled_buffer_2_out;
  wire [18:0] decoder_1_out14;
  wire [18:16] decoder_1_out10;

  Clock clock_1 (.out(clock_1_out));
  and and_1 (and_1_out, cleaned_build_2_1_r_w_mode, low_mem_activate);
  Clock clock_2 (.out(clock_2_out));
  assign controlled_buffer_1_out = low_mem_activate ? cleaned_build_2_1_d_bus_out : 8'bz;  // Controlled_Buffer controlled_buffer_1
  assign controlled_buffer_2_out = system_memory_enable ? decoder_1_out14[15:0] : 16'bz;  // Controlled_Buffer controlled_buffer_2
  not not_1 (not_1_out, decoder_1_out14[10]);
  not not_2 (not_2_out, decoder_1_out14[11]);
  not not_3 (not_3_out, decoder_1_out14[12]);
  not not_4 (not_4_out, decoder_1_out14[13]);
  not not_5 (not_5_out, decoder_1_out14[15]);
  not not_6 (not_6_out, decoder_1_out14[13]);
  not not_7 (not_7_out, decoder_1_out14[12]);
  and and_2 (and_2_out, not_5_out, not_6_out, not_7_out);
  RAM #(.addrWidth(14), .enables("line")) ram_1 (
    .addr(decoder_1_out14[13:0]), .we(and_1_out), .clk(clock_2_out), .din(controlled_buffer_1_out),
    .dout(ram_1_dout));
  ROM #(.addrWidth(16)) rom_1 (.addr(controlled_buffer_2_out), .data(rom_1_data));
  and and_3 (and_3_out, not_2_out, not_1_out, not_3_out, not_4_out);
  not not_8 (not_8_out, decoder_1_out14[14]);
  not not_9 (not_9_out, decoder_1_out14[15]);
  and and_4 (and_4_out, decoder_1_out14[14], not_9_out);
  and and_5 (low_mem_activate, not_8_out, not_9_out);
  and and_6 (io_interface_enable, and_4_out, and_3_out);
  not not_10 (not_10_out, low_mem_activate);
  not not_11 (not_11_out, io_interface_enable);
  and and_7 (hight_mem_enable, and_9_out, and_2_out);
  and and_8 (system_memory_enable, and_9_out, not_12_out);
  not not_12 (not_12_out, hight_mem_enable);
  cleaned_build_2 cleaned_build_2_1 (
    .startup(pwr), .clock(clock_1_out), .nmi(nmi), .irq(irq), .reset(reset),
    .d_bus_in(controlled_buffer_3_out), .d_bus_out(cleaned_build_2_1_d_bus_out),
    .r_w_mode(cleaned_build_2_1_r_w_mode), .adr(decoder_1_out14[15:0]));
  and and_9 (and_9_out, not_10_out, not_11_out);
  assign controlled_buffer_3_out = low_mem_activate ? ram_1_dout : 8'bz;  // Controlled_Buffer controlled_buffer_3
  assign controlled_buffer_3_out = system_memory_enable ? rom_1_data : 8'bz;  // Controlled_Buffer controlled_buffer_4
  Clock clock_3 (.out(clock_3_out));
  and and_10 (and_10_out, hight_mem_enable, out_devices_1_port_b[4]);
  Decoder #(.select(4)) decoder_1 (
    .out8(decoder_1_out10[18]), .out9(decoder_1_out10[17]), .out10(decoder_1_out10[16]),
    .out11(decoder_1_out11), .out12(decoder_1_out14[18]), .out13(decoder_1_out14[17]),
    .out14(decoder_1_out14[16]), .out15(decoder_1_out15), .sel(out_devices_1_port_b[3:0]), .en(and_10_out));  // open: out0, out1, out2, out3, out4, out5, out6, out7
  or or_1 (or_1_out, decoder_1_out11, decoder_1_out10[16], decoder_1_out10[17], decoder_1_out10[18]);
  and and_11 (and_11_out, cleaned_build_2_1_r_w_mode, or_2_out);
  Clock clock_4 (.out(clock_4_out));
  and and_12 (and_12_out, cleaned_build_2_1_r_w_mode, or_1_out);
  Clock clock_5 (.out(clock_5_out));
  out_devices out_devices_1 (
    .enable(io_interface_enable), .we(cleaned_build_2_1_r_w_mode), .clock(clock_3_out),
    .data_in(cleaned_build_2_1_d_bus_out), .address_io(decoder_1_out14[7:0]), .port_b(out_devices_1_port_b));  // open: port_a, port_c, port_d, port_e, port_f, port_g, port_h, port_i
  or or_2 (or_2_out, decoder_1_out15, decoder_1_out14[16], decoder_1_out14[17], decoder_1_out14[18]);
  RAM #(.addrWidth(19), .enables("line")) h_ram_b_1 (
    .addr(decoder_1_out14), .we(and_11_out), .clk(clock_4_out), .din(controlled_buffer_5_out),
    .dout(h_ram_b_1_dout));
  assign controlled_buffer_5_out = or_2_out ? cleaned_build_2_1_d_bus_out : 8'bz;  // Controlled_Buffer controlled_buffer_5
  RAM #(.addrWidth(19), .enables("line")) h_ram_b_2 (
    .addr({decoder_1_out10, decoder_1_out14[15:0]}), .we(and_12_out), .clk(clock_5_out),
    .din(controlled_buffer_6_out), .dout(h_ram_b_2_dout));
  assign controlled_buffer_6_out = or_1_out ? cleaned_build_2_1_d_bus_out : 8'bz;  // Controlled_Buffer controlled_buffer_6
  assign controlled_buffer_3_out = or_2_out ? h_ram_b_1_dout : 8'bz;  // Controlled_Buffer controlled_buffer_7
  assign controlled_buffer_3_out = or_1_out ? h_ram_b_2_dout : 8'bz;  // Controlled_Buffer controlled_buffer_8
endmodule

module main (
  input  pwr,
  input  nmi,
  input  irq,
  input  reset
);

  wire and_1_out, and_2_out, and_3_out, and_4_out, cleaned_build_2_1_r_w_mode, clock_1_out, clock_2_out,
       not_1_out, not_2_out, not_3_out;
  wire [5:0] video_card_1_x_coordinate, video_card_1_y_coordinate;
  wire [7:0] buffer_1_out, cleaned_build_2_1_d_bus_out, controlled_buffer_2_out, controlled_buffer_4_out,
       out_devices_1_port_a, out_devices_1_port_b, out_devices_1_port_c, out_devices_1_port_d,
       out_devices_1_port_e, out_devices_1_port_f, out_devices_1_port_g, out_devices_1_port_h,
       out_devices_1_port_i, ram_1_dout, rom_1_data, video_card_1_frame_buffer;
  wire [15:0] cleaned_build_2_1_adr, controlled_buffer_1_out, controlled_buffer_3_out;

  Clock clock_1 (.out(clock_1_out));
  cleaned_build_2 cleaned_build_2_1 (
    .startup(pwr), .clock(clock_1_out), .nmi(nmi), .irq(irq), .reset(reset),
    .d_bus_in(controlled_buffer_4_out), .d_bus_out(cleaned_build_2_1_d_bus_out),
    .r_w_mode(cleaned_build_2_1_r_w_mode), .adr(cleaned_build_2_1_adr));
  not not_1 (not_1_out, cleaned_build_2_1_adr[15]);
  assign controlled_buffer_1_out = and_1_out ? {2'b00, cleaned_build_2_1_adr[13:0]} : 16'bz;  // Controlled_Buffer controlled_buffer_1
  RAM #(.addrWidth(16), .enables("line")) ram_1 (
    .addr(controlled_buffer_1_out), .we(cleaned_build_2_1_r_w_mode), .clk(clock_1_out),
    .din(controlled_buffer_2_out), .dout(ram_1_dout));
  assign controlled_buffer_2_out = and_1_out ? cleaned_build_2_1_d_bus_out : 8'bz;  // Controlled_Buffer controlled_buffer_2
  not not_2 (not_2_out, cleaned_build_2_1_adr[14]);
  and and_1 (and_1_out, not_2_out, not_3_out);
  not not_3 (not_3_out, cleaned_build_2_1_adr[15]);
  and and_2 (and_2_out, cleaned_build_2_1_adr[14], not_1_out);
  ROM #(.addrWidth(16)) rom_1 (.addr(controlled_buffer_3_out), .data(rom_1_data));
  assign controlled_buffer_3_out = cleaned_build_2_1_adr[15] ? cleaned_build_2_1_adr : 16'bz;  // Controlled_Buffer controlled_buffer_3
  assign buffer_1_out = cleaned_build_2_1_d_bus_out;  // Buffer buffer_1, 8 bits wide
  and and_3 (and_3_out, and_2_out, cleaned_build_2_1_r_w_mode);
  assign controlled_buffer_4_out = and_1_out ? ram_1_dout : 8'bz;  // Controlled_Buffer controlled_buffer_4
  assign controlled_buffer_4_out = cleaned_build_2_1_adr[15] ? rom_1_data : 8'bz;  // Controlled_Buffer controlled_buffer_5
  DotMatrix #(.matrixcols(8), .matrixrows(1)) dotmatrix_1 (
    .col0(out_devices_1_port_h[7]), .col1(out_devices_1_port_h[6]), .col2(out_devices_1_port_h[5]),
    .col3(out_devices_1_port_h[4]), .col4(out_devices_1_port_h[3]), .col5(out_devices_1_port_h[2]),
    .col6(out_devices_1_port_h[1]), .col7(out_devices_1_port_h[0]));
  out_devices out_devices_1 (
    .enable(and_2_out), .we(cleaned_build_2_1_r_w_mode), .clock(clock_1_out), .data_in(buffer_1_out),
    .address_io(cleaned_build_2_1_adr[7:0]), .port_a(out_devices_1_port_a), .port_b(out_devices_1_port_b),
    .port_c(out_devices_1_port_c), .port_d(out_devices_1_port_d), .port_e(out_devices_1_port_e),
    .port_f(out_devices_1_port_f), .port_g(out_devices_1_port_g), .port_h(out_devices_1_port_h),
    .port_i(out_devices_1_port_i));
  Clock clock_2 (.out(clock_2_out));
  and and_4 (and_4_out, 1'b1, out_devices_1_port_h[0]);
  Hex_Digit_Display hex_digit_display_1 (.value(out_devices_1_port_f[7:4]));  // open: dp
  Hex_Digit_Display hex_digit_display_2 (.value(out_devices_1_port_f[3:0]));  // open: dp
  Hex_Digit_Display hex_digit_display_3 (.value(out_devices_1_port_a[7:4]));  // open: dp
  Hex_Digit_Display hex_digit_display_4 (.value(out_devices_1_port_b[7:4]));  // open: dp
  Hex_Digit_Display hex_digit_display_5 (.value(out_devices_1_port_c[7:4]));  // open: dp
  Hex_Digit_Display hex_digit_display_6 (.value(out_devices_1_port_g[7:4]));  // open: dp
  Hex_Digit_Display hex_digit_display_7 (.value(out_devices_1_port_g[3:0]));  // open: dp
  Hex_Digit_Display hex_digit_display_8 (.value(out_devices_1_port_a[3:0]));  // open: dp
  Hex_Digit_Display hex_digit_display_9 (.value(out_devices_1_port_b[3:0]));  // open: dp
  Hex_Digit_Display hex_digit_display_10 (.value(out_devices_1_port_c[3:0]));  // open: dp
  video_card video_card_1 (
    .buffer_in(out_devices_1_port_d), .x_co(out_devices_1_port_f), .y_co(out_devices_1_port_g),
    .mode(out_devices_1_port_e), .frame_buffer(video_card_1_frame_buffer),
    .x_coordinate(video_card_1_x_coordinate), .y_coordinate(video_card_1_y_coordinate));  // open: clock
  // RGB_Video #(.cursor("No Cursor"), .height(64), .scale(5), .width(64)) rgb_video_1: pin names not known; wires that end beside it: clock_2_out, and_4_out, video_card_1_x_coordinate, video_card_1_y_coordinate, video_card_1_frame_buffer
  TTY #(.cols(60), .rows(10)) tty_1 (.data(out_devices_1_port_i[6:0]), .clk(clock_2_out), .we(and_3_out), .clr(1'b0));

  // Notes on the sheet:
  //   contents of rom_1 (hex, n*v repeats v):
  //   32768*0 18 d8 b8 58 a2 0 a0 b a9 0 bd 4a 80 95 50 e8 88 c0 0 d0 f5 a9 50 85 0 a2 b a0 0 b1 0 8d 8 60
  //   c8 ca e0 0 d0 f5 bd 56 80 95 50 e8 88 c0 0 d0 f5 a9 50 85 0 a2 b a0 0 b1 0 8d 8 60 c8 ca e0 0 d0 f5
  //   ea 4c 46 80 48 65 6c 6c 6f 20 57 6f 72 6c 64 0 43 69 61 6f 20 4d 6f 6e 64 6f 32669*0 80
  //   X
  //   Y
  //   PORT_A
  //   PORT_B
  //   PORT_C
endmodule

module cleaned_build (
  input  hidle,
  input  startup,
  input  clock,
  input  nmi,
  input  irq,
  input  reset,
  input  [7:0] d_bus_in,
  output [7:0] d_bus_out,
  output r_w_mode,
  output [15:0] adr
);

  wire address_bus_control_1_disable_other, address_bus_control_1_disable_pc,
       address_bus_control_2_disable_other, address_bus_control_2_disable_pc, and_1_out, and_2_out,
       costant_register_1_b_out, costant_register_1_c_out, costant_register_1_d_out,
       costant_register_1_irq_out, costant_register_1_n_out, costant_register_1_o_out,
       costant_register_1_z_out, cu_final_1_irq_detect, cu_final_1_nmi_detect, cu_final_1_reset_detect,
       cu_final_1_startup, irq_disable, not_1_out, not_2_out, not_3_out, not_4_out, or_1_out, or_2_out,
       or_3_out, or_4_out, or_5_out, or_6_out, or_7_out, or_8_out, or_9_out, rom2_decoder_1_inc_reg_by_2,
       rom2_decoder_1_pc_count, rom2_decoder_1_pc_load_from_adr, rom2_decoder_1_pc_load_reg,
       rom2_decoder_1_pc_oe, rom2_decoder_1_pch_bus, rom2_decoder_1_pch_load, rom2_decoder_1_pcl_bus,
       rom2_decoder_1_pcl_load, rom2_decoder_1_sp_dec, rom2_decoder_1_sp_inc, rom2_decoder_1_sp_oe,
       rom2_decoder_1_sp_reset, rom2_decoder_1_sp_to_bus, rom_1_demux_module_1_brk_data,
       rom_1_demux_module_1_brk_update, rom_1_demux_module_1_carry_data, rom_1_demux_module_1_carry_update,
       rom_1_demux_module_1_data_bus_in, rom_1_demux_module_1_deciamal_data,
       rom_1_demux_module_1_decimal_update, rom_1_demux_module_1_dlatch_h_oe_abh,
       rom_1_demux_module_1_dlatch_h_out_dbus, rom_1_demux_module_1_dlatch_h_we,
       rom_1_demux_module_1_dlatch_oe_abl, rom_1_demux_module_1_dlatch_out_dbus,
       rom_1_demux_module_1_dlatch_we, rom_1_demux_module_1_interrupt_disable_data,
       rom_1_demux_module_1_interrupt_update, rom_1_demux_module_1_isr_block,
       rom_1_demux_module_1_overflow_data, rom_1_demux_module_1_overflow_update,
       rom_1_demux_module_1_pch_load, rom_1_demux_module_1_pcl_load,
       rom_1_demux_module_1_status_input_enable, rom_1_demux_module_1_status_reset,
       rom_1_demux_module_1_status_to_bus, rom_3_decoder_1_alu_a_we, rom_3_decoder_1_alu_oe,
       rom_3_decoder_1_cmp_active, rom_3_decoder_1_inc, rom_3_decoder_1_load_c, rom_3_decoder_1_sub_actived,
       rom_3_decoder_1_sum_actived, rom_3_decoder_1_sum_actived_16b;
  wire [2:0] rom2_decoder_1_alu_b_in;
  wire [3:0] alu_test_1_alu_control_status, alu_test_1_alu_status;
  wire [6:0] costant_register_1_negative;
  wire [7:0] A_q, alu_test_1_abh_out, alu_test_1_abl_out, alu_test_1_alu_out, buffer_1_out, buffer_6_out,
       buffer_7_out, buffer_10_out, buffer_11_out, buffer_12_out, buffer_13_out, controlled_buffer_2_out,
       controlled_buffer_7_out, controlled_buffer_8_out, costant_register_1_d_bus_out,
       cu_final_1_rom_selector_out, register_1_q, transfer_register_1_dbus_out, uspu_1_adh_out,
       uspu_1_adl_out, uspu_1_d_bus_out, X_q, Y_q;
  wire [15:0] address_bus_control_1_low_out, controlled_buffer_6_out, transfer_register_1_adr_bus_out,
       uspu_1_adr;
  wire [31:0] cu_final_1_rom_uscite;

  not not_1 (not_1_out, irq_disable);
  and and_1 (and_1_out, clock, not_2_out);
  not not_2 (not_2_out, hidle);
  Register register_1 (.D(d_bus_in), .en(not_3_out), .clk(and_1_out), .Q(register_1_q));  // open: clr
  not not_3 (not_3_out, rom_1_demux_module_1_isr_block);
  and and_2 (and_2_out, irq, not_1_out);
  CU_Final cu_final_1 (
    .pwr(startup), .nmi(nmi), .reset(reset), .irq(and_2_out), .in_5(and_1_out),
    .mic_reset(cu_final_1_rom_uscite[31]), .isr_input(register_1_q), .mic_count(cu_final_1_rom_uscite[30]),
    .flag_in(or_6_out), .startup(cu_final_1_startup), .nmi_detect(cu_final_1_nmi_detect),
    .irq_detect(cu_final_1_irq_detect), .reset_detect(cu_final_1_reset_detect),
    .rom_selector_out(cu_final_1_rom_selector_out), .rom_uscite(cu_final_1_rom_uscite));
  assign d_bus_out = r_w_mode ? controlled_buffer_2_out : 8'bz;  // Controlled_Buffer controlled_buffer_1
  assign controlled_buffer_2_out = rom_1_demux_module_1_data_bus_in ? d_bus_in : 8'bz;  // Controlled_Buffer controlled_buffer_2
  rom_3_decoder rom_3_decoder_1 (
    .buffer_in(cu_final_1_rom_uscite[23:16]), .alu_a_we(rom_3_decoder_1_alu_a_we),
    .sum_actived(rom_3_decoder_1_sum_actived), .sub_actived(rom_3_decoder_1_sub_actived),
    .cmp_active(rom_3_decoder_1_cmp_active), .inc(rom_3_decoder_1_inc),
    .sum_actived_16b(rom_3_decoder_1_sum_actived_16b), .alu_oe(rom_3_decoder_1_alu_oe),
    .load_c(rom_3_decoder_1_load_c));  // open: and_actived, or_actived, eor_actived, shift_l, shift_r, rotate_l, rotare_r, BIT, dec, bcd_mode, load_from_ad
  rom_1_demux_module rom_1_demux_module_1 (
    .rom_1_out(cu_final_1_rom_uscite[7:0]), .isr_block(rom_1_demux_module_1_isr_block),
    .data_bus_out(r_w_mode), .data_bus_in(rom_1_demux_module_1_data_bus_in),
    .dlatch_we(rom_1_demux_module_1_dlatch_we), .dlatch_oe_abl(rom_1_demux_module_1_dlatch_oe_abl),
    .dlatch_h_we(rom_1_demux_module_1_dlatch_h_we), .dlatch_h_oe_abh(rom_1_demux_module_1_dlatch_h_oe_abh),
    .dlatch_out_dbus(rom_1_demux_module_1_dlatch_out_dbus),
    .dlatch_h_out_dbus(rom_1_demux_module_1_dlatch_h_out_dbus), .pcl_load(rom_1_demux_module_1_pcl_load),
    .pch_load(rom_1_demux_module_1_pch_load), .status_input_enable(rom_1_demux_module_1_status_input_enable),
    .status_reset(rom_1_demux_module_1_status_reset), .status_to_bus(rom_1_demux_module_1_status_to_bus),
    .carry_data(rom_1_demux_module_1_carry_data), .carry_update(rom_1_demux_module_1_carry_update),
    .interrupt_disable_data(rom_1_demux_module_1_interrupt_disable_data),
    .interrupt_update(rom_1_demux_module_1_interrupt_update),
    .deciamal_data(rom_1_demux_module_1_deciamal_data), .decimal_update(rom_1_demux_module_1_decimal_update),
    .overflow_data(rom_1_demux_module_1_overflow_data),
    .overflow_update(rom_1_demux_module_1_overflow_update), .brk_data(rom_1_demux_module_1_brk_data),
    .brk_update(rom_1_demux_module_1_brk_update));
  assign buffer_1_out = controlled_buffer_2_out;  // Buffer buffer_1, 8 bits wide
  or or_1 (or_1_out, rom_3_decoder_1_sub_actived, rom_3_decoder_1_cmp_active);
  assign adr = controlled_buffer_6_out;  // Buffer buffer_2, 16 bits wide
  assign adr = address_bus_control_1_low_out;  // Buffer buffer_3, 16 bits wide
  assign controlled_buffer_2_out = costant_register_1_d_bus_out;  // Buffer buffer_4, 8 bits wide
  assign controlled_buffer_2_out = transfer_register_1_dbus_out;  // Buffer buffer_5, 8 bits wide
  assign buffer_6_out = controlled_buffer_2_out;  // Buffer buffer_6, 8 bits wide
  assign buffer_7_out = controlled_buffer_2_out;  // Buffer buffer_7, 8 bits wide
  alu_test alu_test_1 (
    .clock(and_1_out), .buffer_in(buffer_1_out), .alu_a_in(rom_3_decoder_1_alu_a_we),
    .alu_b_in(rom2_decoder_1_alu_b_in[0]),
    .status_in({1'b0, costant_register_1_negative[6:5], irq_disable, costant_register_1_negative[3:0]}),
    .alu_sum_actived(rom_3_decoder_1_sum_actived), .alu_inc(rom_3_decoder_1_inc), .alu_sub(or_1_out),
    .alu_16b_sum(rom_3_decoder_1_sum_actived_16b), .alu_oe(rom_3_decoder_1_alu_oe),
    .load_c(rom_3_decoder_1_load_c), .abl_oe(rom2_decoder_1_alu_b_in[1]),
    .abh_oe(rom2_decoder_1_alu_b_in[2]), .alu_control_status(alu_test_1_alu_control_status),
    .alu_status(alu_test_1_alu_status), .alu_out(alu_test_1_alu_out), .abl_out(alu_test_1_abl_out),
    .abh_out(alu_test_1_abh_out));  // open: disable_pc
  assign controlled_buffer_2_out = alu_test_1_alu_out;  // Buffer buffer_8, 8 bits wide
  or or_2 (or_2_out, alu_test_1_alu_status[1], rom_1_demux_module_1_overflow_data);
  or or_3 (or_3_out, rom_1_demux_module_1_overflow_update, alu_test_1_alu_control_status[1]);
  or or_4 (or_4_out, alu_test_1_alu_status[3], rom_1_demux_module_1_carry_data);
  or or_5 (or_5_out, rom_1_demux_module_1_carry_update, alu_test_1_alu_control_status[3]);
  transfer_register transfer_register_1 (
    .clk(and_1_out), .data_bus(buffer_6_out), .dlatch_l_we(rom_1_demux_module_1_dlatch_we),
    .dlatch_h_we(rom_1_demux_module_1_dlatch_h_we), .dlatch_l_oe(rom_1_demux_module_1_dlatch_out_dbus),
    .dlatch_h_oe(rom_1_demux_module_1_dlatch_h_out_dbus), .dlatch_oe_adr(rom_1_demux_module_1_dlatch_oe_abl),
    .dlatch_h_oe_adr(rom_1_demux_module_1_dlatch_h_oe_abh), .dbus_out(transfer_register_1_dbus_out),
    .adr_bus_out(transfer_register_1_adr_bus_out));  // open: pc_disable
  costant_register costant_register_1 (
    .n_request(cu_final_1_rom_selector_out[0]), .o_request(cu_final_1_rom_selector_out[1]),
    .b_request(cu_final_1_rom_selector_out[2]), .d_request(cu_final_1_rom_selector_out[3]),
    .irq_request(cu_final_1_rom_selector_out[4]), .z_request(cu_final_1_rom_selector_out[5]),
    .c_request(cu_final_1_rom_selector_out[6]), .out_bus(rom_1_demux_module_1_status_to_bus),
    .read_bus(rom_1_demux_module_1_status_input_enable), .clock(and_1_out), .d_bus(buffer_7_out),
    .negative_data(alu_test_1_alu_status[0]), .negative_update(alu_test_1_alu_control_status[0]),
    .overflow_data(or_2_out), .overflow_update(or_3_out), .break_data(rom_1_demux_module_1_brk_data),
    .break_update(rom_1_demux_module_1_brk_update), .decimal_data(rom_1_demux_module_1_deciamal_data),
    .decimal_update(rom_1_demux_module_1_decimal_update),
    .irq_data(rom_1_demux_module_1_interrupt_disable_data),
    .irq_update(rom_1_demux_module_1_interrupt_update), .zero_data(alu_test_1_alu_status[2]),
    .zero_update(alu_test_1_alu_control_status[2]), .carry_data(or_4_out), .carry_update(or_5_out),
    .status_reset(rom_1_demux_module_1_status_reset), .n_out(costant_register_1_n_out),
    .o_out(costant_register_1_o_out), .b_out(costant_register_1_b_out), .d_out(costant_register_1_d_out),
    .irq_out(costant_register_1_irq_out), .z_out(costant_register_1_z_out), .c_out(costant_register_1_c_out),
    .d_bus_out(costant_register_1_d_bus_out), .negative(costant_register_1_negative[0]),
    .overflow(costant_register_1_negative[1]), .\break (costant_register_1_negative[2]),
    .decimal(costant_register_1_negative[3]), .irq(irq_disable), .zero(costant_register_1_negative[5]),
    .carry(costant_register_1_negative[6]));
  or or_6 (or_6_out, costant_register_1_n_out, costant_register_1_o_out, costant_register_1_b_out, costant_register_1_d_out, costant_register_1_irq_out, costant_register_1_z_out, costant_register_1_c_out);
  or or_7 (or_7_out, cu_final_1_irq_detect, rom_1_demux_module_1_brk_data);
  address_bus_control address_bus_control_1 (
    .clk(and_1_out), .low_bus(alu_test_1_abl_out), .low_oe(rom2_decoder_1_alu_b_in[1]),
    .hight_oe(rom2_decoder_1_alu_b_in[2]), .hight_bus(alu_test_1_abh_out),
    .dis(address_bus_control_2_disable_other), .disable_pc(address_bus_control_1_disable_pc),
    .low_out(address_bus_control_1_low_out[7:0]), .hight_out(address_bus_control_1_low_out[15:8]),
    .disable_other(address_bus_control_1_disable_other));
  or or_8 (or_8_out, address_bus_control_2_disable_pc, address_bus_control_1_disable_pc);
  address_bus_control address_bus_control_2 (
    .clk(and_1_out), .low_bus(transfer_register_1_adr_bus_out[7:0]),
    .low_oe(rom_1_demux_module_1_dlatch_oe_abl), .hight_oe(rom_1_demux_module_1_dlatch_h_oe_abh),
    .hight_bus(transfer_register_1_adr_bus_out[15:8]), .dis(address_bus_control_1_disable_other),
    .disable_pc(address_bus_control_2_disable_pc), .low_out(address_bus_control_1_low_out[7:0]),
    .hight_out(address_bus_control_1_low_out[15:8]), .disable_other(address_bus_control_2_disable_other));
  rom2_decoder rom2_decoder_1 (
    .data_in(cu_final_1_rom_uscite[15:8]), .pc_count(rom2_decoder_1_pc_count), .pc_oe(rom2_decoder_1_pc_oe),
    .pc_load_reg(rom2_decoder_1_pc_load_reg), .pc_load_from_adr(rom2_decoder_1_pc_load_from_adr),
    .pcl_load(rom2_decoder_1_pcl_load), .pch_load(rom2_decoder_1_pch_load), .pcl_bus(rom2_decoder_1_pcl_bus),
    .pch_bus(rom2_decoder_1_pch_bus), .sp_oe(rom2_decoder_1_sp_oe), .sp_inc(rom2_decoder_1_sp_inc),
    .sp_dec(rom2_decoder_1_sp_dec), .sp_reset(rom2_decoder_1_sp_reset),
    .inc_reg_by_2(rom2_decoder_1_inc_reg_by_2), .alu_b_in(rom2_decoder_1_alu_b_in[0]),
    .alu_output_abl(rom2_decoder_1_alu_b_in[1]), .alu_output_abh(rom2_decoder_1_alu_b_in[2]),
    .sp_to_bus(rom2_decoder_1_sp_to_bus));  // open: pc_save_adr, load_saved
  assign controlled_buffer_2_out = uspu_1_d_bus_out;  // Buffer buffer_9, 8 bits wide
  assign buffer_10_out = controlled_buffer_2_out;  // Buffer buffer_10, 8 bits wide
  assign controlled_buffer_2_out = cu_final_1_rom_uscite[24] ? X_q : 8'bz;  // Controlled_Buffer controlled_buffer_3
  assign controlled_buffer_2_out = cu_final_1_rom_uscite[26] ? Y_q : 8'bz;  // Controlled_Buffer controlled_buffer_4
  assign controlled_buffer_2_out = cu_final_1_rom_uscite[28] ? A_q : 8'bz;  // Controlled_Buffer controlled_buffer_5
  assign buffer_11_out = controlled_buffer_2_out;  // Buffer buffer_11, 8 bits wide
  assign buffer_12_out = controlled_buffer_2_out;  // Buffer buffer_12, 8 bits wide
  assign buffer_13_out = controlled_buffer_2_out;  // Buffer buffer_13, 8 bits wide
  Register X (.D(buffer_11_out), .en(cu_final_1_rom_uscite[25]), .clk(and_1_out), .Q(X_q));  // open: clr
  Register Y (.D(buffer_12_out), .en(cu_final_1_rom_uscite[27]), .clk(and_1_out), .Q(Y_q));  // open: clr
  Register A (.D(buffer_13_out), .en(cu_final_1_rom_uscite[29]), .clk(and_1_out), .Q(A_q));  // open: clr
  assign controlled_buffer_6_out = or_8_out ? uspu_1_adr : 16'bz;  // Controlled_Buffer controlled_buffer_6
  USPU uspu_1 (
    .startup(cu_final_1_startup), .clk(and_1_out), .reset(cu_final_1_reset_detect),
    .nmi(cu_final_1_nmi_detect), .irq(or_7_out), .d_bus_in(buffer_10_out), .sp_oe(rom2_decoder_1_sp_oe),
    .sp_reset(rom2_decoder_1_sp_reset), .sp_inc(rom2_decoder_1_sp_inc), .sp_dec(rom2_decoder_1_sp_dec),
    .pcl_we(rom2_decoder_1_pcl_load), .pch_we(rom2_decoder_1_pch_load),
    .pc_load_reg(rom2_decoder_1_pc_load_reg), .pcl_oe(rom2_decoder_1_pcl_bus),
    .pch_oe(rom2_decoder_1_pch_bus), .pc_count(rom2_decoder_1_pc_count), .pc_oe(rom2_decoder_1_pc_oe),
    .mic_reset(cu_final_1_rom_uscite[31]), .load_from_adr(rom2_decoder_1_pc_load_from_adr),
    .pcl_rom1(rom_1_demux_module_1_pcl_load), .pch_rom1(rom_1_demux_module_1_pch_load),
    .reg_inc_by_2(rom2_decoder_1_inc_reg_by_2), .sp_to_bus(rom2_decoder_1_sp_to_bus),
    .adl_buffer_in(controlled_buffer_8_out), .adh_buffer_in(controlled_buffer_7_out),
    .d_bus_out(uspu_1_d_bus_out), .adr(uspu_1_adr), .adl_out(uspu_1_adl_out), .adh_out(uspu_1_adh_out));
  not not_4 (not_4_out, or_9_out);
  assign controlled_buffer_7_out = not_4_out ? uspu_1_adh_out : 8'bz;  // Controlled_Buffer controlled_buffer_7
  assign controlled_buffer_8_out = not_4_out ? uspu_1_adl_out : 8'bz;  // Controlled_Buffer controlled_buffer_8
  assign controlled_buffer_8_out = rom2_decoder_1_alu_b_in[1] ? alu_test_1_abl_out : 8'bz;  // Controlled_Buffer controlled_buffer_9
  assign controlled_buffer_7_out = rom2_decoder_1_alu_b_in[2] ? alu_test_1_abh_out : 8'bz;  // Controlled_Buffer controlled_buffer_10
  or or_9 (or_9_out, rom2_decoder_1_alu_b_in[2], rom2_decoder_1_alu_b_in[1]);
  // also tied to GND on the sheet: cu_final_1_rom_selector_out[7]

  // Notes on the sheet:
  //   status update line
  //   status data line
  //   status in
  //   alu control
endmodule

module cleaned_build_2 (
  input  startup,
  input  clock,
  input  nmi,
  input  irq,
  input  reset,
  input  [7:0] d_bus_in,
  output [7:0] d_bus_out,
  output r_w_mode,
  output [15:0] adr
);

  wire alu_test_2_1_dis_pc, and_1_out, and_2_out, and_3_out, costant_register_1_b_out,
       costant_register_1_c_out, costant_register_1_d_out, costant_register_1_irq_out,
       costant_register_1_n_out, costant_register_1_o_out, costant_register_1_z_out, cu_final_1_irq_detect,
       cu_final_1_nmi_detect, cu_final_1_reset_detect, cu_final_1_startup, irq_disable, not_1_out, not_2_out,
       not_3_out, not_4_out, not_5_out, not_6_out, or_1_out, or_2_out, or_3_out, or_4_out, or_5_out,
       or_6_out, or_7_out, or_8_out, rom_1_demux_module_1_brk_data, rom_1_demux_module_1_brk_update,
       rom_1_demux_module_1_carry_data, rom_1_demux_module_1_carry_update, rom_1_demux_module_1_data_bus_in,
       rom_1_demux_module_1_deciamal_data, rom_1_demux_module_1_decimal_update,
       rom_1_demux_module_1_dlatch_h_oe_abh, rom_1_demux_module_1_dlatch_h_out_dbus,
       rom_1_demux_module_1_dlatch_h_we, rom_1_demux_module_1_dlatch_oe_abl,
       rom_1_demux_module_1_dlatch_out_dbus, rom_1_demux_module_1_dlatch_we,
       rom_1_demux_module_1_interrupt_disable_data, rom_1_demux_module_1_interrupt_update,
       rom_1_demux_module_1_isr_block, rom_1_demux_module_1_overflow_data,
       rom_1_demux_module_1_overflow_update, rom_1_demux_module_1_pch_load, rom_1_demux_module_1_pcl_load,
       rom_1_demux_module_1_status_input_enable, rom_1_demux_module_1_status_reset,
       rom_1_demux_module_1_status_to_bus, rom_3_decoder_1_alu_a_we, rom_3_decoder_1_alu_oe,
       rom_3_decoder_1_cmp_active, rom_3_decoder_1_dec, rom_3_decoder_1_inc, rom_3_decoder_1_load_c,
       rom_3_decoder_1_load_from_ad, rom_3_decoder_1_sub_actived, rom_3_decoder_1_sum_actived,
       rom_3_decoder_1_sum_actived_16b, transfer_register_1_pc_disable;
  wire [2:0] new_uspu_1_alu_b_in;
  wire [3:0] alu_test_2_1_alu_control, alu_test_2_1_alu_flag;
  wire [6:0] costant_register_1_negative;
  wire [7:0] A_q, alu_test_2_1_d_bus_out, alu_test_2_1_hight_b, alu_test_2_1_low_b, buffer_6_out,
       buffer_7_out, buffer_8_out, buffer_10_out, buffer_12_out, buffer_13_out, buffer_14_out,
       controlled_buffer_2_out, controlled_buffer_7_out, controlled_buffer_8_out,
       costant_register_1_d_bus_out, cu_final_1_rom_selector_out, new_uspu_1_adh_out, new_uspu_1_adl_out,
       new_uspu_1_d_bus_out, register_1_q, transfer_register_1_dbus_out, X_q, Y_q;
  wire [15:0] alu_test_2_1_adl, controlled_buffer_6_out, new_uspu_1_adr, transfer_register_1_adr_bus_out;
  wire [31:0] cu_final_1_rom_uscite;

  not not_1 (not_1_out, irq_disable);
  Register register_1 (.D(d_bus_in), .en(not_2_out), .clk(clock), .Q(register_1_q));  // open: clr
  not not_2 (not_2_out, rom_1_demux_module_1_isr_block);
  and and_1 (and_1_out, irq, not_1_out);
  CU_Final cu_final_1 (
    .pwr(startup), .nmi(nmi), .reset(reset), .irq(and_1_out), .in_5(clock),
    .mic_reset(cu_final_1_rom_uscite[31]), .isr_input(register_1_q), .mic_count(cu_final_1_rom_uscite[30]),
    .flag_in(or_5_out), .startup(cu_final_1_startup), .nmi_detect(cu_final_1_nmi_detect),
    .irq_detect(cu_final_1_irq_detect), .reset_detect(cu_final_1_reset_detect),
    .rom_selector_out(cu_final_1_rom_selector_out), .rom_uscite(cu_final_1_rom_uscite));
  assign d_bus_out = r_w_mode ? controlled_buffer_2_out : 8'bz;  // Controlled_Buffer controlled_buffer_1
  assign controlled_buffer_2_out = rom_1_demux_module_1_data_bus_in ? d_bus_in : 8'bz;  // Controlled_Buffer controlled_buffer_2
  rom_3_decoder rom_3_decoder_1 (
    .buffer_in(cu_final_1_rom_uscite[23:16]), .alu_a_we(rom_3_decoder_1_alu_a_we),
    .sum_actived(rom_3_decoder_1_sum_actived), .sub_actived(rom_3_decoder_1_sub_actived),
    .cmp_active(rom_3_decoder_1_cmp_active), .inc(rom_3_decoder_1_inc), .dec(rom_3_decoder_1_dec),
    .sum_actived_16b(rom_3_decoder_1_sum_actived_16b), .alu_oe(rom_3_decoder_1_alu_oe),
    .load_c(rom_3_decoder_1_load_c), .load_from_ad(rom_3_decoder_1_load_from_ad));  // open: and_actived, or_actived, eor_actived, shift_l, shift_r, rotate_l, rotare_r, BIT, bcd_mode
  rom_1_demux_module rom_1_demux_module_1 (
    .rom_1_out(cu_final_1_rom_uscite[7:0]), .isr_block(rom_1_demux_module_1_isr_block),
    .data_bus_out(r_w_mode), .data_bus_in(rom_1_demux_module_1_data_bus_in),
    .dlatch_we(rom_1_demux_module_1_dlatch_we), .dlatch_oe_abl(rom_1_demux_module_1_dlatch_oe_abl),
    .dlatch_h_we(rom_1_demux_module_1_dlatch_h_we), .dlatch_h_oe_abh(rom_1_demux_module_1_dlatch_h_oe_abh),
    .dlatch_out_dbus(rom_1_demux_module_1_dlatch_out_dbus),
    .dlatch_h_out_dbus(rom_1_demux_module_1_dlatch_h_out_dbus), .pcl_load(rom_1_demux_module_1_pcl_load),
    .pch_load(rom_1_demux_module_1_pch_load), .status_input_enable(rom_1_demux_module_1_status_input_enable),
    .status_reset(rom_1_demux_module_1_status_reset), .status_to_bus(rom_1_demux_module_1_status_to_bus),
    .carry_data(rom_1_demux_module_1_carry_data), .carry_update(rom_1_demux_module_1_carry_update),
    .interrupt_disable_data(rom_1_demux_module_1_interrupt_disable_data),
    .interrupt_update(rom_1_demux_module_1_interrupt_update),
    .deciamal_data(rom_1_demux_module_1_deciamal_data), .decimal_update(rom_1_demux_module_1_decimal_update),
    .overflow_data(rom_1_demux_module_1_overflow_data),
    .overflow_update(rom_1_demux_module_1_overflow_update), .brk_data(rom_1_demux_module_1_brk_data),
    .brk_update(rom_1_demux_module_1_brk_update));
  assign adr = controlled_buffer_6_out;  // Buffer buffer_1, 16 bits wide
  assign adr = transfer_register_1_adr_bus_out;  // Buffer buffer_2, 16 bits wide
  assign adr = alu_test_2_1_adl;  // Buffer buffer_3, 16 bits wide
  assign controlled_buffer_2_out = costant_register_1_d_bus_out;  // Buffer buffer_4, 8 bits wide
  assign controlled_buffer_2_out = transfer_register_1_dbus_out;  // Buffer buffer_5, 8 bits wide
  assign buffer_6_out = controlled_buffer_2_out;  // Buffer buffer_6, 8 bits wide
  assign buffer_7_out = controlled_buffer_2_out;  // Buffer buffer_7, 8 bits wide
  assign buffer_8_out = controlled_buffer_2_out;  // Buffer buffer_8, 8 bits wide
  assign controlled_buffer_2_out = alu_test_2_1_d_bus_out;  // Buffer buffer_9, 8 bits wide
  alu_test_2 alu_test_2_1 (
    .clock(clock),
    .status_in({1'b0, costant_register_1_negative[6:5], irq_disable, costant_register_1_negative[3:0]}),
    .buffer_in(buffer_7_out), .alu_a_in(rom_3_decoder_1_alu_a_we), .alu_b_in(new_uspu_1_alu_b_in[0]),
    .load_c(rom_3_decoder_1_load_c), .adl_in(new_uspu_1_adl_out), .alu_inc(rom_3_decoder_1_inc),
    .alu_sum_actived(rom_3_decoder_1_sum_actived), .adh_in(new_uspu_1_adh_out),
    .alu_16b_sum(rom_3_decoder_1_sum_actived_16b), .alu_sub(rom_3_decoder_1_sub_actived),
    .alu_cmp(rom_3_decoder_1_cmp_active), .dec(rom_3_decoder_1_dec), .alu_oe(rom_3_decoder_1_alu_oe),
    .abl_oe(new_uspu_1_alu_b_in[1]), .abh_oe(new_uspu_1_alu_b_in[2]),
    .load_from_ad(rom_3_decoder_1_load_from_ad), .alu_control(alu_test_2_1_alu_control),
    .alu_flag(alu_test_2_1_alu_flag), .d_bus_out(alu_test_2_1_d_bus_out), .adl(alu_test_2_1_adl[7:0]),
    .adh(alu_test_2_1_adl[15:8]), .low_b(alu_test_2_1_low_b), .hight_b(alu_test_2_1_hight_b),
    .dis_pc(alu_test_2_1_dis_pc));
  or or_1 (or_1_out, alu_test_2_1_alu_flag[1], rom_1_demux_module_1_overflow_data);
  or or_2 (or_2_out, rom_1_demux_module_1_overflow_update, alu_test_2_1_alu_control[1]);
  or or_3 (or_3_out, alu_test_2_1_alu_flag[3], rom_1_demux_module_1_carry_data);
  or or_4 (or_4_out, rom_1_demux_module_1_carry_update, alu_test_2_1_alu_control[3]);
  transfer_register transfer_register_1 (
    .clk(clock), .data_bus(buffer_6_out), .dlatch_l_we(rom_1_demux_module_1_dlatch_we),
    .dlatch_h_we(rom_1_demux_module_1_dlatch_h_we), .dlatch_l_oe(rom_1_demux_module_1_dlatch_out_dbus),
    .dlatch_h_oe(rom_1_demux_module_1_dlatch_h_out_dbus), .dlatch_oe_adr(rom_1_demux_module_1_dlatch_oe_abl),
    .dlatch_h_oe_adr(rom_1_demux_module_1_dlatch_h_oe_abh), .dbus_out(transfer_register_1_dbus_out),
    .adr_bus_out(transfer_register_1_adr_bus_out), .pc_disable(transfer_register_1_pc_disable));
  costant_register costant_register_1 (
    .n_request(cu_final_1_rom_selector_out[0]), .o_request(cu_final_1_rom_selector_out[1]),
    .b_request(cu_final_1_rom_selector_out[2]), .d_request(cu_final_1_rom_selector_out[3]),
    .irq_request(cu_final_1_rom_selector_out[4]), .z_request(cu_final_1_rom_selector_out[5]),
    .c_request(cu_final_1_rom_selector_out[6]), .out_bus(rom_1_demux_module_1_status_to_bus),
    .read_bus(rom_1_demux_module_1_status_input_enable), .clock(clock), .d_bus(buffer_8_out),
    .negative_data(alu_test_2_1_alu_flag[0]), .negative_update(alu_test_2_1_alu_control[0]),
    .overflow_data(or_1_out), .overflow_update(or_2_out), .break_data(rom_1_demux_module_1_brk_data),
    .break_update(rom_1_demux_module_1_brk_update), .decimal_data(rom_1_demux_module_1_deciamal_data),
    .decimal_update(rom_1_demux_module_1_decimal_update),
    .irq_data(rom_1_demux_module_1_interrupt_disable_data),
    .irq_update(rom_1_demux_module_1_interrupt_update), .zero_data(alu_test_2_1_alu_flag[2]),
    .zero_update(alu_test_2_1_alu_control[2]), .carry_data(or_3_out), .carry_update(or_4_out),
    .status_reset(rom_1_demux_module_1_status_reset), .n_out(costant_register_1_n_out),
    .o_out(costant_register_1_o_out), .b_out(costant_register_1_b_out), .d_out(costant_register_1_d_out),
    .irq_out(costant_register_1_irq_out), .z_out(costant_register_1_z_out), .c_out(costant_register_1_c_out),
    .d_bus_out(costant_register_1_d_bus_out), .negative(costant_register_1_negative[0]),
    .overflow(costant_register_1_negative[1]), .\break (costant_register_1_negative[2]),
    .decimal(costant_register_1_negative[3]), .irq(irq_disable), .zero(costant_register_1_negative[5]),
    .carry(costant_register_1_negative[6]));
  or or_5 (or_5_out, costant_register_1_n_out, costant_register_1_o_out, costant_register_1_b_out, costant_register_1_d_out, costant_register_1_irq_out, costant_register_1_z_out, costant_register_1_c_out);
  or or_6 (or_6_out, cu_final_1_irq_detect, rom_1_demux_module_1_brk_data);
  or or_7 (or_7_out, and_2_out, and_3_out);
  and and_2 (and_2_out, not_3_out, alu_test_2_1_dis_pc);
  not not_3 (not_3_out, transfer_register_1_pc_disable);
  and and_3 (and_3_out, transfer_register_1_pc_disable, not_4_out);
  not not_4 (not_4_out, alu_test_2_1_dis_pc);
  assign buffer_10_out = controlled_buffer_2_out;  // Buffer buffer_10, 8 bits wide
  new_USPU new_uspu_1 (
    .startup(cu_final_1_startup), .reset(cu_final_1_reset_detect), .nmi(cu_final_1_nmi_detect),
    .irq(or_6_out), .d_bus_in(buffer_10_out), .clock(clock), .control_in(cu_final_1_rom_uscite[15:8]),
    .adl_in(controlled_buffer_8_out), .adh_in(controlled_buffer_7_out),
    .mic_reset(cu_final_1_rom_uscite[31]), .pcl_rom1(rom_1_demux_module_1_pcl_load),
    .pch_rom1(rom_1_demux_module_1_pch_load), .adr(new_uspu_1_adr), .d_bus_out(new_uspu_1_d_bus_out),
    .adl_out(new_uspu_1_adl_out), .adh_out(new_uspu_1_adh_out), .alu_b_in(new_uspu_1_alu_b_in[0]),
    .alu_oe_abl(new_uspu_1_alu_b_in[1]), .alu_oe_abh(new_uspu_1_alu_b_in[2]));
  assign controlled_buffer_2_out = new_uspu_1_d_bus_out;  // Buffer buffer_11, 8 bits wide
  assign controlled_buffer_2_out = cu_final_1_rom_uscite[24] ? X_q : 8'bz;  // Controlled_Buffer controlled_buffer_3
  assign controlled_buffer_2_out = cu_final_1_rom_uscite[26] ? Y_q : 8'bz;  // Controlled_Buffer controlled_buffer_4
  assign controlled_buffer_2_out = cu_final_1_rom_uscite[28] ? A_q : 8'bz;  // Controlled_Buffer controlled_buffer_5
  not not_5 (not_5_out, or_7_out);
  assign controlled_buffer_6_out = not_5_out ? new_uspu_1_adr : 16'bz;  // Controlled_Buffer controlled_buffer_6
  assign buffer_12_out = controlled_buffer_2_out;  // Buffer buffer_12, 8 bits wide
  assign buffer_13_out = controlled_buffer_2_out;  // Buffer buffer_13, 8 bits wide
  assign buffer_14_out = controlled_buffer_2_out;  // Buffer buffer_14, 8 bits wide
  Register X (.D(buffer_12_out), .en(cu_final_1_rom_uscite[25]), .clk(clock), .Q(X_q));  // open: clr
  Register Y (.D(buffer_13_out), .en(cu_final_1_rom_uscite[27]), .clk(clock), .Q(Y_q));  // open: clr
  Register A (.D(buffer_14_out), .en(cu_final_1_rom_uscite[29]), .clk(clock), .Q(A_q));  // open: clr
  not not_6 (not_6_out, or_8_out);
  assign controlled_buffer_7_out = not_6_out ? new_uspu_1_adh_out : 8'bz;  // Controlled_Buffer controlled_buffer_7
  assign controlled_buffer_8_out = not_6_out ? new_uspu_1_adl_out : 8'bz;  // Controlled_Buffer controlled_buffer_8
  assign controlled_buffer_8_out = new_uspu_1_alu_b_in[1] ? alu_test_2_1_low_b : 8'bz;  // Controlled_Buffer controlled_buffer_9
  assign controlled_buffer_7_out = new_uspu_1_alu_b_in[2] ? alu_test_2_1_hight_b : 8'bz;  // Controlled_Buffer controlled_buffer_10
  or or_8 (or_8_out, new_uspu_1_alu_b_in[2], new_uspu_1_alu_b_in[1]);
  // also tied to GND on the sheet: cu_final_1_rom_selector_out[7]
endmodule

module SP_unit (
  input  sp_oe,
  input  sp_reset,
  input  clk,
  input  sp_inc,
  input  sp_dec,
  input  [7:0] buffer_in,
  input  sp_to_bus,
  output [7:0] d_bus_out,
  output [15:0] sp_out
);

  wire and_1_out, or_1_out;
  wire [7:0] counter_1_q;

  and and_1 (and_1_out, sp_inc, or_1_out);
  or or_1 (or_1_out, sp_inc, sp_dec);
  Counter counter_1 (
    .load(sp_reset), .up(and_1_out), .count(or_1_out), .clk(clk), .D(buffer_in), .Q(counter_1_q));  // open: clr, carry
  assign d_bus_out = sp_to_bus ? counter_1_q : 8'bz;  // Controlled_Buffer controlled_buffer_1
  assign sp_out = sp_oe ? {8'h1, counter_1_q} : 16'bz;  // Controlled_Buffer controlled_buffer_2
endmodule

module USPU_buffer_red (
  input  pcl_load_rom1,
  input  pch_load_rom1,
  input  pch_load,
  input  pcl_load,
  input  nmi,
  input  reset,
  input  irq,
  input  startup,
  input  [7:0] bus_dati,
  output [7:0] bus_out
);

  wire and_1_out, and_2_out, and_3_out, and_4_out, not_1_out, or_1_out, or_2_out, or_3_out, or_4_out;

  or or_1 (or_1_out, reset, startup);
  or or_2 (or_2_out, pcl_load_rom1, pch_load_rom1);
  assign bus_out = and_1_out ? {8{1'b1}} : 8'bz;  // Controlled_Buffer controlled_buffer_1
  and and_1 (and_1_out, pch_load, or_3_out);
  and and_2 (and_2_out, pcl_load, irq);
  or or_3 (or_3_out, nmi, or_1_out, irq);
  and and_3 (and_3_out, pcl_load, or_1_out);
  and and_4 (and_4_out, pcl_load, nmi);
  assign bus_out = and_4_out ? 8'hfa : 8'bz;  // Controlled_Buffer controlled_buffer_2
  not not_1 (not_1_out, or_3_out);
  assign bus_out = and_3_out ? 8'hfc : 8'bz;  // Controlled_Buffer controlled_buffer_3
  assign bus_out = and_2_out ? 8'hfe : 8'bz;  // Controlled_Buffer controlled_buffer_4
  assign bus_out = or_4_out ? bus_dati : 8'bz;  // Controlled_Buffer controlled_buffer_5
  or or_4 (or_4_out, not_1_out, or_2_out);
endmodule

module CU_Final (
  input  pwr,
  input  nmi,
  input  reset,
  input  irq,
  input  in_5,
  input  mic_reset,
  input  [7:0] isr_input,
  input  mic_count,
  input  flag_in,
  output startup,
  output nmi_detect,
  output irq_detect,
  output reset_detect,
  output [7:0] rom_selector_out,
  output [31:0] rom_uscite
);

  wire and_1_out, and_2_out, counter_1_carry, d_ff_1_q, int_res_startup_logic_1_mic_reset_out;
  wire [7:0] rom_1, rom_1_data, rom_2, rom_2_data, rom_3, rom_3_data, rom_4, rom_4_data, rom_5_data;
  wire [7:4] counter_1_q;
  wire [12:0] buffer_1_out, int_res_startup_logic_1_buffer_out;

  and and_1 (and_1_out, nmi, int_res_startup_logic_1_mic_reset_out);
  and and_2 (and_2_out, irq, int_res_startup_logic_1_mic_reset_out);
  D_Flip_Flop d_ff_1 (
    .D(int_res_startup_logic_1_mic_reset_out), .clk(in_5), .Q(d_ff_1_q), .reset(d_ff_1_q));  // open: Qn, preset
  int_res_startup_logic int_res_startup_logic_1 (
    .power(pwr), .clock(in_5), .mic_reset(mic_reset), .buffer_in(isr_input), .reset(reset), .nmi(and_1_out),
    .irq(and_2_out), .startup_out(startup), .reset_out(reset_detect), .nmi_out(nmi_detect),
    .irq_out(irq_detect), .buffer_out(int_res_startup_logic_1_buffer_out[7:0]),
    .mic_reset_out(int_res_startup_logic_1_mic_reset_out));
  Counter counter_1 (
    .clr(d_ff_1_q), .load(1'b0), .count(mic_count), .clk(in_5), .D({8{1'b0}}), .carry(counter_1_carry),
    .Q({{3{counter_1_q[7]}}, counter_1_q[4], int_res_startup_logic_1_buffer_out[11:8]}));  // open: up
  or or_1 (int_res_startup_logic_1_buffer_out[12], counter_1_q[4], flag_in);
  ROM #(.addrWidth(13)) u_rom_1 (.addr(buffer_1_out), .data(rom_1_data));
  assign buffer_1_out = int_res_startup_logic_1_buffer_out;  // Buffer buffer_1, 13 bits wide
  ROM u_rom_2 (.addr(int_res_startup_logic_1_buffer_out[7:0]), .data(rom_2_data));
  ROM #(.addrWidth(13)) u_rom_3 (.addr(buffer_1_out), .data(rom_3_data));
  assign rom_1 = rom_1_data;  // Buffer buffer_2, 8 bits wide
  assign rom_2 = rom_3_data;  // Buffer buffer_3, 8 bits wide
  assign rom_selector_out = rom_2_data;  // Buffer buffer_4, 8 bits wide
  ROM #(.addrWidth(13)) u_rom_4 (.addr(buffer_1_out), .data(rom_4_data));
  ROM #(.addrWidth(13)) rom_5 (.addr(buffer_1_out), .data(rom_5_data));
  assign rom_uscite = {rom_4, rom_3, rom_2, rom_1};  // Buffer buffer_5, 32 bits wide
  assign rom_3 = rom_4_data;  // Buffer buffer_6, 8 bits wide
  assign rom_4 = rom_5_data;  // Buffer buffer_7, 8 bits wide
  // also tied to GND on the sheet: {counter_1_carry, counter_1_q[7]}

  // Notes on the sheet:
  //   segnale di reset e count del mpc ritardato di un ciclo di clock
  //   contents of rom_1 (hex, n*v repeats v):
  //   1 63*0 1 11*0 1 19*0 1 110*0 1 26*0 1 4*0 1 16*0 b 3 0 0 0 7 7 0 3f 3 3 0 0 7 7 0 1 7 0 0 0 3 3 0 47
  //   3 0 0 0 3 3 0 1 3 0 0 7 7 7 0 1 3 3 0 7 7 7 0 1 7 0 0 0 3 3 0 4b 3 0 0 0 3 3 0 1 3 0 0 0 7 7 0 b 3 3
  //   0 13 7 7 0 1 7 0 0 0 3 3 0 4f 3 0 0 0 3 3 0 1 3 0 0 0 7 7 0 1 3 3 0 7 7 7 0 1 7 0 0 0 3 3 0 53 3 0 0
  //   0 3 3 0 0 3 0 0 7 7 7 0 1 0 1 0 7 7 7 0 1 7 0 0 3 3 3 0 1 3 b 0 0 3 0 0 3 3 3 0 7 7 7 0 1 3 1 0 7 7
  //   7 0 1 7 0 0 3 3 3 0 5f 3 3 0 3 3 3 0 1 3 0 0 7 7 7 0 1 1 1 0 7 7 7 1 1 7 0 0 0 3 7 0 57 3 0 0 0 3 7
  //   b 1 3 0 0 7 7 7 0 1 3 0 0 7 7 7 1 1 7 0 0 0 3 7 0 5b 3 0 0 0 3 7 b b 1 0 0 0 f f 0 0 1 0 0 0 1b 1b 0
  //   1 f 0 0 0 1 1 0 0 3 0 0 0 3 3 0 b 1 0 0 f f f 0 43 1 1 0 1b 1b 1b 0 0 f 0 0 0 1 1 0 0 3 0 0 0 3 3 0
  //   3 1 0 0 0 f f 0 1 1 1 0 17 1b 1b 0 1 f 0 0 0 1 1 0 0 3 0 0 0 3 3 0 3 1 0 0 0 f f 0 3 1 1 0 1b 1b 1b
  //   0 0 f 0 0 0 1 1 0 0 3 0 0 0 3 3 0 0 1 0 0 f f f 0 1 0 0 0 1b 1b 1b 0 1 f 0 0 1 1 1 0 0 3 1 0 0 3 0 0
  //   1 1 1 0 f f f 0 0 1 0 0 1b 1b 1b 0 0 f 0 0 1 1 1 0 0 3 1 0 3 3 3 0 3 1 0 0 f f f 0 0 3 1 0 1b 1b 1b
  //   1 1 f 0 0 0 1 1 0 0 3 0 0 0 3 1b b 3 1 0 0 f 1 f 0 0 1 0 0 1b 1b 1b 1 0 f 0 0 0 1 1 0 0 3 0 0 0 3 1b
  //   b 3f 1 0 0 0 3 3 0 0 1 0 0 0 23 1 0 3 3 0 0 0 1 1 0 0 1 0 0 0 1 1 0 b 1 0 0 3 3 3 0 1 1 0 0 23 23 23
  //   0 0 3 0 0 0 1 1 0 0 1 0 0 0 1 1 0 43 1 0 0 0 3 3 0 0 1 0 0 1 23 23 0 3 3 0 0 0 1 1 0 0 1 0 0 0 1 1 0
  //   3 1 0 0 0 3 3 0 1 1 0 0 1 23 23 0 0 3 0 0 0 1 1 0 0 1 0 0 0 1 1 0 0 1 0 0 b b b 5*0 23 23 23 0 3 3 0
  //   0 1 1 1 0 0 1 0 0 0 1 0 0 0 1 0 0 3 3 3 5*0 23 23 23 0 0 3 0 0 3 3 3 0 0 1 0 0 1 1 1 0 1 1 0 0 3 3 3
  //   0 0 1 0 0 23 23 23 1 3 3 0 0 0 1 1 0 0 1 0 0 0 1 1 3f 1 1 0 0 3 3 3 0 0 1 0 0 23 23 23 1 0 3 0 0 0 1
  //   1 0 0 1 0 0 0 1 1 3f 1 7 0 0 0 1 1 6*0 3 3 0 1 1 0 0 0 3 3 0 0 1 0 0 0 1 1 0 13 7 0 0 1 1 1 5*0 3 3
  //   3 0 0 1 0 0 0 3 3 0 0 1 0 0 0 1 1 0 3 7 0 0 0 1 1 6*0 3 3 0 1 1 0 0 0 3 3 0 0 1 0 0 0 1 1 0 1 7 0 0
  //   0 1 1 5*0 1 3 3 0 0 1 0 0 0 3 3 0 0 1 0 0 0 1 1 0 0 7 0 0 1 1 1 5*0 b b b 0 1 1 0 0 b b b 0 0 1 0 0
  //   0 1 0 0 0 7 0 0 1 1 1 5*0 3 3 3 0 0 1 0 0 3 3 3 0 0 1 0 0 1 1 1 0 0 7 0 0 1 1 b 5*0 3 3 3 13 1 1 0 0
  //   0 3 3 0 0 1 0 0 0 1 1 b 0 7 0 0 1 1 b 5*0 3 3 3 13 0 1 0 0 0 3 3 0 0 1 0 0 0 1 1 b 1 f 11*0 1 1 0 1
  //   3 0 0 0 1 1 0 0 3 0 0 0 3 3 0 17 f 10*0 1 1 1 0 0 3 0 0 0 1 1 0 0 3 0 0 0 3 3 0 3 f 11*0 1 1 0 1 3 0
  //   0 0 1 1 0 0 3 0 0 0 3 3 0 0 f 10*0 13 1 1 0 0 3 0 0 0 1 1 0 0 3 0 0 0 3 3 0 0 f 10*0 1 1 1 0 1 b 0 0
  //   1 1 1 0 0 b 0 0 0 b 0 0 0 f 10*0 1 1 1 0 0 3 0 0 1 1 1 0 0 3 0 0 3 3 3 0 0 f 10*0 1 1 b 17 1 3 0 0 0
  //   1 b 0 0 3 0 0 0 3 3 1 0 f 10*0 1 1 b 17 0 3 0 0 0 1 b 0 0 3 0 0 0 3 3 1 1 3 14*0 1 1 7*0 1 0 0 0 1 1
  //   0 1 3 15*0 1 7*0 1 0 0 0 1 1 0 1 3 14*0 1 1 7*0 1 0 0 0 1 1 0 0 3 10*0 17 4*0 1 7*0 1 0 0 0 1 1 0 0
  //   b 14*0 1 12*0 1 0 0 0 3 23*0 1 0 0 1 1 1 0 0 3 13*0 1 1 1 7*0 1 0 0 0 1 b 1 0 3 13*0 1 0 1 7*0 1 0 0
  //   0 1 b 1 1 1 31*0 1 31*0 1 31*0 1 10*0 1 84*0 1 29*0 1 0 1 29*0 1 13 222*0 13 31*0 13 17 222*0 17
  //   31*0 17 1 222*0 1 31*0 1 1552*0 1 31*0 1 31*0 1 31*0 1 31*0 1 31*0 1 31*0 1 31*0 1 63*0 1 63*0 1
  //   63*0 1 63*0 1 63*0 3 63*0 3 63*0 3 63*0 3 63*0 1 63*0 1 63*0 1 63*0 1 63*0 1 63*0 1 63*0 1 63*0 1
  //   63*0 1 63*0 1 63*0 1 63*0 1
  //   contents of rom_2 (hex, n*v repeats v):
  //   16*0 1 31*0 1 31*0 2 31*0 2 31*0 40 31*0 40 31*0 20 31*0 20
  //   contents of rom_3 (hex, n*v repeats v):
  //   12 5 0 0 0 5 5 0 5 5 12 0 0 5 5 0 5 5 0 0 0 5 5 0 5 5 0 0 0 5 5 0 5 5 0 0 5 5 5 0 5 5 12 0 5 5 5 0 5
  //   5 0 0 0 5 5 0 5 5 0 0 0 5 5 0 12 5 0 0 0 5 5 0 5 5 12 0 5 5 5 0 5 5 0 0 0 5 5 0 5 5 0 0 0 5 5 0 12 5
  //   0 0 0 5 5 0 5 5 12 0 12 5 5 0 5 5 0 0 0 5 5 0 5 5 0 0 0 5 5 0 0 5 0 0 5 5 5 0 5 0 5 0 5 5 5 0 5 5 0
  //   0 5 5 5 0 5 5 5 0 0 5 0 0 5 5 5 0 5 5 5 0 5 5 5 0 5 5 5 0 5 5 0 0 5 5 5 0 5 5 5 0 5 5 5 0 5 5 0 0 5
  //   5 5 0 5 5 5 0 5 5 5 12 5 5 0 0 0 5 5 0 5 5 0 0 0 5 5 12 5 5 0 0 5 5 5 0 5 5 5 0 5 5 5 12 5 5 0 0 0 5
  //   5 0 5 5 0 0 0 5 5 12 a 4*0 12 12 0 c 32 12 0 0 5 5 0 27 4*0 32 32 0 12 5 0 0 0 5 5 0 13 0 0 0 12 12
  //   12 0 d 32 12 0 5 5 5 0 5 4*0 32 32 0 12 5 0 0 0 5 5 0 d 4*0 12 12 0 c 32 12 0 5 5 5 0 27 4*0 32 32 0
  //   12 5 0 0 0 5 5 0 d 4*0 12 12 0 d 32 12 0 5 5 5 0 5 4*0 32 32 0 12 5 0 0 0 5 5 5*0 12 12 12 0 12 0 12
  //   0 5 5 5 0 27 0 0 0 32 32 32 0 12 5 12 0 0 5 0 0 12 0 12 0 12 12 12 0 12 12 12 0 5 5 5 0 5 0 0 0 32
  //   32 32 0 12 5 16 0 5 5 5 0 12 0 0 0 12 12 12 0 12 12 12 0 5 5 5 2 27 4*0 32 25 0 12 5 0 0 0 5 5 a 12
  //   0 0 0 12 12 12 0 12 32 12 0 5 5 5 2 5 4*0 32 25 0 12 5 0 0 0 5 5 a b 20 0 0 0 12 12 0 12 12 5 0 0 12
  //   12 0 6 4*0 12 12 0 0 32 0 0 0 32 32 0 a 20 0 0 12 12 12 0 8 12 5 0 12 12 12 6*0 12 12 0 0 32 0 0 0
  //   32 32 0 d 20 0 0 0 12 12 0 12 12 5 0 12 12 12 0 6 4*0 12 12 0 0 32 0 0 0 32 32 0 e 20 0 0 0 12 12 0
  //   8 12 5 0 12 12 12 6*0 12 12 0 0 32 0 0 0 32 32 0 0 20 0 0 12 12 12 0 12 0 0 0 12 12 12 0 6 0 0 0 12
  //   12 12 0 0 32 12 0 0 32 0 0 5 20 5 0 12 12 12 0 0 5 0 0 12 12 12 5*0 12 12 12 0 0 32 12 0 32 32 32 0
  //   32 20 0 0 12 12 12 0 12 32 12 0 12 12 12 3 6 4*0 12 12 0 0 32 0 0 0 32 25 b 32 20 0 0 12 12 12 0 12
  //   12 0 0 12 12 5 3 5*0 12 12 0 0 32 0 0 0 32 25 b 8 53 0 0 0 32 0 0 0 5 0 0 0 12 12 0 12 20 0 0 0 53
  //   53 0 0 12 0 0 0 12 12 0 b 53 0 0 20 20 0 0 12 5 0 0 12 12 12 0 0 20 0 0 0 53 53 0 0 12 0 0 0 12 12 0
  //   d 53 0 0 0 32 0 0 0 5 0 0 1 12 12 0 12 20 0 0 0 53 53 0 0 12 0 0 0 12 12 0 14 53 0 0 0 20 0 0 12 5 0
  //   0 1 12 12 0 0 20 0 0 0 53 53 0 0 12 0 0 0 12 12 0 0 53 10*0 12 12 12 0 12 20 0 0 53 53 53 0 0 12 7*0
  //   53 15*0 20 0 0 53 53 53 0 0 12 6*0 5 53 0 0 20 20 20 0 0 5 0 0 12 12 12 1 12 20 0 0 0 53 53 0 0 12 0
  //   0 0 12 12 c 5 53 0 0 20 20 53 0 0 5 0 0 12 12 0 1 0 20 0 0 0 53 53 0 0 12 0 0 0 12 12 c 2 4*0 5 5
  //   6*0 20 0 0 cf d3 0 0 0 32 0 0 0 d3 0 0 0 d3 d3 0 5 0 0 0 5 5 5 5*0 20 20 0 0 0 d3 0 0 0 20 0 0 0 d3
  //   0 0 0 d3 d3 0 e 4*0 5 5 5*0 12 20 0 0 cf d3 0 0 0 32 0 0 0 d3 0 0 0 d3 d3 0 1 4*0 5 5 5*0 12 20 0 0
  //   0 d3 0 0 0 20 0 0 0 d3 0 0 0 d3 d3 5*0 5 5 5 9*0 cf d3 7*0 d3 0 0 0 d3 6*0 5 5 5 10*0 d3 7*0 d3 0 0
  //   d3 d3 d3 5*0 5 5 6*0 20 20 20 5 cf d3 0 0 0 5 0 0 0 d3 0 0 0 d3 d3 c 4*0 5 5 6*0 20 20 d3 5 0 d3 0 0
  //   0 20 0 0 0 d3 0 0 0 d3 d3 c 3 12*0 5 5 0 5 20 0 0 0 5 5 0 0 20 0 0 0 20 0 0 12 11*0 5 5 5 0 0 20 0 0
  //   0 5 5 0 0 20 0 0 0 20 0 0 14 12*0 5 5 0 5 20 0 0 0 5 5 0 0 20 0 0 0 20 0 0 12 11*0 5 5 5 0 0 20 0 0
  //   0 5 5 0 0 20 0 0 0 20 14*0 5 5 5 0 5 5 0 0 5 5 5 21*0 5 5 5 0 0 5 0 0 5 5 5 21*0 5 5 0 12 5 20 0 0 0
  //   5 0 0 0 20 0 0 0 20 0 2 12*0 5 5 0 12 0 20 0 0 0 5 0 0 0 20 0 0 0 20 0 2 1 20 14*0 5 5 7*0 5 0 0 0 5
  //   5 0 1 20 15*0 5 7*0 5 0 0 0 5 5 0 1 20 14*0 5 5 7*0 5 0 0 0 5 5 0 0 20 10*0 12 4*0 5 7*0 5 0 0 0 5 5
  //   0 0 5 14*0 5 12*0 5 0 0 0 5 23*0 5 0 0 5 5 5 0 0 20 13*0 1 5 5 7*0 5 0 0 0 5 0 3 0 20 13*0 1 0 5 7*0
  //   5 0 0 0 5 0 3 12 5 30*0 12 5 30*0 12 5 31*0 5 10*0 1 84*0 5 13*0 12 15*0 1 0 5 13*0 12 15*0 1 5
  //   107*0 12 114*0 5 31*0 5 12 222*0 12 31*0 12 1 222*0 1 31*0 1 12 222*0 12 31*0 12 1040*0 5 31*0 5
  //   31*0 5 31*0 5 31*0 5 31*0 5 31*0 5 31*0 5 31*0 5 31*0 27 31*0 5 31*0 27 31*0 5 31*0 27 31*0 5 31*0
  //   27 63*0 6 63*0 6 63*0 6 63*0 6 63*0 12 63*0 12 63*0 12 63*0 12 63*0 cf 63*0 cf 63*0 cf 63*0 cf 63*0
  //   5 63*0 5 63*0 5 63*0 5 63*0 5 63*0 5 63*0 5 63*0 5
  //   contents of rom_4 (hex, n*v repeats v):
  //   257*0 1 8*0 8b 14*0 1 0 0 0 1 1 0 0 1 8*0 8f 14*0 1 0 0 0 1 1 0 0 1 8*0 8d 14*0 1 0 0 0 1 1 0 0 1
  //   8*0 91 14*0 1 0 0 0 1 1 0 0 1 6*0 9b 16*0 1 0 0 0 1 0 0 0 1 23*0 1 0 0 1 1 1 0 1 1 6*0 99 1 9b 14*0
  //   1 0 0 0 1 1 0 1 1 6*0 99 16*0 1 0 0 0 1 1 0 0 80 0 0 0 1 4*0 20 5*0 1 1 0 0 0 81 81 10*0 80 0 0 1 1
  //   4*0 20 6*0 1 0 0 0 81 81 10*0 80 0 0 0 1 4*0 20 5*0 1 1 0 0 0 81 81 10*0 80 0 0 0 1 0 0 0 81 20 6*0
  //   1 0 0 0 81 81 10*0 80 6*0 20 7*0 1 1 0 0 81 81 81 10*0 80 15*0 1 0 0 81 81 81 9*0 94 80 0 0 1 1 0 0
  //   20 94 20 5*0 1 1 0 0 0 81 81 9*0 94 80 0 0 1 1 0 0 20 8*0 1 0 0 0 81 81 14*0 86 8b 0 0 20 0 0 0 1 0
  //   0 9e 80 0 0 0 1 0 0 0 9e 0 0 0 9e 9e 5*0 92 84 8f 0 0 20 0 0 1 1 0 0 0 80 0 0 0 1 0 0 0 9e 0 0 0 9e
  //   9e 6*0 88 8d 0 0 20 0 0 0 1 0 0 9e 80 0 0 0 1 0 0 0 9e 0 0 0 9e 9e 6*0 80 91 0 0 20 0 0 0 1 0 0 0 80
  //   0 0 0 1 0 0 0 9e 0 0 0 9e 9e 17*0 9e 80 7*0 9e 0 0 0 9e 19*0 80 7*0 9e 0 0 9e 9e 9e 0 20 0 0 0 94 94
  //   94 0 0 20 0 0 1 1 0 0 9e 80 0 0 0 1 0 0 0 9e 0 0 0 9e 9e 0 20 0 0 0 94 82 99 0 0 20 0 0 1 1 0 0 0 80
  //   0 0 0 1 0 0 0 9e 0 0 0 9e 9e 6*0 20 20 6*0 86 8b 0 0 1 0 0 0 86 8b 0 0 1 0 0 0 1 6*0 20 20 20 5*0 92
  //   84 8f 0 0 1 0 0 0 84 8f 0 0 1 0 0 0 1 7*0 20 20 6*0 88 8d 0 0 1 0 0 0 88 8d 0 0 1 0 0 0 1 7*0 20 20
  //   6*0 80 91 0 0 1 0 0 0 80 91 0 0 1 0 0 0 1 70*0 20 20 20 5*0 94 94 9b 0 0 1 0 0 0 94 9b 0 0 1 0 0 0 1
  //   6*0 20 20 20 5*0 94 82 99 0 0 1 0 0 0 82 99 0 0 1 0 0 0 1 0 0 0 1 11*0 20 20 0 0 86 0 0 0 20 20 0 0
  //   86 0 0 0 86 8b 0 0 1 10*0 20 20 20 0 0 84 0 0 0 20 20 0 0 84 0 0 0 84 8f 0 0 1 11*0 20 20 0 0 88 0 0
  //   0 20 20 0 0 88 0 0 0 88 8d 0 0 1 11*0 20 20 0 0 80 0 0 0 20 20 0 0 80 0 0 0 80 91 66*0 1 10*0 20 20
  //   20 0 0 94 0 0 0 20 20 0 0 94 0 0 0 94 20 0 0 1 10*0 20 20 20 0 0 82 0 0 0 20 20 0 0 82 0 0 0 82 20 0
  //   0 86 15*0 20 7*0 20 0 0 0 20 20 0 0 84 15*0 20 7*0 20 0 0 0 20 20 0 0 88 15*0 20 7*0 20 0 0 0 20 20
  //   0 0 80 15*0 20 7*0 20 0 0 0 20 20 66*0 94 15*0 20 7*0 20 0 0 0 20 20 0 0 82 15*0 20 7*0 20 0 0 0 20
  //   20 0 0 20 31*0 20 31*0 20 31*0 20 95*0 20 31*0 20 2638*0 1 63*0 1 63*0 1 63*0 1 63*0 9e 63*0 9e 63*0
  //   9e 63*0 9e
  //   contents of rom_5 (hex, n*v repeats v):
  //   40 40 0 0 0 40 40 0 40 40 40 0 0 40 40 0 40 40 0 0 0 40 40 0 40 40 0 0 0 40 40 0 40 40 0 0 40 40 40
  //   0 40 40 40 0 40 40 40 0 40 40 0 0 0 40 40 0 40 40 0 0 0 40 40 0 40 40 0 0 0 40 40 0 40 40 40 0 40 40
  //   40 0 40 40 0 0 0 40 40 0 40 40 0 0 0 40 40 0 40 40 0 0 0 40 40 0 40 40 40 0 40 40 40 0 40 40 0 0 0
  //   40 40 0 40 40 0 0 0 40 40 0 0 40 0 0 40 40 40 0 40 0 40 0 40 40 40 0 40 40 0 0 40 40 40 0 40 40 40 0
  //   0 40 0 0 40 40 40 0 40 40 40 0 40 40 40 0 40 40 40 0 40 40 0 0 40 40 40 0 40 40 40 0 40 40 40 0 40
  //   40 0 0 40 40 40 0 40 40 40 0 6*40 0 0 0 40 40 0 40 40 0 0 0 5*40 0 0 40 40 40 0 40 40 40 0 6*40 0 0
  //   0 40 40 0 40 40 0 0 0 5*40 0 0 0 40 40 0 40 40 40 0 0 40 40 0 40 40 0 0 0 40 40 0 80 40 0 0 0 40 40
  //   0 40 40 0 0 40 40 40 0 40 40 40 0 40 40 40 0 80 40 0 0 0 40 40 0 80 40 0 0 0 40 40 0 40 40 0 0 0 40
  //   40 0 50 40 40 0 40 40 40 0 40 40 0 0 0 40 40 0 80 40 0 0 0 40 40 0 40 40 0 0 0 40 40 0 40 40 40 0 40
  //   40 40 0 80 40 0 0 0 40 40 0 80 40 0 0 0 40 40 0 0 40 0 0 40 40 40 0 44 0 a1 0 40 40 40 0 40 40 0 0
  //   40 40 40 0 a4 40 41 0 0 40 0 0 48 40 42 0 40 40 40 0 98 60 92 0 40 40 40 0 80 40 0 0 40 40 40 0 80
  //   40 42 0 40 40 40 0 44 40 0 0 40 40 40 0 44 50 41 0 6*40 0 0 0 40 40 0 80 40 0 0 0 40 40 40 41 40 0 0
  //   40 40 40 0 41 40 80 0 4*40 80 40 0 0 0 40 40 0 80 40 0 0 0 4*40 41 0 0 0 50 40 0 80 50 a0 0 0 40 40
  //   0 40 44 0 0 0 41 41 0 0 40 0 0 0 40 40 0 40 41 0 0 50 50 40 0 40 50 a0 0 40 40 40 0 0 44 0 0 0 41 41
  //   0 0 40 0 0 0 40 40 0 60 41 0 0 0 50 40 0 80 50 a0 0 40 40 40 0 40 44 0 0 0 41 41 0 0 40 0 0 0 40 40
  //   0 40 41 0 0 0 50 40 0 60 50 a0 0 40 40 40 0 0 44 0 0 0 41 41 0 0 40 0 0 0 40 40 0 0 41 0 0 40 40 40
  //   0 88 0 0 0 40 40 40 0 40 44 0 0 40 40 40 0 0 40 80 0 0 40 0 0 80 41 80 0 40 40 40 0 0 80 0 0 40 40
  //   40 0 0 44 0 0 41 41 44 0 0 40 80 0 40 40 40 0 40 41 0 0 44 50 40 0 88 40 82 0 5*40 44 0 0 0 41 41 0
  //   0 40 0 0 0 4*40 41 0 0 41 50 40 0 82 50 0 0 4*40 0 44 0 0 0 41 41 0 0 40 0 0 0 5*40 0 0 0 40 40 0 0
  //   a0 0 0 0 50 40 0 40 40 0 0 0 50 40 0 0 44 0 0 0 41 41 0 40 40 0 0 40 40 40 0 80 a0 0 0 50 50 40 0 0
  //   40 0 0 0 50 40 0 0 44 0 0 0 41 41 0 40 40 0 0 0 40 40 0 0 a0 0 0 40 50 40 0 40 40 0 0 0 50 40 0 0 44
  //   0 0 0 41 41 0 40 40 0 0 0 40 40 0 80 a0 0 0 40 50 40 0 0 40 0 0 0 50 40 0 0 44 0 0 0 41 41 0 0 40 0
  //   0 44 50 41 5*0 40 40 40 0 40 40 0 0 40 40 40 0 0 44 0 0 0 41 0 0 0 40 0 0 48 60 42 5*0 40 40 40 0 0
  //   40 0 0 40 40 40 0 0 44 0 0 41 41 44 0 80 40 0 0 40 40 40 0 0 80 0 0 44 50 4*40 0 0 0 50 40 0 0 44 0
  //   0 0 41 41 40 80 40 0 0 40 40 40 0 0 a0 0 0 41 50 40 40 0 40 0 0 0 50 40 0 0 44 0 0 0 41 41 40 40 40
  //   0 0 0 a0 a0 6*0 40 40 0 40 50 0 0 0 40 40 0 0 50 0 0 0 50 40 0 40 40 0 0 80 a0 a0 5*0 40 40 40 0 0
  //   50 0 0 0 40 40 0 0 50 0 0 0 50 40 0 40 40 0 0 0 a0 a0 5*0 80 40 40 0 40 50 0 0 0 40 40 0 0 50 0 0 0
  //   50 40 0 40 40 0 0 0 a0 a0 5*0 40 40 40 0 0 50 0 0 0 40 40 0 0 50 0 0 0 50 40 0 0 40 0 0 80 80 80 5*0
  //   44 50 41 0 40 40 0 0 44 50 41 0 0 40 0 0 0 40 0 0 0 40 0 0 80 80 80 5*0 48 60 42 0 0 40 0 0 48 60 42
  //   0 0 40 0 0 40 40 40 0 0 40 0 0 80 80 80 5*0 5*40 50 0 0 0 40 40 0 0 50 0 0 0 50 40 50 0 40 0 0 80 a0
  //   40 5*0 4*40 0 50 0 0 0 40 40 0 0 50 0 0 0 50 40 50 40 50 11*0 80 a0 0 40 40 0 0 0 a0 a0 0 0 40 0 0 0
  //   40 40 0 40 50 10*0 80 a0 a0 0 0 40 0 0 0 a0 a0 0 0 40 0 0 0 40 40 0 40 50 11*0 80 a0 0 40 40 0 0 0
  //   a0 a0 0 0 40 0 0 0 40 40 0 80 50 10*0 40 a0 a0 0 0 40 0 0 0 a0 a0 0 0 40 0 0 0 40 40 0 0 40 10*0 80
  //   80 80 0 40 90 0 0 80 80 80 0 0 50 0 0 0 50 0 0 0 40 10*0 80 80 80 0 0 a0 0 0 80 80 80 0 0 60 0 0 48
  //   60 42 0 0 50 10*0 80 80 80 40 40 40 0 0 0 80 80 0 0 40 0 0 0 40 40 40 0 50 10*0 80 a0 80 40 0 40 0 0
  //   0 a0 80 0 0 40 0 0 0 5*40 14*0 80 a0 7*0 a0 0 0 0 a0 a0 0 40 40 15*0 a0 7*0 a0 0 0 0 a0 a0 0 40 40
  //   14*0 80 a0 7*0 a0 0 0 0 a0 a0 0 0 40 10*0 40 4*0 a0 7*0 a0 0 0 0 a0 a0 0 0 a0 14*0 80 12*0 80 0 0 0
  //   a0 23*0 80 0 0 80 80 80 0 0 40 13*0 40 80 a0 7*0 80 0 0 0 80 80 40 0 40 13*0 40 0 a0 7*0 a0 0 0 0 a0
  //   80 40 40 a0 30*0 80 a0 30*0 80 a0 31*0 a0 10*0 40 84*0 a0 13*0 80 15*0 40 0 a0 13*0 80 15*0 40 40
  //   107*0 80 114*0 40 31*0 40 40 222*0 40 31*0 40 40 222*0 40 31*0 40 80 222*0 80 31*0 80 1040*0 40 31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
endmodule

module rom_1_demux_module (
  input  [7:0] rom_1_out,
  output isr_block,
  output data_bus_out,
  output data_bus_in,
  output dlatch_we,
  output dlatch_oe_abl,
  output dlatch_h_we,
  output dlatch_h_oe_abh,
  output dlatch_out_dbus,
  output dlatch_h_out_dbus,
  output pcl_load,
  output pch_load,
  output status_input_enable,
  output status_reset,
  output status_to_bus,
  output carry_data,
  output carry_update,
  output interrupt_disable_data,
  output interrupt_update,
  output deciamal_data,
  output decimal_update,
  output overflow_data,
  output overflow_update,
  output brk_data,
  output brk_update
);

  wire and_1_out, decoder_1_out0, decoder_1_out1, decoder_1_out2, decoder_1_out3, decoder_1_out4,
       decoder_1_out5, decoder_1_out6, decoder_1_out7, decoder_1_out8, decoder_1_out9, decoder_1_out10,
       decoder_1_out11, decoder_1_out12, decoder_1_out13, decoder_2_out0, decoder_2_out1, decoder_2_out2,
       decoder_2_out3, decoder_2_out4, decoder_2_out5, decoder_2_out6, decoder_2_out8, decoder_2_out9,
       not_1_out, not_2_out, not_3_out, not_4_out, not_5_out, not_6_out, or_12_out, or_14_out, or_16_out,
       or_18_out, xor_1_out;

  and and_1 (and_1_out, rom_1_out[1], not_1_out);
  not not_1 (not_1_out, rom_1_out[6]);
  Decoder #(.select(4)) decoder_1 (
    .out0(decoder_1_out0), .out1(decoder_1_out1), .out2(decoder_1_out2), .out3(decoder_1_out3),
    .out4(decoder_1_out4), .out5(decoder_1_out5), .out6(decoder_1_out6), .out7(decoder_1_out7),
    .out8(decoder_1_out8), .out9(decoder_1_out9), .out10(decoder_1_out10), .out11(decoder_1_out11),
    .out12(decoder_1_out12), .out13(decoder_1_out13), .out14(status_reset), .out15(status_to_bus),
    .sel(rom_1_out[5:2]), .en(and_1_out));
  buf xor_1 (xor_1_out, rom_1_out[6]);  // XOR_Gate
  Decoder #(.select(4)) decoder_2 (
    .out0(decoder_2_out0), .out1(decoder_2_out1), .out2(decoder_2_out2), .out3(decoder_2_out3),
    .out4(decoder_2_out4), .out5(decoder_2_out5), .out6(decoder_2_out6), .out7(overflow_update),
    .out8(decoder_2_out8), .out9(decoder_2_out9), .sel(rom_1_out[5:2]), .en(xor_1_out));  // open: out10, out11, out12, out13, out14, out15
  or or_1 (data_bus_out, decoder_1_out2, status_to_bus);
  or or_2 (data_bus_in, decoder_1_out0, decoder_1_out1, decoder_1_out4, decoder_1_out5, decoder_1_out6, decoder_2_out0);
  or or_3 (dlatch_we, decoder_1_out1, decoder_1_out9);
  or or_4 (dlatch_oe_abl, decoder_1_out3, decoder_1_out8);
  or or_5 (dlatch_h_we, decoder_1_out6, decoder_1_out10);
  or or_6 (dlatch_h_oe_abh, decoder_1_out7, decoder_1_out8);
  buf or_7 (dlatch_out_dbus, decoder_1_out11);  // OR_Gate
  buf or_8 (dlatch_h_out_dbus, decoder_1_out12);  // OR_Gate
  buf or_9 (pcl_load, decoder_1_out4);  // OR_Gate
  buf or_10 (pch_load, decoder_1_out5);  // OR_Gate
  or or_11 (status_input_enable, decoder_1_out13, decoder_2_out0);
  or or_12 (or_12_out, decoder_2_out2, not_2_out);
  not not_2 (not_2_out, decoder_2_out1);
  or or_13 (carry_update, decoder_2_out1, decoder_2_out2);
  or or_14 (or_14_out, decoder_2_out4, not_3_out);
  not not_3 (not_3_out, decoder_2_out3);
  and and_2 (interrupt_disable_data, or_14_out, interrupt_update);
  or or_15 (interrupt_update, decoder_2_out3, decoder_2_out4);
  or or_16 (or_16_out, decoder_2_out6, not_4_out);
  not not_4 (not_4_out, decoder_2_out5);
  and and_3 (deciamal_data, or_16_out, decimal_update);
  or or_17 (decimal_update, decoder_2_out5, decoder_2_out6);
  or or_18 (or_18_out, decoder_2_out8, not_5_out);
  not not_5 (not_5_out, decoder_2_out9);
  and and_4 (brk_data, or_18_out, brk_update);
  or or_19 (brk_update, decoder_2_out9, decoder_2_out8);
  and and_5 (carry_data, or_12_out, carry_update);
  not not_6 (not_6_out, overflow_update);
  and and_6 (overflow_data, not_6_out, overflow_update);

  assign isr_block = rom_1_out[0];
endmodule

module rom2_decoder (
  input  [7:0] data_in,
  output pc_count,
  output pc_oe,
  output pc_load_reg,
  output pc_load_from_adr,
  output pcl_load,
  output pch_load,
  output pcl_bus,
  output pch_bus,
  output sp_oe,
  output sp_inc,
  output sp_dec,
  output sp_reset,
  output inc_reg_by_2,
  output alu_b_in,
  output alu_output_abl,
  output alu_output_abh,
  output sp_to_bus,
  output pc_save_adr,
  output load_saved
);

  wire decoder_1_out0, decoder_1_out1, decoder_1_out2, decoder_1_out3, decoder_1_out4, decoder_1_out5,
       decoder_1_out6, decoder_1_out7, decoder_1_out8, decoder_1_out9, decoder_1_out10, decoder_1_out11,
       decoder_1_out12, decoder_1_out13, decoder_1_out14, decoder_2_out0, decoder_2_out1, decoder_2_out2,
       decoder_2_out4, decoder_2_out5, not_1_out, or_6_out, or_10_out;

  Decoder #(.select(4)) decoder_1 (
    .out0(decoder_1_out0), .out1(decoder_1_out1), .out2(decoder_1_out2), .out3(decoder_1_out3),
    .out4(decoder_1_out4), .out5(decoder_1_out5), .out6(decoder_1_out6), .out7(decoder_1_out7),
    .out8(decoder_1_out8), .out9(decoder_1_out9), .out10(decoder_1_out10), .out11(decoder_1_out11),
    .out12(decoder_1_out12), .out13(decoder_1_out13), .out14(decoder_1_out14), .out15(pc_load_from_adr),
    .sel(data_in[3:0]), .en(not_1_out));
  not not_1 (not_1_out, data_in[4]);
  Decoder #(.select(4)) decoder_2 (
    .out0(decoder_2_out0), .out1(decoder_2_out1), .out2(decoder_2_out2), .out3(inc_reg_by_2),
    .out4(decoder_2_out4), .out5(decoder_2_out5), .out6(sp_to_bus), .out7(pc_save_adr), .out8(load_saved),
    .sel(data_in[3:0]), .en(data_in[4]));  // open: out9, out10, out11, out12, out13, out14, out15
  buf or_1 (pc_load_reg, decoder_1_out1);  // OR_Gate
  or or_2 (pcl_load, decoder_1_out2, decoder_1_out4, decoder_2_out4);
  or or_3 (pch_load, decoder_1_out3, decoder_1_out14, decoder_2_out5);
  or or_4 (pcl_bus, decoder_1_out6, decoder_1_out10, decoder_2_out0);
  or or_5 (pch_bus, decoder_1_out7, decoder_1_out11, decoder_2_out1);
  or or_6 (or_6_out, decoder_1_out4, decoder_1_out8, decoder_1_out10, decoder_1_out10, decoder_1_out13, decoder_1_out14, decoder_2_out0);
  or or_7 (sp_inc, decoder_1_out4, decoder_1_out13, decoder_1_out14);
  or or_8 (sp_dec, decoder_1_out10, decoder_1_out10, decoder_1_out12, decoder_1_out11);
  buf or_9 (sp_reset, decoder_1_out9);  // OR_Gate
  or or_10 (or_10_out, decoder_1_out4, decoder_2_out2, decoder_1_out5, decoder_1_out9, decoder_1_out14, decoder_1_out1, inc_reg_by_2);
  or or_11 (sp_oe, sp_dec, decoder_1_out11, or_6_out, decoder_2_out4, decoder_2_out1, decoder_2_out5);
  or or_12 (pc_oe, or_10_out, pch_bus, pcl_bus);
  or or_13 (pc_count, decoder_1_out5, pc_save_adr);

  assign alu_b_in = data_in[5];
  assign alu_output_abh = data_in[7];
  assign alu_output_abl = data_in[6];
  // also tied to GND on the sheet: decoder_1_out0
endmodule

module PC_unit_2 (
  input  inc_by_2,
  input  clock,
  input  [7:0] d_bus,
  input  pcl_we,
  input  [7:0] adl,
  input  pch_we,
  input  [7:0] adh,
  input  pc_load_reg,
  input  pcl_oe,
  input  pch_oe,
  input  mic_reset,
  input  pc_count,
  input  pc_oe,
  input  load_from_adr,
  output [7:0] d_bus_out,
  output [15:0] address,
  output [7:0] adl_out,
  output [7:0] adh_out
);

  wire adder_1_cout, or_1_out, or_2_out, or_3_out, or_4_out, or_5_out, or_6_out, or_7_out, or_8_out,
       or_9_out, or_10_out, pcl_counter_carry;
  wire [7:0] adder_1_out, adder_2_out, buffer_1_out, buffer_2_out, buffer_3_out, controlled_buffer_1_out,
       controlled_buffer_2_out, controlled_buffer_3_out, controlled_buffer_6_out, controlled_buffer_7_out,
       controlled_buffer_9_out, controlled_buffer_10_out, pch_q, pcl_q, undriven;

  assign controlled_buffer_1_out = or_1_out ? d_bus : 8'bz;  // Controlled_Buffer controlled_buffer_1
  or or_1 (or_1_out, pch_we, pcl_we);
  or or_2 (or_2_out, pc_load_reg, load_from_adr);
  assign buffer_1_out = controlled_buffer_1_out;  // Buffer buffer_1, 8 bits wide
  assign controlled_buffer_2_out = or_3_out ? buffer_1_out : 8'bz;  // Controlled_Buffer controlled_buffer_2
  or or_3 (or_3_out, mic_reset, pcl_we);
  assign buffer_2_out = controlled_buffer_1_out;  // Buffer buffer_2, 8 bits wide
  assign controlled_buffer_3_out = or_4_out ? buffer_2_out : 8'bz;  // Controlled_Buffer controlled_buffer_3
  or or_4 (or_4_out, pch_we, mic_reset);
  assign controlled_buffer_2_out = inc_by_2 ? adder_1_out : 8'bz;  // Controlled_Buffer controlled_buffer_4
  assign controlled_buffer_3_out = inc_by_2 ? adder_2_out : 8'bz;  // Controlled_Buffer controlled_buffer_5
  Counter pcl_counter (
    .load(or_2_out), .count(pc_count), .clk(clock), .D(controlled_buffer_6_out), .carry(pcl_counter_carry),
    .Q(adl_out));  // open: clr, up
  assign controlled_buffer_6_out = pc_load_reg ? controlled_buffer_9_out : 8'bz;  // Controlled_Buffer controlled_buffer_6
  Counter pch_counter (
    .load(or_2_out), .count(pcl_counter_carry), .clk(clock), .D(controlled_buffer_7_out), .Q(adh_out));  // open: clr, up, carry
  assign controlled_buffer_7_out = pc_load_reg ? controlled_buffer_10_out : 8'bz;  // Controlled_Buffer controlled_buffer_7
  Adder adder_1 (.a(undriven), .b(8'h3), .out(adder_1_out), .cout(adder_1_cout));  // open: cin
  Adder adder_2 (.a(buffer_2_out), .b({8{1'b0}}), .out(adder_2_out), .cin(adder_1_cout));  // open: cout
  Register pcl (.D(controlled_buffer_2_out), .en(or_5_out), .clk(clock), .Q(pcl_q));  // open: clr
  or or_5 (or_5_out, inc_by_2, or_3_out);
  Register pch (.D(controlled_buffer_3_out), .en(or_6_out), .clk(clock), .Q(pch_q));  // open: clr
  or or_6 (or_6_out, inc_by_2, or_4_out);
  Controlled_Buffer #(.width(8)) controlled_buffer_8 (.in(pcl_q));  // open: out, en
  assign controlled_buffer_9_out = or_7_out ? pcl_q : 8'bz;  // Controlled_Buffer controlled_buffer_9
  or or_7 (or_7_out, pc_load_reg, pcl_oe);
  or or_8 (or_8_out, pc_load_reg, pch_oe);
  assign controlled_buffer_10_out = or_8_out ? pch_q : 8'bz;  // Controlled_Buffer controlled_buffer_10
  Controlled_Buffer #(.width(8)) controlled_buffer_11 ();  // open: in, out, en
  assign controlled_buffer_2_out = mic_reset ? adl_out : 8'bz;  // Controlled_Buffer controlled_buffer_12
  assign buffer_2_out = mic_reset ? adh_out : 8'bz;  // Controlled_Buffer controlled_buffer_13
  assign address = or_9_out ? {adh_out, adl_out} : 16'bz;  // Controlled_Buffer controlled_buffer_14
  assign buffer_3_out = controlled_buffer_9_out;  // Buffer buffer_3, 8 bits wide
  assign buffer_3_out = controlled_buffer_10_out;  // Buffer buffer_4, 8 bits wide
  or or_9 (or_9_out, pc_oe, mic_reset, pc_count);
  assign d_bus_out = or_10_out ? buffer_3_out : 8'bz;  // Controlled_Buffer controlled_buffer_15
  or or_10 (or_10_out, pcl_oe, pch_oe);
  assign controlled_buffer_6_out = load_from_adr ? adl : 8'bz;  // Controlled_Buffer controlled_buffer_16
  assign controlled_buffer_7_out = load_from_adr ? adh : 8'bz;  // Controlled_Buffer controlled_buffer_17
endmodule

module int_res_startup_logic (
  input  power,
  input  clock,
  input  mic_reset,
  input  [7:0] buffer_in,
  input  reset,
  input  nmi,
  input  irq,
  output startup_out,
  output reset_out,
  output nmi_out,
  output irq_out,
  output [7:0] buffer_out,
  output mic_reset_out
);

  wire and_1_out, nand_1_out, not_1_out, or_1_out, register_1_q, register_2_q;

  assign buffer_out = startup_out ? 8'hcf : 8'bz;  // Controlled_Buffer controlled_buffer_1
  assign buffer_out = reset_out ? 8'hef : 8'bz;  // Controlled_Buffer controlled_buffer_2
  assign buffer_out = nmi_out ? 8'hdf : 8'bz;  // Controlled_Buffer controlled_buffer_3
  assign buffer_out = irq_out ? {8{1'b1}} : 8'bz;  // Controlled_Buffer controlled_buffer_4
  assign buffer_out = not_1_out ? buffer_in : 8'bz;  // Controlled_Buffer controlled_buffer_5
  not not_1 (not_1_out, or_1_out);
  nand nand_1 (nand_1_out, register_2_q, power);
  Register #(.width(1)) register_1 (.D(nand_1_out), .en(nand_1_out), .clk(clock), .Q(register_1_q));  // open: clr
  or or_1 (or_1_out, startup_out, reset_out, nmi_out, irq_out);
  S_R_Flip_Flop s_r_ff_1 (.S(reset), .R(mic_reset), .clk(clock), .Q(reset_out));  // open: reset, Qn, preset
  S_R_Flip_Flop s_r_ff_2 (.S(nmi), .R(mic_reset), .clk(clock), .Q(nmi_out));  // open: reset, Qn, preset
  S_R_Flip_Flop s_r_ff_3 (.S(irq), .R(mic_reset), .clk(clock), .Q(irq_out));  // open: reset, Qn, preset
  and and_1 (and_1_out, mic_reset, register_1_q);
  Register #(.width(1)) register_2 (.D(and_1_out), .en(mic_reset), .clk(clock), .Q(register_2_q));  // open: clr
  xor xor_1 (startup_out, register_1_q, register_2_q);
  or or_2 (mic_reset_out, mic_reset, irq, nmi, reset);

  // Notes on the sheet:
  //   start
  //   reset
  //   nmi
  //   irq
endmodule

module transfer_register (
  input  clk,
  input  [7:0] data_bus,
  input  dlatch_l_we,
  input  dlatch_h_we,
  input  dlatch_l_oe,
  input  dlatch_h_oe,
  input  dlatch_oe_adr,
  input  dlatch_h_oe_adr,
  output [7:0] dbus_out,
  output [15:0] adr_bus_out,
  output pc_disable
);

  wire and_1_out, and_2_out, d_ff_1_q, d_ff_2_q, not_1_out, not_2_out;
  wire [7:0] controlled_buffer_3_out, controlled_buffer_5_out, register_1_q, register_2_q;

  D_Flip_Flop d_ff_1 (.D(dlatch_oe_adr), .clk(clk), .Q(d_ff_1_q));  // open: Qn, preset, reset
  D_Flip_Flop d_ff_2 (.D(dlatch_h_oe_adr), .clk(clk), .Q(d_ff_2_q));  // open: Qn, preset, reset
  Register register_1 (.D(data_bus), .en(dlatch_l_we), .clk(clk), .Q(register_1_q));  // open: clr
  Register register_2 (.D(data_bus), .en(dlatch_h_we), .clk(clk), .Q(register_2_q));  // open: clr
  assign dbus_out = dlatch_l_oe ? register_1_q : 8'bz;  // Controlled_Buffer controlled_buffer_1
  assign dbus_out = dlatch_h_oe ? register_2_q : 8'bz;  // Controlled_Buffer controlled_buffer_2
  assign controlled_buffer_3_out = and_2_out ? {8{1'b0}} : 8'bz;  // Controlled_Buffer controlled_buffer_3
  assign controlled_buffer_3_out = d_ff_1_q ? register_1_q : 8'bz;  // Controlled_Buffer controlled_buffer_4
  assign controlled_buffer_5_out = d_ff_2_q ? register_2_q : 8'bz;  // Controlled_Buffer controlled_buffer_5
  assign controlled_buffer_5_out = and_1_out ? {8{1'b0}} : 8'bz;  // Controlled_Buffer controlled_buffer_6
  and and_1 (and_1_out, d_ff_1_q, not_1_out);
  not not_1 (not_1_out, d_ff_2_q);
  not not_2 (not_2_out, d_ff_1_q);
  and and_2 (and_2_out, not_2_out, d_ff_2_q);
  assign adr_bus_out = pc_disable ? {controlled_buffer_5_out, controlled_buffer_3_out} : 16'bz;  // Controlled_Buffer controlled_buffer_7
  or or_1 (pc_disable, d_ff_1_q, d_ff_2_q);
endmodule

module USPU (
  input  startup,
  input  clk,
  input  reset,
  input  nmi,
  input  irq,
  input  [7:0] d_bus_in,
  input  sp_oe,
  input  sp_reset,
  input  sp_inc,
  input  sp_dec,
  input  pcl_we,
  input  pch_we,
  input  pc_load_reg,
  input  pcl_oe,
  input  pch_oe,
  input  pc_count,
  input  pc_oe,
  input  mic_reset,
  input  load_from_adr,
  input  pcl_rom1,
  input  pch_rom1,
  input  reg_inc_by_2,
  input  sp_to_bus,
  input  [7:0] adl_buffer_in,
  input  [7:0] adh_buffer_in,
  output [7:0] d_bus_out,
  output [15:0] adr,
  output [7:0] adl_out,
  output [7:0] adh_out
);

  wire and_1_out, d_ff_1_q, nand_1_out, or_1_out, or_2_out;
  wire [7:0] uspu_buffer_red_1_bus_out;
  wire [15:0] pc_unit_2_1_address;

  D_Flip_Flop d_ff_1 (.D(mic_reset), .clk(clk), .Q(d_ff_1_q));  // open: Qn, preset, reset
  nand nand_1 (nand_1_out, sp_oe, pc_oe);
  or or_1 (or_1_out, pch_we, pch_rom1);
  and and_1 (and_1_out, nand_1_out, pc_oe);
  or or_2 (or_2_out, pcl_we, pcl_rom1);
  USPU_buffer_red uspu_buffer_red_1 (
    .pcl_load_rom1(pcl_rom1), .pch_load_rom1(pch_rom1), .pch_load(pch_we), .pcl_load(pcl_we), .nmi(nmi),
    .reset(reset), .irq(irq), .startup(startup), .bus_dati(d_bus_in), .bus_out(uspu_buffer_red_1_bus_out));
  SP_unit sp_unit_1 (
    .sp_oe(sp_oe), .sp_reset(sp_reset), .clk(clk), .sp_inc(sp_inc), .sp_dec(sp_dec), .buffer_in(d_bus_in),
    .sp_to_bus(sp_to_bus), .d_bus_out(d_bus_out), .sp_out(adr));
  PC_unit_2 pc_unit_2_1 (
    .inc_by_2(reg_inc_by_2), .clock(clk), .d_bus(uspu_buffer_red_1_bus_out), .pcl_we(or_2_out),
    .adl(adl_buffer_in), .pch_we(or_1_out), .adh(adh_buffer_in), .pc_load_reg(pc_load_reg), .pcl_oe(pcl_oe),
    .pch_oe(pch_oe), .mic_reset(d_ff_1_q), .pc_count(pc_count), .pc_oe(and_1_out),
    .load_from_adr(load_from_adr), .d_bus_out(d_bus_out), .address(pc_unit_2_1_address), .adl_out(adl_out),
    .adh_out(adh_out));
  assign adr = pc_unit_2_1_address;  // Buffer buffer_1, 16 bits wide
endmodule

module costant_register (
  input  n_request,
  input  o_request,
  input  b_request,
  input  d_request,
  input  irq_request,
  input  z_request,
  input  c_request,
  input  out_bus,
  input  read_bus,
  input  clock,
  input  [7:0] d_bus,
  input  negative_data,
  input  negative_update,
  input  overflow_data,
  input  overflow_update,
  input  break_data,
  input  break_update,
  input  decimal_data,
  input  decimal_update,
  input  irq_data,
  input  irq_update,
  input  zero_data,
  input  zero_update,
  input  carry_data,
  input  carry_update,
  input  status_reset,
  output n_out,
  output o_out,
  output b_out,
  output d_out,
  output irq_out,
  output z_out,
  output c_out,
  output [7:0] d_bus_out,
  output negative,
  output overflow,
  output \break ,
  output decimal,
  output irq,
  output zero,
  output carry
);

  wire not_1_out, or_1_out, or_2_out, or_3_out, or_4_out, or_5_out, or_6_out, or_7_out;
  wire [7:0] controlled_buffer_1_out;

  assign controlled_buffer_1_out = read_bus ? d_bus : 8'bz;  // Controlled_Buffer controlled_buffer_1
  assign controlled_buffer_1_out = not_1_out ? {1'b0, carry_data, zero_data, irq_data, decimal_data, break_data, overflow_data, negative_data} : 8'bz;  // Controlled_Buffer controlled_buffer_2
  not not_1 (not_1_out, read_bus);
  or or_1 (or_1_out, negative_update, read_bus);
  or or_2 (or_2_out, overflow_update, read_bus);
  or or_3 (or_3_out, break_update, read_bus);
  or or_4 (or_4_out, decimal_update, read_bus);
  or or_5 (or_5_out, irq_update, read_bus);
  or or_6 (or_6_out, zero_update, read_bus);
  or or_7 (or_7_out, carry_update, read_bus);
  Register #(.width(1)) register_1 (
    .D(controlled_buffer_1_out[0]), .en(or_1_out), .clk(clock), .Q(negative), .clr(status_reset));
  Register #(.width(1)) register_2 (
    .D(controlled_buffer_1_out[1]), .en(or_2_out), .clk(clock), .Q(overflow), .clr(status_reset));
  Register #(.width(1)) register_3 (
    .D(controlled_buffer_1_out[2]), .en(or_3_out), .clk(clock), .Q(\break ), .clr(status_reset));
  Register #(.width(1)) register_4 (
    .D(controlled_buffer_1_out[3]), .en(or_4_out), .clk(clock), .Q(decimal), .clr(status_reset));
  Register #(.width(1)) register_5 (
    .D(controlled_buffer_1_out[4]), .en(or_5_out), .clk(clock), .Q(irq), .clr(status_reset));
  Register #(.width(1)) register_6 (
    .D(controlled_buffer_1_out[5]), .en(or_6_out), .clk(clock), .Q(zero), .clr(status_reset));
  Register #(.width(1)) register_7 (
    .D(controlled_buffer_1_out[6]), .en(or_7_out), .clk(clock), .Q(carry), .clr(status_reset));
  and and_1 (n_out, n_request, negative);
  and and_2 (o_out, o_request, overflow);
  and and_3 (b_out, b_request, \break );
  and and_4 (d_out, d_request, decimal);
  and and_5 (irq_out, irq_request, irq);
  and and_6 (z_out, z_request, zero);
  and and_7 (c_out, c_request, carry);
  assign d_bus_out = out_bus ? {1'b0, carry, zero, irq, decimal, \break , overflow, negative} : 8'bz;  // Controlled_Buffer controlled_buffer_3
  // also tied to GND on the sheet: controlled_buffer_1_out[7]
endmodule

module out_devices (
  input  enable,
  input  we,
  input  clock,
  input  [7:0] data_in,
  input  [7:0] address_io,
  output [7:0] port_a,
  output [7:0] port_b,
  output [7:0] port_c,
  output [7:0] port_d,
  output [7:0] port_e,
  output [7:0] port_f,
  output [7:0] port_g,
  output [7:0] port_h,
  output [7:0] port_i
);

  wire and_1_out, and_2_out, and_3_out, and_4_out, and_5_out, and_6_out, and_7_out, and_8_out, and_9_out,
       decoder_1_out0, decoder_1_out1, decoder_1_out2, decoder_1_out3, decoder_1_out4, decoder_1_out5,
       decoder_1_out6, decoder_1_out7, decoder_1_out8;

  Decoder #(.select(4)) decoder_1 (
    .out0(decoder_1_out0), .out1(decoder_1_out1), .out2(decoder_1_out2), .out3(decoder_1_out3),
    .out4(decoder_1_out4), .out5(decoder_1_out5), .out6(decoder_1_out6), .out7(decoder_1_out7),
    .out8(decoder_1_out8), .sel(address_io[3:0]), .en(enable));  // open: out9, out10, out11, out12, out13, out14, out15
  Register register_1 (.D(data_in), .en(and_1_out), .clk(clock), .Q(port_a));  // open: clr
  and and_1 (and_1_out, we, decoder_1_out0);
  Register register_2 (.D(data_in), .en(and_2_out), .clk(clock), .Q(port_b));  // open: clr
  and and_2 (and_2_out, we, decoder_1_out1);
  Register register_3 (.D(data_in), .en(and_3_out), .clk(clock), .Q(port_c));  // open: clr
  and and_3 (and_3_out, we, decoder_1_out2);
  Register register_4 (.D(data_in), .en(and_4_out), .clk(clock), .Q(port_d));  // open: clr
  and and_4 (and_4_out, we, decoder_1_out3);
  Register register_5 (.D(data_in), .en(and_5_out), .clk(clock), .Q(port_e));  // open: clr
  and and_5 (and_5_out, we, decoder_1_out4);
  Register register_6 (.D(data_in), .en(and_6_out), .clk(clock), .Q(port_f));  // open: clr
  and and_6 (and_6_out, we, decoder_1_out5);
  Register register_7 (.D(data_in), .en(and_7_out), .clk(clock), .Q(port_g));  // open: clr
  and and_7 (and_7_out, we, decoder_1_out6);
  Register register_8 (.D(data_in), .en(and_8_out), .clk(clock), .Q(port_h));  // open: clr
  and and_8 (and_8_out, we, decoder_1_out7);
  Register register_9 (.D(data_in), .en(and_9_out), .clk(clock), .Q(port_i));  // open: clr
  and and_9 (and_9_out, we, decoder_1_out8);
endmodule

module video_card (
  input  clock,
  input  [7:0] buffer_in,
  input  [7:0] x_co,
  input  [7:0] y_co,
  input  [7:0] mode,
  output [7:0] frame_buffer,
  output [5:0] x_coordinate,
  output [5:0] y_coordinate
);

  wire counter_1_carry, decoder_1_out0, decoder_1_out1, decoder_1_out2, not_1_out, or_1_out, or_2_out;
  wire [7:0] controlled_buffer_1_out, ram_1_dout;
  wire [11:0] controlled_buffer_2_out;

  Decoder #(.select(4)) decoder_1 (
    .out0(decoder_1_out0), .out1(decoder_1_out1), .out2(decoder_1_out2), .sel(mode[3:0]), .en(1'b1));  // open: out3, out4, out5, out6, out7, out8, out9, out10, out11, out12, out13, out14, out15
  assign controlled_buffer_1_out = or_1_out ? buffer_in : 8'bz;  // Controlled_Buffer controlled_buffer_1
  assign controlled_buffer_2_out = decoder_1_out2 ? {y_co[5:0], x_co[5:0]} : 12'bz;  // Controlled_Buffer controlled_buffer_2
  or or_1 (or_1_out, decoder_1_out2, decoder_1_out1);
  or or_2 (or_2_out, decoder_1_out1, decoder_1_out0);
  RAM #(.addrWidth(12), .enables("line")) ram_1 (
    .addr(controlled_buffer_2_out), .we(or_1_out), .clk(clock), .din(controlled_buffer_1_out),
    .dout(ram_1_dout));
  assign controlled_buffer_2_out = or_2_out ? {y_coordinate, x_coordinate} : 12'bz;  // Controlled_Buffer controlled_buffer_3
  Counter #(.max('h3f), .width(6)) counter_1 (
    .up(1'b1), .count(or_2_out), .clk(clock), .carry(counter_1_carry), .Q(x_coordinate));  // open: clr, load, D
  Counter #(.max('h3f), .width(6)) counter_2 (
    .up(1'b1), .count(counter_1_carry), .clk(clock), .Q(y_coordinate));  // open: clr, load, D, carry
  Register register_1 (.D(ram_1_dout), .en(not_1_out), .clk(clock), .Q(frame_buffer));  // open: clr
  not not_1 (not_1_out, decoder_1_out2);
endmodule

module rom_3_decoder (
  input  [7:0] buffer_in,
  output alu_a_we,
  output sum_actived,
  output sub_actived,
  output and_actived,
  output or_actived,
  output eor_actived,
  output shift_l,
  output shift_r,
  output rotate_l,
  output rotare_r,
  output BIT,
  output cmp_active,
  output inc,
  output dec,
  output sum_actived_16b,
  output alu_oe,
  output bcd_mode,
  output load_c,
  output load_from_ad
);

  wire decoder_1_out2, decoder_1_out14;

  Decoder #(.select(4)) decoder_1 (
    .out0(sum_actived), .out1(sub_actived), .out2(decoder_1_out2), .out3(or_actived), .out4(eor_actived),
    .out5(shift_l), .out6(shift_r), .out7(rotate_l), .out8(rotare_r), .out9(BIT), .out10(cmp_active),
    .out11(load_from_ad), .out12(inc), .out13(dec), .out14(decoder_1_out14), .out15(load_c),
    .sel(buffer_in[4:1]), .en(buffer_in[7]));
  or or_1 (and_actived, decoder_1_out2, BIT);
  or or_2 (sum_actived_16b, decoder_1_out14, load_c);

  assign alu_a_we = buffer_in[0];
  assign alu_oe = buffer_in[5];
  assign bcd_mode = buffer_in[6];
endmodule

module alu_test (
  input  clock,
  input  [7:0] buffer_in,
  input  alu_a_in,
  input  alu_b_in,
  input  [7:0] status_in,
  input  alu_sum_actived,
  input  alu_inc,
  input  alu_sub,
  input  alu_16b_sum,
  input  alu_oe,
  input  load_c,
  input  abl_oe,
  input  abh_oe,
  output [3:0] alu_control_status,
  output [3:0] alu_status,
  output [7:0] alu_out,
  output [7:0] abl_out,
  output [7:0] abh_out,
  output disable_pc
);

  wire adder_1_cout, adder_2_cout, adder_3_cout, adder_4_cout, adder_5_cout, controlled_buffer_2_out,
       controlled_buffer_12_out, controlled_buffer_13_out, controlled_buffer_14_out,
       controlled_buffer_16_out, d_ff_1_q, d_ff_2_q, d_ff_3_q, d_ff_4_q, d_ff_6_q, d_ff_7_q, not_1_out,
       not_2_out, not_3_out, not_4_out, not_5_out, not_6_out, or_1_out;
  wire [3:0] register_1_q_2;
  wire [6:0] register_1_q;
  wire [7:0] a_q, abh_q, abl_q, adder_1_out, adder_2_out, adder_3_out, adder_4_out, adder_5_out, b_q, c_q,
       controlled_buffer_1_out, controlled_buffer_3_out, controlled_buffer_4_out, controlled_buffer_5_out,
       controlled_buffer_6_out, controlled_buffer_7_out, controlled_buffer_8_out, controlled_buffer_9_out,
       controlled_buffer_10_out, controlled_buffer_11_out, controlled_buffer_15_out,
       controlled_buffer_17_out, controlled_inverter_1_out;

  Register a (.D(buffer_in), .en(alu_a_in), .clk(clock), .Q(a_q));  // open: clr
  D_Flip_Flop d_ff_1 (.D(alu_sum_actived), .clk(clock), .Q(d_ff_1_q));  // open: Qn, preset, reset
  D_Flip_Flop d_ff_2 (.D(alu_inc), .clk(clock), .Q(d_ff_2_q));  // open: Qn, preset, reset
  D_Flip_Flop d_ff_3 (.D(alu_sub), .clk(clock), .Q(d_ff_3_q));  // open: Qn, preset, reset
  D_Flip_Flop d_ff_4 (.D(alu_16b_sum), .clk(clock), .Q(d_ff_4_q));  // open: Qn, preset, reset
  Register b (.D(buffer_in), .en(alu_b_in), .clk(clock), .Q(b_q));  // open: clr
  Register c (.D(buffer_in), .en(load_c), .clk(clock), .Q(c_q));  // open: clr
  assign controlled_buffer_1_out = d_ff_4_q ? c_q : 8'bz;  // Controlled_Buffer controlled_buffer_1
  assign controlled_buffer_2_out = d_ff_1_q ? status_in[6] : 1'bz;  // Controlled_Buffer controlled_buffer_2
  assign controlled_buffer_3_out = d_ff_1_q ? a_q : 8'bz;  // Controlled_Buffer controlled_buffer_3
  assign controlled_buffer_4_out = d_ff_1_q ? b_q : 8'bz;  // Controlled_Buffer controlled_buffer_4
  assign controlled_buffer_5_out = d_ff_2_q ? a_q : 8'bz;  // Controlled_Buffer controlled_buffer_5
  assign controlled_buffer_6_out = d_ff_2_q ? 8'h1 : 8'bz;  // Controlled_Buffer controlled_buffer_6
  assign controlled_inverter_1_out = d_ff_3_q ? ~a_q : 8'bz;  // Controlled_Inverter controlled_inverter_1
  assign controlled_buffer_7_out = d_ff_3_q ? b_q : 8'bz;  // Controlled_Buffer controlled_buffer_7
  assign controlled_buffer_8_out = d_ff_4_q ? a_q : 8'bz;  // Controlled_Buffer controlled_buffer_8
  assign controlled_buffer_9_out = d_ff_4_q ? controlled_buffer_1_out : 8'bz;  // Controlled_Buffer controlled_buffer_9
  assign controlled_buffer_10_out = d_ff_4_q ? {8{1'b0}} : 8'bz;  // Controlled_Buffer controlled_buffer_10
  assign controlled_buffer_11_out = d_ff_1_q ? adder_1_out : 8'bz;  // Controlled_Buffer controlled_buffer_11
  Adder adder_1 (
    .a(controlled_buffer_3_out), .b(controlled_buffer_4_out), .out(adder_1_out),
    .cin(controlled_buffer_2_out), .cout(adder_1_cout));
  assign controlled_buffer_12_out = d_ff_1_q ? adder_1_cout : 1'bz;  // Controlled_Buffer controlled_buffer_12
  Adder adder_2 (
    .a(controlled_buffer_5_out), .b(controlled_buffer_6_out), .out(adder_2_out), .cin(1'b0),
    .cout(adder_2_cout));
  assign controlled_buffer_13_out = d_ff_3_q ? 1'b1 : 1'bz;  // Controlled_Buffer controlled_buffer_13
  Adder adder_3 (
    .a(controlled_inverter_1_out), .b(controlled_buffer_7_out), .out(adder_3_out),
    .cin(controlled_buffer_13_out), .cout(adder_3_cout));
  assign controlled_buffer_14_out = d_ff_4_q ? status_in[6] : 1'bz;  // Controlled_Buffer controlled_buffer_14
  assign controlled_buffer_15_out = d_ff_4_q ? adder_4_out : 8'bz;  // Controlled_Buffer controlled_buffer_15
  Adder adder_4 (
    .a(controlled_buffer_8_out), .b(controlled_buffer_9_out), .out(adder_4_out),
    .cin(controlled_buffer_14_out), .cout(adder_4_cout));
  assign controlled_buffer_16_out = d_ff_4_q ? adder_4_cout : 1'bz;  // Controlled_Buffer controlled_buffer_16
  assign controlled_buffer_17_out = d_ff_4_q ? adder_5_out : 8'bz;  // Controlled_Buffer controlled_buffer_17
  Adder adder_5 (
    .a(b_q), .b(controlled_buffer_10_out), .out(adder_5_out), .cin(controlled_buffer_16_out),
    .cout(adder_5_cout));
  assign controlled_buffer_12_out = d_ff_4_q ? adder_5_cout : 1'bz;  // Controlled_Buffer controlled_buffer_18
  D_Flip_Flop d_ff_5 (.D(controlled_buffer_12_out), .clk(not_1_out), .Q(register_1_q_2[3]));  // open: Qn, preset, reset
  not not_1 (not_1_out, clock);
  or or_1 (or_1_out, d_ff_3_q, d_ff_1_q, d_ff_2_q, d_ff_4_q);
  assign controlled_buffer_11_out = d_ff_2_q ? adder_2_out : 8'bz;  // Controlled_Buffer controlled_buffer_19
  assign controlled_buffer_12_out = d_ff_2_q ? adder_2_cout : 1'bz;  // Controlled_Buffer controlled_buffer_20
  assign controlled_buffer_11_out = d_ff_3_q ? adder_3_out : 8'bz;  // Controlled_Buffer controlled_buffer_21
  assign controlled_buffer_12_out = d_ff_3_q ? adder_3_cout : 1'bz;  // Controlled_Buffer controlled_buffer_22
  assign controlled_buffer_15_out = controlled_buffer_11_out;  // Buffer buffer_1, 8 bits wide
  not not_2 (not_2_out, clock);
  assign controlled_buffer_15_out = controlled_buffer_11_out;  // Buffer buffer_2, 8 bits wide
  assign controlled_buffer_17_out = controlled_buffer_11_out;  // Buffer buffer_3, 8 bits wide
  nor nor_1 (register_1_q_2[2], register_1_q[0], register_1_q[1], register_1_q[2], register_1_q[3], register_1_q[4], register_1_q[5], register_1_q[6], register_1_q_2[0]);
  Register register_1 (
    .D(controlled_buffer_15_out), .en(or_1_out), .clk(not_2_out), .Q({register_1_q_2[0], register_1_q}));  // open: clr
  Register abl (.D(controlled_buffer_15_out), .en(or_1_out), .clk(not_3_out), .Q(abl_q));  // open: clr
  not not_3 (not_3_out, clock);
  Register abh (.D(controlled_buffer_17_out), .en(or_1_out), .clk(not_4_out), .Q(abh_q));  // open: clr
  not not_4 (not_4_out, clock);
  assign abl_out = d_ff_6_q ? abl_q : 8'bz;  // Controlled_Buffer controlled_buffer_23
  assign abh_out = d_ff_7_q ? abh_q : 8'bz;  // Controlled_Buffer controlled_buffer_24
  assign alu_control_status = alu_oe ? 4'b1111 : 4'bz;  // Controlled_Buffer controlled_buffer_25
  assign alu_status = alu_oe ? {register_1_q_2[3:2], 1'b0, register_1_q_2[0]} : 4'bz;  // Controlled_Buffer controlled_buffer_26
  assign alu_out = alu_oe ? {register_1_q_2[0], register_1_q} : 8'bz;  // Controlled_Buffer controlled_buffer_27
  D_Flip_Flop d_ff_6 (.D(abl_oe), .clk(clock), .Q(d_ff_6_q));  // open: Qn, preset, reset
  D_Flip_Flop d_ff_7 (.D(abh_oe), .clk(clock), .Q(d_ff_7_q));  // open: Qn, preset, reset
  assign alu_control_status = not_5_out ? 4'b0000 : 4'bz;  // Controlled_Buffer controlled_buffer_28
  not not_5 (not_5_out, alu_oe);
  assign alu_status = not_6_out ? 4'b0000 : 4'bz;  // Controlled_Buffer controlled_buffer_29
  not not_6 (not_6_out, alu_oe);
  or or_2 (disable_pc, abl_oe, d_ff_7_q);
endmodule

module address_bus_control (
  input  clk,
  input  [7:0] low_bus,
  input  low_oe,
  input  hight_oe,
  input  [7:0] hight_bus,
  input  dis,
  output disable_pc,
  output [7:0] low_out,
  output [7:0] hight_out,
  output disable_other
);

  wire and_1_out, and_2_out, and_4_out, d_ff_1_q, d_ff_2_q, nor_1_out, not_1_out, not_2_out, not_3_out,
       not_4_out;
  wire [7:0] register_1_q, register_2_q;

  D_Flip_Flop d_ff_1 (.D(low_oe), .clk(clk), .Q(d_ff_1_q));  // open: Qn, preset, reset
  Register register_1 (.D(low_bus), .en(low_oe), .clk(clk), .Q(register_1_q));  // open: clr
  Register register_2 (.D(hight_bus), .en(hight_oe), .clk(clk), .Q(register_2_q));  // open: clr
  D_Flip_Flop d_ff_2 (.D(hight_oe), .clk(clk), .Q(d_ff_2_q));  // open: Qn, preset, reset
  assign low_out = and_1_out ? register_1_q : 8'bz;  // Controlled_Buffer controlled_buffer_1
  and and_1 (and_1_out, not_1_out, d_ff_1_q);
  not not_1 (not_1_out, dis);
  assign hight_out = and_2_out ? register_2_q : 8'bz;  // Controlled_Buffer controlled_buffer_2
  and and_2 (and_2_out, not_2_out, d_ff_2_q);
  not not_2 (not_2_out, dis);
  not not_3 (not_3_out, dis);
  not not_4 (not_4_out, d_ff_2_q);
  assign hight_out = and_4_out ? {8{1'b0}} : 8'bz;  // Controlled_Buffer controlled_buffer_3
  nor nor_1 (nor_1_out, d_ff_1_q, d_ff_2_q);
  and and_3 (disable_pc, not_3_out, nor_1_out);
  and and_4 (and_4_out, d_ff_1_q, not_4_out);
  or or_1 (disable_other, d_ff_2_q, d_ff_1_q);
endmodule

module new_USPU (
  input  startup,
  input  reset,
  input  nmi,
  input  irq,
  input  [7:0] d_bus_in,
  input  clock,
  input  [7:0] control_in,
  input  [7:0] adl_in,
  input  [7:0] adh_in,
  input  mic_reset,
  input  pcl_rom1,
  input  pch_rom1,
  output [15:0] adr,
  output [7:0] d_bus_out,
  output [7:0] adl_out,
  output [7:0] adh_out,
  output alu_b_in,
  output alu_oe_abl,
  output alu_oe_abh
);

  wire d_ff_1_q, not_1_out, or_1_out, or_2_out, or_3_out, rom2_decoder_1_inc_reg_by_2,
       rom2_decoder_1_load_saved, rom2_decoder_1_pc_count, rom2_decoder_1_pc_load_from_adr,
       rom2_decoder_1_pc_load_reg, rom2_decoder_1_pc_save_adr, rom2_decoder_1_pch_bus,
       rom2_decoder_1_pch_load, rom2_decoder_1_pcl_bus, rom2_decoder_1_pcl_load, rom2_decoder_1_sp_dec,
       rom2_decoder_1_sp_inc, rom2_decoder_1_sp_oe, rom2_decoder_1_sp_reset, rom2_decoder_1_sp_to_bus;
  wire [7:0] uspu_buffer_red_1_bus_out;
  wire [15:0] pc_unit_3_1_address_out, sp_unit_1_sp_out;

  D_Flip_Flop d_ff_1 (.D(mic_reset), .clk(clock), .Q(d_ff_1_q));  // open: Qn, preset, reset
  rom2_decoder rom2_decoder_1 (
    .data_in(control_in), .pc_count(rom2_decoder_1_pc_count), .pc_load_reg(rom2_decoder_1_pc_load_reg),
    .pc_load_from_adr(rom2_decoder_1_pc_load_from_adr), .pcl_load(rom2_decoder_1_pcl_load),
    .pch_load(rom2_decoder_1_pch_load), .pcl_bus(rom2_decoder_1_pcl_bus), .pch_bus(rom2_decoder_1_pch_bus),
    .sp_oe(rom2_decoder_1_sp_oe), .sp_inc(rom2_decoder_1_sp_inc), .sp_dec(rom2_decoder_1_sp_dec),
    .sp_reset(rom2_decoder_1_sp_reset), .inc_reg_by_2(rom2_decoder_1_inc_reg_by_2), .alu_b_in(alu_b_in),
    .alu_output_abl(alu_oe_abl), .alu_output_abh(alu_oe_abh), .sp_to_bus(rom2_decoder_1_sp_to_bus),
    .pc_save_adr(rom2_decoder_1_pc_save_adr), .load_saved(rom2_decoder_1_load_saved));  // open: pc_oe
  or or_1 (or_1_out, rom2_decoder_1_pcl_load, pcl_rom1);
  or or_2 (or_2_out, rom2_decoder_1_pch_load, pch_rom1);
  USPU_buffer_red uspu_buffer_red_1 (
    .pcl_load_rom1(pcl_rom1), .pch_load_rom1(pch_rom1), .pch_load(rom2_decoder_1_pch_load),
    .pcl_load(rom2_decoder_1_pcl_load), .nmi(nmi), .reset(reset), .irq(irq), .startup(startup),
    .bus_dati(d_bus_in), .bus_out(uspu_buffer_red_1_bus_out));
  PC_unit_3 pc_unit_3_1 (
    .clock(clock), .d_bus(uspu_buffer_red_1_bus_out), .pcl_we(or_1_out), .pch_we(or_2_out), .adl_in(adl_in),
    .pc_load_reg(rom2_decoder_1_pc_load_reg), .adh_in(adh_in), .pcl_oe(rom2_decoder_1_pcl_bus),
    .pch_oe(rom2_decoder_1_pch_bus), .mic_reset(d_ff_1_q), .pc_count(rom2_decoder_1_pc_count),
    .load_from_adr(rom2_decoder_1_pc_load_from_adr), .inc_reg_by_2(rom2_decoder_1_inc_reg_by_2),
    .save_register(rom2_decoder_1_pc_save_adr), .load_saved(rom2_decoder_1_load_saved),
    .address_out(pc_unit_3_1_address_out), .d_bus_out(d_bus_out), .adl_out(adl_out), .adh_out(adh_out));
  SP_unit sp_unit_1 (
    .sp_oe(rom2_decoder_1_sp_oe), .sp_reset(rom2_decoder_1_sp_reset), .clk(clock),
    .sp_inc(rom2_decoder_1_sp_inc), .sp_dec(rom2_decoder_1_sp_dec), .buffer_in(uspu_buffer_red_1_bus_out),
    .sp_to_bus(rom2_decoder_1_sp_to_bus), .d_bus_out(d_bus_out), .sp_out(sp_unit_1_sp_out));
  assign adr = not_1_out ? pc_unit_3_1_address_out : 16'bz;  // Controlled_Buffer controlled_buffer_1
  not not_1 (not_1_out, or_3_out);
  assign adr = or_3_out ? sp_unit_1_sp_out : 16'bz;  // Controlled_Buffer controlled_buffer_2
  or or_3 (or_3_out, rom2_decoder_1_sp_oe, rom2_decoder_1_sp_reset, rom2_decoder_1_sp_inc, rom2_decoder_1_sp_dec, rom2_decoder_1_sp_to_bus, 1'b0);
endmodule

module PC_unit_3 (
  input  clock,
  input  [7:0] d_bus,
  input  pcl_we,
  input  pch_we,
  input  [7:0] adl_in,
  input  pc_load_reg,
  input  [7:0] adh_in,
  input  pcl_oe,
  input  pch_oe,
  input  mic_reset,
  input  pc_count,
  input  load_from_adr,
  input  inc_reg_by_2,
  input  save_register,
  input  load_saved,
  output [15:0] address_out,
  output [7:0] d_bus_out,
  output [7:0] adl_out,
  output [7:0] adh_out
);

  wire adder_1_cout, adder_2_cout, low_carry, or_1_out, or_2_out, or_3_out, or_4_out;
  wire [7:0] adder_1_out, adder_2_out, controlled_buffer_1_out, controlled_buffer_2_out,
       controlled_buffer_7_out, controlled_buffer_9_out, controlled_buffer_11_out, controlled_buffer_12_out,
       controlled_buffer_15_out, controlled_buffer_16_out, pch_q, pcl_q, register_1_q, register_2_q;

  assign controlled_buffer_1_out = pcl_we ? d_bus : 8'bz;  // Controlled_Buffer controlled_buffer_1
  assign controlled_buffer_2_out = pch_we ? d_bus : 8'bz;  // Controlled_Buffer controlled_buffer_2
  or or_1 (or_1_out, pc_load_reg, load_saved, load_from_adr);
  or or_2 (or_2_out, pc_load_reg, load_saved, load_from_adr);
  assign controlled_buffer_1_out = mic_reset ? controlled_buffer_15_out : 8'bz;  // Controlled_Buffer controlled_buffer_3
  assign controlled_buffer_1_out = inc_reg_by_2 ? adder_1_out : 8'bz;  // Controlled_Buffer controlled_buffer_4
  assign controlled_buffer_2_out = mic_reset ? controlled_buffer_16_out : 8'bz;  // Controlled_Buffer controlled_buffer_5
  assign controlled_buffer_2_out = inc_reg_by_2 ? adder_2_out : 8'bz;  // Controlled_Buffer controlled_buffer_6
  or or_3 (or_3_out, pcl_we, inc_reg_by_2, mic_reset);
  or or_4 (or_4_out, pch_we, mic_reset, inc_reg_by_2);
  assign controlled_buffer_7_out = pc_load_reg ? pcl_q : 8'bz;  // Controlled_Buffer controlled_buffer_7
  assign controlled_buffer_7_out = load_from_adr ? adl_in : 8'bz;  // Controlled_Buffer controlled_buffer_8
  assign controlled_buffer_9_out = pc_load_reg ? pch_q : 8'bz;  // Controlled_Buffer controlled_buffer_9
  assign controlled_buffer_9_out = load_from_adr ? adh_in : 8'bz;  // Controlled_Buffer controlled_buffer_10
  Register pcl (.D(controlled_buffer_1_out), .en(or_3_out), .clk(clock), .Q(pcl_q));  // open: clr
  Register pch (.D(controlled_buffer_2_out), .en(or_4_out), .clk(clock), .Q(pch_q));  // open: clr
  Counter low (
    .clr(1'b0), .load(or_1_out), .count(pc_count), .clk(clock), .D(controlled_buffer_7_out),
    .carry(low_carry), .Q(address_out[7:0]));  // open: up
  Counter hight (
    .clr(1'b0), .load(or_2_out), .up(low_carry), .count(low_carry), .clk(clock), .D(controlled_buffer_9_out),
    .Q(address_out[15:8]));  // open: carry
  Register register_1 (.D(address_out[7:0]), .en(save_register), .clk(clock), .Q(register_1_q));  // open: clr
  Register register_2 (.D(address_out[15:8]), .en(save_register), .clk(clock), .Q(register_2_q));  // open: clr
  Adder adder_1 (.a(controlled_buffer_11_out), .b(8'h3), .out(adder_1_out), .cin(1'b0), .cout(adder_1_cout));
  Adder adder_2 (
    .a(controlled_buffer_12_out), .b({8{1'b0}}), .out(adder_2_out), .cin(adder_1_cout), .cout(adder_2_cout));
  assign controlled_buffer_11_out = inc_reg_by_2 ? pcl_q : 8'bz;  // Controlled_Buffer controlled_buffer_11
  assign controlled_buffer_12_out = inc_reg_by_2 ? pch_q : 8'bz;  // Controlled_Buffer controlled_buffer_12
  assign controlled_buffer_7_out = load_saved ? register_1_q : 8'bz;  // Controlled_Buffer controlled_buffer_13
  assign controlled_buffer_9_out = load_saved ? register_2_q : 8'bz;  // Controlled_Buffer controlled_buffer_14
  assign controlled_buffer_15_out = mic_reset ? address_out[7:0] : 8'bz;  // Controlled_Buffer controlled_buffer_15
  assign controlled_buffer_16_out = mic_reset ? address_out[15:8] : 8'bz;  // Controlled_Buffer controlled_buffer_16
  assign d_bus_out = pcl_oe ? pcl_q : 8'bz;  // Controlled_Buffer controlled_buffer_17
  assign d_bus_out = pch_oe ? pch_q : 8'bz;  // Controlled_Buffer controlled_buffer_18

  assign adh_out = address_out[15:8];
  assign adl_out = address_out[7:0];
  // also tied to GND on the sheet: adder_2_cout
endmodule
module alu_test_2 (
  input  clock,
  input  [7:0] status_in,
  input  [7:0] buffer_in,
  input  alu_a_in,
  input  alu_b_in,
  input  load_c,
  input  [7:0] adl_in,
  input  alu_inc,
  input  alu_sum_actived,
  input  [7:0] adh_in,
  input  alu_16b_sum,
  input  alu_sub,
  input  alu_cmp,
  input  dec,
  input  alu_oe,
  input  abl_oe,
  input  abh_oe,
  input  load_from_ad,
  output [3:0] alu_control,
  output [3:0] alu_flag,
  output [7:0] d_bus_out,
  output [7:0] adl,
  output [7:0] adh,
  output [7:0] low_b,
  output [7:0] hight_b,
  output dis_pc
);

  wire d_ff_1_q, d_ff_2_q, d_ff_3_q, d_ff_4_q, d_ff_5_q, d_ff_6_q, d_ff_7_q, d_ff_8_q, d_ff_9_q, not_1_out,
       not_2_out, not_3_out, not_4_out, not_5_out, not_6_out, or_1_out, or_2_out, or_3_out, or_4_out,
       or_5_out, or_6_out;
  wire [2:0] dec_unit_1_n_out, inc_unit_1_n_out;
  wire [3:0] cmp_unit_1_n_out, controlled_buffer_3_out, controlled_buffer_12_out, controlled_buffer_22_out,
       register_1_q, register_2_q, sub_unit_1_n_out, sum_unit_1_n_out;
  wire [7:0] a_bus, abh_q, abl_q, b_bus, bus_out_q, c_bus, controlled_buffer_1_out, controlled_buffer_2_out,
       inc_unit_1_d_out, sum_16b_unit_1_h_out, sum_16b_unit_1_l_ou;

  D_Flip_Flop d_ff_1 (.D(alu_inc), .clk(clock), .Q(d_ff_1_q));  // open: Qn, preset, reset
  D_Flip_Flop d_ff_2 (.D(alu_sum_actived), .clk(clock), .Q(d_ff_2_q));  // open: Qn, preset, reset
  D_Flip_Flop d_ff_3 (.D(alu_16b_sum), .clk(clock), .Q(d_ff_3_q));  // open: Qn, preset, reset
  D_Flip_Flop d_ff_4 (.D(alu_sub), .clk(clock), .Q(d_ff_4_q));  // open: Qn, preset, reset
  D_Flip_Flop d_ff_5 (.D(alu_cmp), .clk(clock), .Q(d_ff_5_q));  // open: Qn, preset, reset
  D_Flip_Flop d_ff_6 (.D(dec), .clk(clock), .Q(d_ff_6_q));  // open: Qn, preset, reset
  assign controlled_buffer_1_out = not_1_out ? buffer_in : 8'bz;  // Controlled_Buffer controlled_buffer_1
  or or_1 (or_1_out, alu_a_in, load_from_ad);
  not not_1 (not_1_out, load_from_ad);
  Register b (.D(controlled_buffer_2_out), .en(or_2_out), .clk(clock), .Q(b_bus));  // open: clr
  assign controlled_buffer_2_out = not_2_out ? buffer_in : 8'bz;  // Controlled_Buffer controlled_buffer_2
  or or_2 (or_2_out, alu_b_in, load_from_ad);
  not not_2 (not_2_out, load_from_ad);
  Register c (.D(buffer_in), .en(load_c), .clk(clock), .Q(c_bus));  // open: clr
  Register a (.D(controlled_buffer_1_out), .en(or_1_out), .clk(clock), .Q(a_bus));  // open: clr
  or or_3 (or_3_out, d_ff_1_q, d_ff_2_q, d_ff_3_q, d_ff_4_q, d_ff_5_q, d_ff_6_q);
  inc_unit inc_unit_1 (
    .enable(d_ff_1_q), .a_in(a_bus), .d_out(inc_unit_1_d_out), .z_out(inc_unit_1_n_out[2]),
    .n_out(inc_unit_1_n_out[0]));
  dec_unit dec_unit_1 (
    .enable(d_ff_6_q), .a_in(a_bus), .d_out(inc_unit_1_d_out), .z_out(dec_unit_1_n_out[2]),
    .n_out(dec_unit_1_n_out[0]));
  sum_unit sum_unit_1 (
    .enable(d_ff_2_q), .a_in(a_bus), .b_in(b_bus), .c_in(status_in[6]), .d_out(inc_unit_1_d_out),
    .c_out(sum_unit_1_n_out[3]), .z_out(sum_unit_1_n_out[2]), .n_out(sum_unit_1_n_out[0]),
    .v_out(sum_unit_1_n_out[1]));
  sub_unit sub_unit_1 (
    .enable(d_ff_4_q), .a_in(a_bus), .b_in(b_bus), .c_in(status_in[6]), .d_out(inc_unit_1_d_out),
    .c_out(sub_unit_1_n_out[3]), .z_out(sub_unit_1_n_out[2]), .n_out(sub_unit_1_n_out[0]),
    .v_out(sub_unit_1_n_out[1]));
  sum_16b_unit sum_16b_unit_1 (
    .enable(d_ff_3_q), .a_in(a_bus), .b_in(b_bus), .c_in(c_bus), .l_ou(sum_16b_unit_1_l_ou),
    .h_out(sum_16b_unit_1_h_out));
  cmp_unit cmp_unit_1 (
    .enable(d_ff_5_q), .a_in(a_bus), .b_in(b_bus), .d_out(inc_unit_1_d_out), .c_out(cmp_unit_1_n_out[3]),
    .z_out(cmp_unit_1_n_out[2]), .n_out(cmp_unit_1_n_out[0]));
  assign sum_16b_unit_1_l_ou = inc_unit_1_d_out;  // Buffer buffer_1, 8 bits wide
  Register #(.width(4)) register_1 (
    .D(controlled_buffer_12_out), .en(or_3_out), .clk(not_3_out), .Q(register_1_q));  // open: clr
  Register #(.width(4)) register_2 (
    .D(controlled_buffer_3_out), .en(or_3_out), .clk(not_3_out), .Q(register_2_q));  // open: clr
  Register bus_out (.D(sum_16b_unit_1_l_ou), .en(or_3_out), .clk(not_3_out), .Q(bus_out_q));  // open: clr
  not not_3 (not_3_out, clock);
  Register abl (.D(sum_16b_unit_1_l_ou), .en(or_3_out), .clk(not_4_out), .Q(abl_q));  // open: clr
  assign sum_16b_unit_1_l_ou = inc_unit_1_d_out;  // Buffer buffer_2, 8 bits wide
  not not_4 (not_4_out, clock);
  Register abh (.D(sum_16b_unit_1_h_out), .en(or_3_out), .clk(not_5_out), .Q(abh_q));  // open: clr
  assign sum_16b_unit_1_h_out = inc_unit_1_d_out;  // Buffer buffer_3, 8 bits wide
  not not_5 (not_5_out, clock);
  assign controlled_buffer_3_out = d_ff_5_q ? {cmp_unit_1_n_out[3:2], 1'b0, cmp_unit_1_n_out[0]} : 4'bz;  // Controlled_Buffer controlled_buffer_3
  D_Flip_Flop d_ff_7 (.D(abl_oe), .clk(clock), .Q(d_ff_7_q));  // open: Qn, preset, reset
  assign controlled_buffer_3_out = d_ff_1_q ? {1'b0, inc_unit_1_n_out[2], 1'b0, inc_unit_1_n_out[0]} : 4'bz;  // Controlled_Buffer controlled_buffer_4
  assign controlled_buffer_3_out = d_ff_6_q ? {1'b0, dec_unit_1_n_out[2], 1'b0, dec_unit_1_n_out[0]} : 4'bz;  // Controlled_Buffer controlled_buffer_5
  assign controlled_buffer_3_out = d_ff_2_q ? sum_unit_1_n_out : 4'bz;  // Controlled_Buffer controlled_buffer_6
  assign controlled_buffer_3_out = d_ff_4_q ? sub_unit_1_n_out : 4'bz;  // Controlled_Buffer controlled_buffer_7
  assign controlled_buffer_3_out = d_ff_3_q ? 4'b0000 : 4'bz;  // Controlled_Buffer controlled_buffer_8
  D_Flip_Flop d_ff_8 (.D(or_4_out), .clk(not_3_out), .Q(d_ff_8_q));  // open: Qn, preset, reset
  assign d_bus_out = alu_oe ? bus_out_q : 8'bz;  // Controlled_Buffer controlled_buffer_9
  or or_4 (or_4_out, alu_oe, d_ff_7_q, d_ff_9_q);
  assign adl = d_ff_7_q ? abl_q : 8'bz;  // Controlled_Buffer controlled_buffer_10
  assign adh = d_ff_9_q ? abh_q : 8'bz;  // Controlled_Buffer controlled_buffer_11
  D_Flip_Flop d_ff_9 (.D(abh_oe), .clk(clock), .Q(d_ff_9_q));  // open: Qn, preset, reset
  or or_5 (or_5_out, d_ff_1_q, d_ff_6_q);
  assign controlled_buffer_12_out = or_6_out ? 4'b1111 : 4'bz;  // Controlled_Buffer controlled_buffer_12
  or or_6 (or_6_out, d_ff_2_q, d_ff_4_q);
  assign controlled_buffer_12_out = d_ff_3_q ? 4'b0000 : 4'bz;  // Controlled_Buffer controlled_buffer_13
  assign controlled_buffer_12_out = d_ff_5_q ? 4'b1101 : 4'bz;  // Controlled_Buffer controlled_buffer_14
  assign low_b = abl_oe ? abl_q : 8'bz;  // Controlled_Buffer controlled_buffer_15
  assign hight_b = abh_oe ? abh_q : 8'bz;  // Controlled_Buffer controlled_buffer_16
  or or_7 (dis_pc, d_ff_9_q, d_ff_7_q);
  assign controlled_buffer_12_out = or_5_out ? 4'b0101 : 4'bz;  // Controlled_Buffer controlled_buffer_17
  assign alu_control = d_ff_8_q ? register_1_q : 4'bz;  // Controlled_Buffer controlled_buffer_18
  assign alu_flag = d_ff_8_q ? register_2_q : 4'bz;  // Controlled_Buffer controlled_buffer_19
  assign controlled_buffer_1_out = load_from_ad ? adl_in : 8'bz;  // Controlled_Buffer controlled_buffer_20
  assign controlled_buffer_2_out = load_from_ad ? adh_in : 8'bz;  // Controlled_Buffer controlled_buffer_21
  assign alu_control = controlled_buffer_22_out;  // Buffer buffer_4, 4 bits wide
  assign alu_flag = controlled_buffer_22_out;  // Buffer buffer_5, 4 bits wide
  assign controlled_buffer_22_out = not_6_out ? 4'b0000 : 4'bz;  // Controlled_Buffer controlled_buffer_22
  not not_6 (not_6_out, d_ff_8_q);

  // Other names for the same wires on the sheet: carry_in = status_in[6]
endmodule

module inc_unit (
  input  enable,
  input  [7:0] a_in,
  output [7:0] d_out,
  output z_out,
  output n_out
);

  wire adder_1_cout, and_1_out, and_2_out, and_3_out, not_1_out, not_2_out, not_3_out, not_4_out, not_5_out,
       not_6_out, not_7_out, not_8_out, not_9_out;
  wire [7:0] adder_1_out, controlled_buffer_1_out, controlled_buffer_2_out;

  assign controlled_buffer_1_out = enable ? a_in : 8'bz;  // Controlled_Buffer controlled_buffer_1
  assign controlled_buffer_2_out = enable ? 8'h1 : 8'bz;  // Controlled_Buffer controlled_buffer_2
  Adder adder_1 (
    .a(controlled_buffer_1_out), .b(controlled_buffer_2_out), .out(adder_1_out), .cin(1'b0),
    .cout(adder_1_cout));
  assign d_out = enable ? adder_1_out : 8'bz;  // Controlled_Buffer controlled_buffer_3
  not not_1 (not_1_out, d_out[7]);
  not not_2 (not_2_out, d_out[6]);
  not not_3 (not_3_out, d_out[5]);
  not not_4 (not_4_out, d_out[4]);
  not not_5 (not_5_out, d_out[3]);
  not not_6 (not_6_out, d_out[2]);
  not not_7 (not_7_out, d_out[1]);
  not not_8 (not_8_out, d_out[0]);
  and and_1 (and_1_out, not_1_out, not_2_out, not_3_out, not_4_out, not_6_out, not_7_out, not_8_out, not_5_out);
  not not_9 (not_9_out, d_out[0]);
  and and_2 (and_2_out, d_out[7], d_out[6], d_out[5], d_out[4], d_out[3], d_out[2], d_out[1]);
  assign z_out = enable ? and_1_out : 1'bz;  // Controlled_Buffer controlled_buffer_4
  and and_3 (and_3_out, not_9_out, and_2_out);
  assign n_out = enable ? and_3_out : 1'bz;  // Controlled_Buffer controlled_buffer_5
  // also tied to GND on the sheet: adder_1_cout
endmodule

module sub_unit (
  input  enable,
  input  [7:0] a_in,
  input  [7:0] b_in,
  input  c_in,
  output [7:0] d_out,
  output c_out,
  output z_out,
  output n_out,
  output v_out
);

  wire and_1_out, and_2_out, and_3_out, and_4_out, controlled_buffer_3_out, not_1_out, not_2_out, not_3_out,
       not_4_out, not_5_out, not_6_out, not_7_out, not_8_out, not_9_out, subtractor_1_bout;
  wire [7:0] controlled_buffer_1_out, controlled_buffer_2_out, subtractor_1_out;

  assign controlled_buffer_1_out = enable ? a_in : 8'bz;  // Controlled_Buffer controlled_buffer_1
  assign controlled_buffer_2_out = enable ? b_in : 8'bz;  // Controlled_Buffer controlled_buffer_2
  assign controlled_buffer_3_out = enable ? c_in : 1'bz;  // Controlled_Buffer controlled_buffer_3
  Subtractor subtractor_1 (
    .a(controlled_buffer_1_out), .b(controlled_buffer_2_out), .out(subtractor_1_out),
    .bin(controlled_buffer_3_out), .bout(subtractor_1_bout));
  assign d_out = enable ? subtractor_1_out : 8'bz;  // Controlled_Buffer controlled_buffer_4
  assign c_out = enable ? subtractor_1_bout : 1'bz;  // Controlled_Buffer controlled_buffer_5
  not not_1 (not_1_out, d_out[7]);
  not not_2 (not_2_out, d_out[6]);
  not not_3 (not_3_out, d_out[5]);
  not not_4 (not_4_out, d_out[4]);
  not not_5 (not_5_out, d_out[3]);
  not not_6 (not_6_out, d_out[2]);
  not not_7 (not_7_out, d_out[1]);
  not not_8 (not_8_out, d_out[0]);
  and and_1 (and_1_out, not_1_out, not_2_out, not_3_out, not_4_out, not_6_out, not_7_out, not_8_out, not_5_out);
  not not_9 (not_9_out, d_out[0]);
  and and_2 (and_2_out, d_out[7], d_out[6], d_out[5], d_out[4], d_out[3], d_out[2], d_out[1]);
  and and_3 (and_3_out, d_out[4], d_out[7], d_out[6], d_out[5], d_out[3], d_out[2], d_out[1], d_out[0]);
  assign z_out = enable ? and_1_out : 1'bz;  // Controlled_Buffer controlled_buffer_6
  and and_4 (and_4_out, not_9_out, and_2_out);
  assign n_out = enable ? and_4_out : 1'bz;  // Controlled_Buffer controlled_buffer_7
  assign v_out = enable ? and_3_out : 1'bz;  // Controlled_Buffer controlled_buffer_8
endmodule

module sum_unit (
  input  enable,
  input  [7:0] a_in,
  input  [7:0] b_in,
  input  c_in,
  output [7:0] d_out,
  output c_out,
  output z_out,
  output n_out,
  output v_out
);

  wire adder_1_cout, and_1_out, and_2_out, and_3_out, and_4_out, controlled_buffer_3_out, not_1_out,
       not_2_out, not_3_out, not_4_out, not_5_out, not_6_out, not_7_out, not_8_out, not_9_out;
  wire [7:0] adder_1_out, controlled_buffer_1_out, controlled_buffer_2_out;

  assign controlled_buffer_1_out = enable ? a_in : 8'bz;  // Controlled_Buffer controlled_buffer_1
  assign controlled_buffer_2_out = enable ? b_in : 8'bz;  // Controlled_Buffer controlled_buffer_2
  assign controlled_buffer_3_out = enable ? c_in : 1'bz;  // Controlled_Buffer controlled_buffer_3
  Adder adder_1 (
    .a(controlled_buffer_1_out), .b(controlled_buffer_2_out), .out(adder_1_out),
    .cin(controlled_buffer_3_out), .cout(adder_1_cout));
  assign d_out = enable ? adder_1_out : 8'bz;  // Controlled_Buffer controlled_buffer_4
  assign c_out = enable ? adder_1_cout : 1'bz;  // Controlled_Buffer controlled_buffer_5
  not not_1 (not_1_out, d_out[7]);
  not not_2 (not_2_out, d_out[6]);
  not not_3 (not_3_out, d_out[5]);
  not not_4 (not_4_out, d_out[4]);
  not not_5 (not_5_out, d_out[3]);
  not not_6 (not_6_out, d_out[2]);
  not not_7 (not_7_out, d_out[1]);
  not not_8 (not_8_out, d_out[0]);
  and and_1 (and_1_out, not_1_out, not_2_out, not_3_out, not_4_out, not_6_out, not_7_out, not_8_out, not_5_out);
  not not_9 (not_9_out, d_out[0]);
  and and_2 (and_2_out, d_out[7], d_out[6], d_out[5], d_out[4], d_out[3], d_out[2], d_out[1]);
  and and_3 (and_3_out, d_out[4], d_out[7], d_out[6], d_out[5], d_out[3], d_out[2], d_out[1], d_out[0]);
  assign z_out = enable ? and_1_out : 1'bz;  // Controlled_Buffer controlled_buffer_6
  and and_4 (and_4_out, not_9_out, and_2_out);
  assign n_out = enable ? and_4_out : 1'bz;  // Controlled_Buffer controlled_buffer_7
  assign v_out = enable ? and_3_out : 1'bz;  // Controlled_Buffer controlled_buffer_8
endmodule

module dec_unit (
  input  enable,
  input  [7:0] a_in,
  output [7:0] d_out,
  output z_out,
  output n_out
);

  wire and_1_out, and_2_out, and_3_out, not_1_out, not_2_out, not_3_out, not_4_out, not_5_out, not_6_out,
       not_7_out, not_8_out, not_9_out, subtractor_1_bout;
  wire [7:0] controlled_buffer_1_out, controlled_buffer_2_out, subtractor_1_out;

  assign controlled_buffer_1_out = enable ? a_in : 8'bz;  // Controlled_Buffer controlled_buffer_1
  assign controlled_buffer_2_out = enable ? 8'h1 : 8'bz;  // Controlled_Buffer controlled_buffer_2
  Subtractor subtractor_1 (
    .a(controlled_buffer_1_out), .b(controlled_buffer_2_out), .out(subtractor_1_out), .bin(1'b0),
    .bout(subtractor_1_bout));
  assign d_out = enable ? subtractor_1_out : 8'bz;  // Controlled_Buffer controlled_buffer_3
  not not_1 (not_1_out, d_out[7]);
  not not_2 (not_2_out, d_out[6]);
  not not_3 (not_3_out, d_out[5]);
  not not_4 (not_4_out, d_out[4]);
  not not_5 (not_5_out, d_out[3]);
  not not_6 (not_6_out, d_out[2]);
  not not_7 (not_7_out, d_out[1]);
  not not_8 (not_8_out, d_out[0]);
  and and_1 (and_1_out, not_1_out, not_2_out, not_3_out, not_4_out, not_6_out, not_7_out, not_8_out, not_5_out);
  not not_9 (not_9_out, d_out[0]);
  and and_2 (and_2_out, d_out[7], d_out[6], d_out[5], d_out[4], d_out[3], d_out[2], d_out[1]);
  assign z_out = enable ? and_1_out : 1'bz;  // Controlled_Buffer controlled_buffer_4
  and and_3 (and_3_out, not_9_out, and_2_out);
  assign n_out = enable ? and_3_out : 1'bz;  // Controlled_Buffer controlled_buffer_5
  // also tied to GND on the sheet: subtractor_1_bout
endmodule

module cmp_unit (
  input  enable,
  input  [7:0] a_in,
  input  [7:0] b_in,
  output [7:0] d_out,
  output c_out,
  output z_out,
  output n_out
);

  wire and_1_out, and_2_out, and_3_out, not_1_out, not_2_out, not_3_out, not_4_out, not_5_out, not_6_out,
       not_7_out, not_8_out, not_9_out, subtractor_1_bout;
  wire [7:0] controlled_buffer_1_out, controlled_buffer_2_out, subtractor_1_out;

  assign controlled_buffer_1_out = enable ? a_in : 8'bz;  // Controlled_Buffer controlled_buffer_1
  assign controlled_buffer_2_out = enable ? b_in : 8'bz;  // Controlled_Buffer controlled_buffer_2
  Subtractor subtractor_1 (
    .a(controlled_buffer_1_out), .b(controlled_buffer_2_out), .out(subtractor_1_out), .bin(1'b0),
    .bout(subtractor_1_bout));
  assign d_out = enable ? subtractor_1_out : 8'bz;  // Controlled_Buffer controlled_buffer_3
  assign c_out = enable ? subtractor_1_bout : 1'bz;  // Controlled_Buffer controlled_buffer_4
  not not_1 (not_1_out, d_out[7]);
  not not_2 (not_2_out, d_out[6]);
  not not_3 (not_3_out, d_out[5]);
  not not_4 (not_4_out, d_out[4]);
  not not_5 (not_5_out, d_out[3]);
  not not_6 (not_6_out, d_out[2]);
  not not_7 (not_7_out, d_out[1]);
  not not_8 (not_8_out, d_out[0]);
  and and_1 (and_1_out, not_1_out, not_2_out, not_3_out, not_4_out, not_6_out, not_7_out, not_8_out, not_5_out);
  not not_9 (not_9_out, d_out[0]);
  and and_2 (and_2_out, d_out[7], d_out[6], d_out[5], d_out[4], d_out[3], d_out[2], d_out[1]);
  assign z_out = enable ? and_1_out : 1'bz;  // Controlled_Buffer controlled_buffer_5
  and and_3 (and_3_out, not_9_out, and_2_out);
  assign n_out = enable ? and_3_out : 1'bz;  // Controlled_Buffer controlled_buffer_6
endmodule

module sum_16b_unit (
  input  enable,
  input  [7:0] a_in,
  input  [7:0] b_in,
  input  [7:0] c_in,
  output [7:0] l_ou,
  output [7:0] h_out
);

  wire and_1_out, and_2_out, not_2_out, subtractor_1_bout;
  wire [7:0] not_1_out;
  wire [15:0] adder_1_out, subtractor_1_out;

  assign not_1_out = ~c_in;  // NOT_Gate not_1, 8 bits wide
  not not_2 (not_2_out, c_in[7]);
  Adder #(.width(16)) adder_1 (.a({b_in, a_in}), .b({{8{1'b0}}, c_in}), .out(adder_1_out));  // open: cin, cout
  and and_1 (and_1_out, enable, not_2_out);
  Subtractor #(.width(16)) subtractor_1 (
    .a({b_in, a_in}), .b({{8{1'b0}}, not_1_out}), .out(subtractor_1_out), .bin(c_in[7]),
    .bout(subtractor_1_bout));
  assign {h_out, l_ou} = and_1_out ? adder_1_out : 16'bz;  // Controlled_Buffer controlled_buffer_1
  assign {h_out, l_ou} = and_2_out ? subtractor_1_out : 16'bz;  // Controlled_Buffer controlled_buffer_2
  and and_2 (and_2_out, c_in[7], enable);
  // also tied to GND on the sheet: subtractor_1_bout
endmodule
