// Logisim project Esperimenti_CU.circ as structural Verilog
module pipeline (
  input  in_1,
  input  in_2,
  input  in_3,
  input  in_4,
  input  in_5
);

  wire adder_1_cout, and_1_out, buffer_1_out, buffer_2_out, buffer_3_out, clk, clock_1_out, counter_1_carry,
       d_ff_1_q, d_ff_1_qn, decoder_9_out0, decoder_9_out1, decoder_9_out2, decoder_9_out3, decoder_9_out4,
       decoder_9_out5, decoder_10_out0, decoder_10_out1, decoder_10_out2, decoder_10_out3, decoder_10_out4,
       decoder_10_out5, decoder_13_out0, decoder_13_out1, decoder_13_out2, decoder_13_out3, decoder_13_out4,
       decoder_13_out5, nand_1_out, nand_2_out, nand_3_out, not_1_out, not_2_out, not_3_out, not_4_out,
       not_5_out, not_6_out, or_2_out, or_5_out, or_6_out, or_7_out, or_8_out, or_9_out, or_10_out,
       or_11_out, or_12_out, or_13_out, or_14_out, or_15_out, or_16_out, or_17_out, or_18_out, or_20_out,
       or_21_out, or_22_out, or_23_out, or_24_out, or_25_out, or_26_out, wb_all_a, wb_all_x, wb_all_y;
  wire [2:0] or_3_out, or_4_out, or_19_out, wb_address_a, wb_address_x, wb_address_y;
  wire [3:0] adder_3_out, adder_4_out, adder_5_out, inc_adr_reg_q, register_13_q, register_20_q;
  wire [5:0] decoder_11_out0, decoder_12_out0, decoder_14_out0;
  wire [7:0] aa_q, ab_q, ac_q, ad_q, adder_1_out, adder_2_out, ae_q, af_q, buffer_4_out,
       controlled_buffer_1_out, controlled_buffer_3_out, controlled_buffer_9_out, controlled_buffer_15_out,
       increment_index, instruction_register_q, memory_data, register_3_q, register_14_q, register_15_q,
       register_16_q, register_17_q, register_18_q, register_19_q, register_21_q, register_22_q,
       register_23_q, register_24_q, register_25_q, register_26_q, rom_1_data, rom_2_data, rom_3_data,
       rom_4_data, wb_data_a, wb_data_x, wb_data_y;
  wire [15:0] address, address_bus, address_register_pipeline_q, decoder_1_out0, decoder_2_out0,
       decoder_3_out0, decoder_4_out0, decoder_5_out0, decoder_6_out0, decoder_7_out0, decoder_8_out0,
       register_4_q, register_5_q, register_6_q, register_7_q, register_8_q, register_9_q, register_10_q,
       register_11_q, register_12_q;

  Clock clock_1 (.out(clock_1_out));
  ROM #(.addrWidth(16)) memory (.addr(address), .data(memory_data));
  assign controlled_buffer_1_out = not_1_out ? 8'h2 : 8'bz;  // Controlled_Buffer controlled_buffer_1
  not not_1 (not_1_out, increment_index[0]);
  assign controlled_buffer_1_out = increment_index[0] ? 8'h3 : 8'bz;  // Controlled_Buffer controlled_buffer_2
  or or_1 (clk, clock_1_out, in_4);
  buf buffer_1 (buffer_1_out, increment_index[1]);
  buf buffer_2 (buffer_2_out, increment_index[2]);
  buf buffer_3 (buffer_3_out, increment_index[3]);
  D_Flip_Flop d_ff_1 (.D(buffer_3_out), .clk(clk), .Q(d_ff_1_q), .Qn(d_ff_1_qn), .reset(and_1_out));  // open: preset
  Adder adder_1 (
    .a(address_bus[7:0]), .b(controlled_buffer_1_out), .out(adder_1_out), .cout(adder_1_cout));  // open: cin
  Adder adder_2 (.a(address_bus[15:8]), .b({8{1'b0}}), .out(adder_2_out), .cin(adder_1_cout));  // open: cout
  and and_1 (and_1_out, d_ff_1_qn, clk);
  assign buffer_4_out = memory_data;  // Buffer buffer_4, 8 bits wide
  or or_2 (or_2_out, in_5, buffer_1_out);
  Counter counter_1 (
    .clr(d_ff_1_q), .load(buffer_2_out), .count(or_2_out), .clk(clk), .D(adder_1_out),
    .carry(counter_1_carry), .Q(address_bus[7:0]));  // open: up
  Counter counter_2 (
    .clr(d_ff_1_q), .load(buffer_2_out), .up(counter_1_carry), .count(counter_1_carry), .clk(clk),
    .D(adder_2_out), .Q(address_bus[15:8]));  // open: carry
  ROM decodifica_incrementale (.addr(buffer_4_out), .data(increment_index));
  nand nand_1 (nand_1_out, in_3, 1'b1);
  not not_2 (not_2_out, increment_index[4]);
  Register register_1 (.D(address_bus[7:0]), .en(not_2_out), .clk(clk), .Q(address[7:0]));  // open: clr
  Register register_2 (.D(address_bus[15:8]), .en(not_2_out), .clk(clk), .Q(address[15:8]));  // open: clr
  Register instruction_register (
    .D(buffer_4_out), .en(nand_1_out), .clk(clk), .Q(instruction_register_q));  // open: clr
  Register #(.width(16)) address_register_pipeline (
    .D(address_bus), .en(nand_1_out), .clk(clk), .Q(address_register_pipeline_q));  // open: clr
  ROM #(.addrWidth(16)) rom_1 (.addr({{8{1'b0}}, instruction_register_q}), .data(rom_1_data));
  ROM #(.addrWidth(16)) rom_2 (.addr({{8{1'b0}}, instruction_register_q}), .data(rom_2_data));
  ROM #(.addrWidth(16)) rom_3 (.addr({{8{1'b0}}, instruction_register_q}), .data(rom_3_data));
  ROM #(.addrWidth(16)) rom_4 (.addr({{8{1'b0}}, instruction_register_q}), .data(rom_4_data));
  not not_3 (not_3_out, rom_1_data[4]);
  not not_4 (not_4_out, rom_2_data[4]);
  not not_5 (not_5_out, rom_3_data[4]);
  not not_6 (not_6_out, rom_4_data[4]);
  Decoder #(.select(4)) decoder_1 (
    .out0(decoder_1_out0[0]), .out1(decoder_1_out0[1]), .out2(decoder_1_out0[2]), .out3(decoder_1_out0[3]),
    .out4(decoder_1_out0[4]), .out5(decoder_1_out0[5]), .out6(decoder_1_out0[6]), .out7(decoder_1_out0[7]),
    .out8(decoder_1_out0[8]), .out9(decoder_1_out0[9]), .out10(decoder_1_out0[10]),
    .out11(decoder_1_out0[11]), .out12(decoder_1_out0[12]), .out13(decoder_1_out0[13]),
    .out14(decoder_1_out0[14]), .out15(decoder_1_out0[15]), .sel(rom_1_data[3:0]), .en(not_3_out));
  Decoder #(.select(4)) decoder_2 (
    .out0(decoder_2_out0[0]), .out1(decoder_2_out0[1]), .out2(decoder_2_out0[2]), .out3(decoder_2_out0[3]),
    .out4(decoder_2_out0[4]), .out5(decoder_2_out0[5]), .out6(decoder_2_out0[6]), .out7(decoder_2_out0[7]),
    .out8(decoder_2_out0[8]), .out9(decoder_2_out0[9]), .out10(decoder_2_out0[10]),
    .out11(decoder_2_out0[11]), .out12(decoder_2_out0[12]), .out13(decoder_2_out0[13]),
    .out14(decoder_2_out0[14]), .out15(decoder_2_out0[15]), .sel(rom_1_data[3:0]), .en(rom_1_data[4]));
  Decoder #(.select(4)) decoder_3 (
    .out0(decoder_3_out0[0]), .out1(decoder_3_out0[1]), .out2(decoder_3_out0[2]), .out3(decoder_3_out0[3]),
    .out4(decoder_3_out0[4]), .out5(decoder_3_out0[5]), .out6(decoder_3_out0[6]), .out7(decoder_3_out0[7]),
    .out8(decoder_3_out0[8]), .out9(decoder_3_out0[9]), .out10(decoder_3_out0[10]),
    .out11(decoder_3_out0[11]), .out12(decoder_3_out0[12]), .out13(decoder_3_out0[13]),
    .out14(decoder_3_out0[14]), .out15(decoder_3_out0[15]), .sel(rom_2_data[3:0]), .en(not_4_out));
  Decoder #(.select(4)) decoder_4 (
    .out0(decoder_4_out0[0]), .out1(decoder_4_out0[1]), .out2(decoder_4_out0[2]), .out3(decoder_4_out0[3]),
    .out4(decoder_4_out0[4]), .out5(decoder_4_out0[5]), .out6(decoder_4_out0[6]), .out7(decoder_4_out0[7]),
    .out8(decoder_4_out0[8]), .out9(decoder_4_out0[9]), .out10(decoder_4_out0[10]),
    .out11(decoder_4_out0[11]), .out12(decoder_4_out0[12]), .out13(decoder_4_out0[13]),
    .out14(decoder_4_out0[14]), .out15(decoder_4_out0[15]), .sel(rom_2_data[3:0]), .en(rom_2_data[4]));
  Decoder #(.select(4)) decoder_5 (
    .out0(decoder_5_out0[0]), .out1(decoder_5_out0[1]), .out2(decoder_5_out0[2]), .out3(decoder_5_out0[3]),
    .out4(decoder_5_out0[4]), .out5(decoder_5_out0[5]), .out6(decoder_5_out0[6]), .out7(decoder_5_out0[7]),
    .out8(decoder_5_out0[8]), .out9(decoder_5_out0[9]), .out10(decoder_5_out0[10]),
    .out11(decoder_5_out0[11]), .out12(decoder_5_out0[12]), .out13(decoder_5_out0[13]),
    .out14(decoder_5_out0[14]), .out15(decoder_5_out0[15]), .sel(rom_3_data[3:0]), .en(not_5_out));
  Decoder #(.select(4)) decoder_6 (
    .out0(decoder_6_out0[0]), .out1(decoder_6_out0[1]), .out2(decoder_6_out0[2]), .out3(decoder_6_out0[3]),
    .out4(decoder_6_out0[4]), .out5(decoder_6_out0[5]), .out6(decoder_6_out0[6]), .out7(decoder_6_out0[7]),
    .out8(decoder_6_out0[8]), .out9(decoder_6_out0[9]), .out10(decoder_6_out0[10]),
    .out11(decoder_6_out0[11]), .out12(decoder_6_out0[12]), .out13(decoder_6_out0[13]),
    .out14(decoder_6_out0[14]), .out15(decoder_6_out0[15]), .sel(rom_3_data[3:0]), .en(rom_3_data[4]));
  Decoder #(.select(4)) decoder_7 (
    .out0(decoder_7_out0[0]), .out1(decoder_7_out0[1]), .out2(decoder_7_out0[2]), .out3(decoder_7_out0[3]),
    .out4(decoder_7_out0[4]), .out5(decoder_7_out0[5]), .out6(decoder_7_out0[6]), .out7(decoder_7_out0[7]),
    .out8(decoder_7_out0[8]), .out9(decoder_7_out0[9]), .out10(decoder_7_out0[10]),
    .out11(decoder_7_out0[11]), .out12(decoder_7_out0[12]), .out13(decoder_7_out0[13]),
    .out14(decoder_7_out0[14]), .out15(decoder_7_out0[15]), .sel(rom_4_data[3:0]), .en(not_6_out));
  Decoder #(.select(4)) decoder_8 (
    .out0(decoder_8_out0[0]), .out1(decoder_8_out0[1]), .out2(decoder_8_out0[2]), .out3(decoder_8_out0[3]),
    .out4(decoder_8_out0[4]), .out5(decoder_8_out0[5]), .out6(decoder_8_out0[6]), .out7(decoder_8_out0[7]),
    .out8(decoder_8_out0[8]), .out9(decoder_8_out0[9]), .out10(decoder_8_out0[10]),
    .out11(decoder_8_out0[11]), .out12(decoder_8_out0[12]), .out13(decoder_8_out0[13]),
    .out14(decoder_8_out0[14]), .out15(decoder_8_out0[15]), .sel(rom_4_data[3:0]), .en(rom_4_data[4]));
  nand nand_2 (nand_2_out, 1'b1, in_2);
  Register register_3 (.D(instruction_register_q), .en(nand_2_out), .clk(clk), .Q(register_3_q));  // open: clr
  Register #(.width(16)) register_4 (
    .D(address_register_pipeline_q), .en(nand_2_out), .clk(clk), .Q(register_4_q));  // open: clr
  Register #(.width(16)) register_5 (.D(decoder_1_out0), .en(nand_2_out), .clk(clk), .Q(register_5_q));  // open: clr
  Register #(.width(16)) register_6 (.D(decoder_2_out0), .en(nand_2_out), .clk(clk), .Q(register_6_q));  // open: clr
  Register #(.width(16)) register_7 (.D(decoder_3_out0), .en(nand_2_out), .clk(clk), .Q(register_7_q));  // open: clr
  Register #(.width(16)) register_8 (.D(decoder_4_out0), .en(nand_2_out), .clk(clk), .Q(register_8_q));  // open: clr
  Register #(.width(16)) register_9 (.D(decoder_5_out0), .en(nand_2_out), .clk(clk), .Q(register_9_q));  // open: clr
  Register #(.width(16)) register_10 (.D(decoder_6_out0), .en(nand_2_out), .clk(clk), .Q(register_10_q));  // open: clr
  Register #(.width(16)) register_11 (.D(decoder_7_out0), .en(nand_2_out), .clk(clk), .Q(register_11_q));  // open: clr
  Register #(.width(16)) register_12 (.D(decoder_8_out0), .en(nand_2_out), .clk(clk), .Q(register_12_q));  // open: clr
  assign or_3_out = 3'b000 | wb_address_a;  // OR_Gate or_3, 3 bits wide
  Register #(.width(4)) inc_adr_reg (.D(adder_3_out), .en(1'b1), .clk(clk), .Q(inc_adr_reg_q));  // open: clr
  assign or_4_out = 3'b000 | wb_address_x;  // OR_Gate or_4, 3 bits wide
  Register #(.width(4)) register_13 (.D(adder_4_out), .en(1'b1), .clk(clk), .Q(register_13_q));  // open: clr
  Decoder #(.select(3)) decoder_9 (
    .out0(decoder_9_out0), .out1(decoder_9_out1), .out2(decoder_9_out2), .out3(decoder_9_out3),
    .out4(decoder_9_out4), .out5(decoder_9_out5), .sel(or_3_out));  // open: out6, out7, en
  Adder #(.width(4)) adder_3 (.a(inc_adr_reg_q), .b(4'b0001), .out(adder_3_out));  // open: cin, cout
  Decoder #(.select(3)) decoder_10 (
    .out0(decoder_10_out0), .out1(decoder_10_out1), .out2(decoder_10_out2), .out3(decoder_10_out3),
    .out4(decoder_10_out4), .out5(decoder_10_out5), .sel(or_4_out));  // open: out6, out7, en
  Adder #(.width(4)) adder_4 (.a(register_13_q), .b(4'b0001), .out(adder_4_out));  // open: cin, cout
  Decoder #(.select(3)) decoder_11 (
    .out0(decoder_11_out0[0]), .out1(decoder_11_out0[1]), .out2(decoder_11_out0[2]),
    .out3(decoder_11_out0[3]), .out4(decoder_11_out0[4]), .out5(decoder_11_out0[5]), .sel(inc_adr_reg_q[2:0]));  // open: out6, out7, en
  or or_5 (or_5_out, decoder_9_out0, or_17_out);
  or or_6 (or_6_out, decoder_9_out1, or_17_out);
  or or_7 (or_7_out, decoder_9_out2, or_17_out);
  or or_8 (or_8_out, decoder_9_out3, or_17_out);
  or or_9 (or_9_out, decoder_9_out4, or_17_out);
  or or_10 (or_10_out, decoder_9_out5, or_17_out);
  Decoder #(.select(3)) decoder_12 (
    .out0(decoder_12_out0[0]), .out1(decoder_12_out0[1]), .out2(decoder_12_out0[2]),
    .out3(decoder_12_out0[3]), .out4(decoder_12_out0[4]), .out5(decoder_12_out0[5]), .sel(register_13_q[2:0]));  // open: out6, out7, en
  or or_11 (or_11_out, decoder_10_out0, or_18_out);
  or or_12 (or_12_out, decoder_10_out1, or_18_out);
  or or_13 (or_13_out, decoder_10_out2, or_18_out);
  or or_14 (or_14_out, decoder_10_out3, or_18_out);
  or or_15 (or_15_out, decoder_10_out4, or_18_out);
  or or_16 (or_16_out, decoder_10_out5, or_18_out);
  or or_17 (or_17_out, wb_all_a, 1'b0);
  or or_18 (or_18_out, wb_all_x, 1'b0);
  Register aa (.D(wb_data_a), .en(or_5_out), .clk(clk), .Q(aa_q));  // open: clr
  Register ab (.D(wb_data_a), .en(or_6_out), .clk(clk), .Q(ab_q));  // open: clr
  Register ac (.D(wb_data_a), .en(or_7_out), .clk(clk), .Q(ac_q));  // open: clr
  Register ad (.D(wb_data_a), .en(or_8_out), .clk(clk), .Q(ad_q));  // open: clr
  Register ae (.D(wb_data_a), .en(or_9_out), .clk(clk), .Q(ae_q));  // open: clr
  Register af (.D(wb_data_a), .en(or_10_out), .clk(clk), .Q(af_q));  // open: clr
  Register register_14 (.D(wb_data_x), .en(or_11_out), .clk(clk), .Q(register_14_q));  // open: clr
  Register register_15 (.D(wb_data_x), .en(or_12_out), .clk(clk), .Q(register_15_q));  // open: clr
  Register register_16 (.D(wb_data_x), .en(or_13_out), .clk(clk), .Q(register_16_q));  // open: clr
  Register register_17 (.D(wb_data_x), .en(or_14_out), .clk(clk), .Q(register_17_q));  // open: clr
  Register register_18 (.D(wb_data_x), .en(or_15_out), .clk(clk), .Q(register_18_q));  // open: clr
  Register register_19 (.D(wb_data_x), .en(or_16_out), .clk(clk), .Q(register_19_q));  // open: clr
  assign controlled_buffer_3_out = decoder_11_out0[0] ? aa_q : 8'bz;  // Controlled_Buffer controlled_buffer_3
  assign controlled_buffer_3_out = decoder_11_out0[1] ? ab_q : 8'bz;  // Controlled_Buffer controlled_buffer_4
  assign controlled_buffer_3_out = decoder_11_out0[2] ? ac_q : 8'bz;  // Controlled_Buffer controlled_buffer_5
  assign controlled_buffer_3_out = decoder_11_out0[3] ? ad_q : 8'bz;  // Controlled_Buffer controlled_buffer_6
  assign controlled_buffer_3_out = decoder_11_out0[4] ? ae_q : 8'bz;  // Controlled_Buffer controlled_buffer_7
  assign controlled_buffer_3_out = decoder_11_out0[5] ? af_q : 8'bz;  // Controlled_Buffer controlled_buffer_8
  assign controlled_buffer_9_out = decoder_12_out0[0] ? register_14_q : 8'bz;  // Controlled_Buffer controlled_buffer_9
  assign controlled_buffer_9_out = decoder_12_out0[1] ? register_15_q : 8'bz;  // Controlled_Buffer controlled_buffer_10
  assign controlled_buffer_9_out = decoder_12_out0[2] ? register_16_q : 8'bz;  // Controlled_Buffer controlled_buffer_11
  assign controlled_buffer_9_out = decoder_12_out0[3] ? register_17_q : 8'bz;  // Controlled_Buffer controlled_buffer_12
  assign controlled_buffer_9_out = decoder_12_out0[4] ? register_18_q : 8'bz;  // Controlled_Buffer controlled_buffer_13
  assign controlled_buffer_9_out = decoder_12_out0[5] ? register_19_q : 8'bz;  // Controlled_Buffer controlled_buffer_14
  Register x_address (.D({2'b00, decoder_12_out0}), .en(1'b1), .clk(clk));  // open: Q, clr
  Register x_data (.D(controlled_buffer_9_out), .en(1'b1), .clk(clk));  // open: Q, clr
  Register ac_address (.D({2'b00, decoder_11_out0}), .en(1'b1), .clk(clk));  // open: Q, clr
  Register ac_data (.D(controlled_buffer_3_out), .en(1'b1), .clk(clk));  // open: Q, clr
  assign or_19_out = 3'b000 | wb_address_y;  // OR_Gate or_19, 3 bits wide
  Register #(.width(4)) register_20 (.D(adder_5_out), .en(1'b1), .clk(clk), .Q(register_20_q));  // open: clr
  Decoder #(.select(3)) decoder_13 (
    .out0(decoder_13_out0), .out1(decoder_13_out1), .out2(decoder_13_out2), .out3(decoder_13_out3),
    .out4(decoder_13_out4), .out5(decoder_13_out5), .sel(or_19_out));  // open: out6, out7, en
  Adder #(.width(4)) adder_5 (.a(register_20_q), .b(4'b0001), .out(adder_5_out));  // open: cin, cout
  Decoder #(.select(3)) decoder_14 (
    .out0(decoder_14_out0[0]), .out1(decoder_14_out0[1]), .out2(decoder_14_out0[2]),
    .out3(decoder_14_out0[3]), .out4(decoder_14_out0[4]), .out5(decoder_14_out0[5]), .sel(register_20_q[2:0]));  // open: out6, out7, en
  or or_20 (or_20_out, decoder_13_out0, or_26_out);
  or or_21 (or_21_out, decoder_13_out1, or_26_out);
  or or_22 (or_22_out, decoder_13_out2, or_26_out);
  or or_23 (or_23_out, decoder_13_out3, or_26_out);
  or or_24 (or_24_out, decoder_13_out4, or_26_out);
  or or_25 (or_25_out, decoder_13_out5, or_26_out);
  or or_26 (or_26_out, wb_all_y, 1'b0);
  Register register_21 (.D(wb_data_y), .en(or_20_out), .clk(clk), .Q(register_21_q));  // open: clr
  Register register_22 (.D(wb_data_y), .en(or_21_out), .clk(clk), .Q(register_22_q));  // open: clr
  Register register_23 (.D(wb_data_y), .en(or_22_out), .clk(clk), .Q(register_23_q));  // open: clr
  Register register_24 (.D(wb_data_y), .en(or_23_out), .clk(clk), .Q(register_24_q));  // open: clr
  Register register_25 (.D(wb_data_y), .en(or_24_out), .clk(clk), .Q(register_25_q));  // open: clr
  Register register_26 (.D(wb_data_y), .en(or_25_out), .clk(clk), .Q(register_26_q));  // open: clr
  assign controlled_buffer_15_out = decoder_14_out0[0] ? register_21_q : 8'bz;  // Controlled_Buffer controlled_buffer_15
  assign controlled_buffer_15_out = decoder_14_out0[1] ? register_22_q : 8'bz;  // Controlled_Buffer controlled_buffer_16
  assign controlled_buffer_15_out = decoder_14_out0[2] ? register_23_q : 8'bz;  // Controlled_Buffer controlled_buffer_17
  assign controlled_buffer_15_out = decoder_14_out0[3] ? register_24_q : 8'bz;  // Controlled_Buffer controlled_buffer_18
  assign controlled_buffer_15_out = decoder_14_out0[4] ? register_25_q : 8'bz;  // Controlled_Buffer controlled_buffer_19
  assign controlled_buffer_15_out = decoder_14_out0[5] ? register_26_q : 8'bz;  // Controlled_Buffer controlled_buffer_20
  Register y_address (.D({2'b00, decoder_14_out0}), .en(1'b1), .clk(clk));  // open: Q, clr
  Register y_data (.D(controlled_buffer_15_out), .en(1'b1), .clk(clk));  // open: Q, clr
  nand nand_3 (nand_3_out, 1'b1, in_1);
  Register isr (.D(register_3_q), .en(nand_3_out), .clk(clk));  // open: Q, clr
  Register #(.width(16)) adr (.D(register_4_q), .en(nand_3_out), .clk(clk));  // open: Q, clr
  Register #(.width(16)) register_27 (.D(register_5_q), .en(nand_3_out), .clk(clk));  // open: Q, clr
  Register #(.width(16)) register_28 (.D(register_6_q), .en(nand_3_out), .clk(clk));  // open: Q, clr
  Register #(.width(16)) register_29 (.D(register_7_q), .en(nand_3_out), .clk(clk));  // open: Q, clr
  Register #(.width(16)) register_30 (.D(register_8_q), .en(nand_3_out), .clk(clk));  // open: Q, clr
  Register #(.width(16)) register_31 (.D(register_9_q), .en(nand_3_out), .clk(clk));  // open: Q, clr
  Register #(.width(16)) register_32 (.D(register_10_q), .en(nand_3_out), .clk(clk));  // open: Q, clr
  Register #(.width(16)) register_33 (.D(register_11_q), .en(nand_3_out), .clk(clk));  // open: Q, clr
  Register #(.width(16)) register_34 (.D(register_12_q), .en(nand_3_out), .clk(clk));  // open: Q, clr

  // Other names for the same wires on the sheet: decode_stage_halt = in_2; fetch_stage_halt = in_3;
  //   register_rename_halt = in_1

  // Notes on the sheet:
  //   computer memory
  //   fetch_stage
  //   qui vengono recuperate le istruzioni e il loro indirizo
  //   program_counter
  //   adress_register
  //   decode stage
  //   qui le istruzioni vengono decodificate
  //   decode rom
  //   instruction_register
  //   address_register
  //   signal_register
  //   decoder_di_Scrittura
  //   decoder_di_Scrittura
  //   decoder_di_lettura
  //   decoder_di_lettura
  //   vengono assegnati dei registri univochi per le singole istruzioni
  //   register_rename
  //   register_rename
  //   Accumulator Pile
  //   Accumulator Pile
  //   decoder_di_Scrittura
  //   decoder_di_lettura
  //   register_rename
  //   Accumulator Pile
  //   memory_find
  //   stadio dove si accede alla memoria per recuperare i dati se necessario
endmodule

module decode_experiment (
  input  in_1,
  input  nmi,
  input  reset,
  input  interrupt,
  input  [7:0] in_5,
  input  [3:0] state_input,
  input  micro_count,
  input  micro_reset,
  output nmi_seq,
  output reset_seq,
  output [31:0] rom_1_dec,
  output [31:0] rom_3_dec,
  output int_seq,
  output [31:0] rom_4_dec,
  output [31:0] rom_2_dec
);

  wire and_1_out, clock_1_out, d_ff_1_q, interrupt_reset_1_mic_res, or_1_out;
  wire [3:0] counter_1_q;
  wire [7:0] interrupt_reset_1_instruction, rom_1_data, rom_2_data, rom_3_data, rom_4_data;
  wire [15:0] buffer_1_out, buffer_2_out, buffer_3_out, buffer_4_out;

  Clock clock_1 (.out(clock_1_out));
  or or_1 (or_1_out, in_1, clock_1_out);
  D_Flip_Flop d_ff_1 (
    .D(interrupt_reset_1_mic_res), .clk(or_1_out), .Q(d_ff_1_q), .reset(and_1_out));  // open: Qn, preset
  and and_1 (and_1_out, d_ff_1_q, or_1_out);
  interrupt_reset interrupt_reset_1 (
    .nmi(nmi), .reset(reset), .irq(interrupt), .clock(or_1_out), .mic_reset(micro_reset), .isr_input(in_5),
    .nmi_sequence(nmi_seq), .int_sequence(int_seq), .reset_sequence(reset_seq),
    .mic_res(interrupt_reset_1_mic_res), .instruction(interrupt_reset_1_instruction));
  Counter #(.max('hf), .width(4)) counter_1 (
    .clr(d_ff_1_q), .count(micro_count), .clk(or_1_out), .D(4'b0000), .Q(counter_1_q));  // open: load, up, carry
  assign buffer_1_out = {counter_1_q, state_input, interrupt_reset_1_instruction};  // Buffer buffer_1, 16 bits wide
  ROM #(.addrWidth(16)) rom_1 (.addr(buffer_1_out), .data(rom_1_data));
  assign buffer_2_out = {counter_1_q, state_input, interrupt_reset_1_instruction};  // Buffer buffer_2, 16 bits wide
  ROM #(.addrWidth(16)) rom_2 (.addr(buffer_2_out), .data(rom_2_data));
  ROM #(.addrWidth(16)) rom_3 (.addr(buffer_3_out), .data(rom_3_data));
  assign buffer_3_out = {counter_1_q, state_input, interrupt_reset_1_instruction};  // Buffer buffer_3, 16 bits wide
  ROM #(.addrWidth(16)) rom_4 (.addr(buffer_4_out), .data(rom_4_data));
  assign buffer_4_out = {counter_1_q, state_input, interrupt_reset_1_instruction};  // Buffer buffer_4, 16 bits wide
endmodule

module interrupt_reset (
  input  nmi,
  input  reset,
  input  irq,
  input  clock,
  input  mic_reset,
  input  [7:0] isr_input,
  output nmi_sequence,
  output int_sequence,
  output reset_sequence,
  output mic_res,
  output [7:0] instruction
);

  wire and_1_out, not_1_out, or_1_out, or_2_out;

  assign instruction = nmi_sequence ? 8'hfd : 8'bz;  // Controlled_Buffer controlled_buffer_1
  assign instruction = reset_sequence ? 8'hfe : 8'bz;  // Controlled_Buffer controlled_buffer_2
  assign instruction = int_sequence ? {8{1'b1}} : 8'bz;  // Controlled_Buffer controlled_buffer_3
  assign instruction = not_1_out ? isr_input : 8'bz;  // Controlled_Buffer controlled_buffer_4
  not not_1 (not_1_out, or_2_out);
  or or_1 (or_1_out, reset, nmi, irq);
  and and_1 (and_1_out, or_1_out, clock);
  D_Flip_Flop d_ff_1 (.D(nmi), .clk(and_1_out), .Q(nmi_sequence), .reset(mic_reset));  // open: Qn, preset
  D_Flip_Flop d_ff_2 (.D(irq), .clk(and_1_out), .Q(int_sequence), .reset(mic_reset));  // open: Qn, preset
  D_Flip_Flop d_ff_3 (.D(reset), .clk(and_1_out), .Q(reset_sequence), .reset(mic_reset));  // open: Qn, preset
  or or_2 (or_2_out, reset_sequence, nmi_sequence, int_sequence);
  or or_3 (mic_res, and_1_out, mic_reset);
endmodule

module pipeline_2 (
  input  in_1,
  input  in_2,
  input  in_3,
  input  in_4
);

  wire adder_1_cout, clock_1_out, decode_halt, decoder_9_out2, decoder_9_out3, decoder_9_out4,
       decoder_9_out5, decoder_9_out6, decoder_9_out7, decoder_10_out2, decoder_10_out3, decoder_10_out4,
       decoder_10_out5, decoder_10_out6, decoder_10_out7, decoder_11_out2, decoder_11_out3, decoder_11_out4,
       decoder_11_out5, decoder_11_out6, decoder_11_out7, decoder_12_out2, decoder_12_out3, decoder_12_out4,
       decoder_12_out5, decoder_12_out6, decoder_12_out7, decoder_13_out2, decoder_13_out3, decoder_13_out4,
       decoder_13_out5, decoder_13_out6, decoder_13_out7, decoder_14_out2, decoder_14_out3, decoder_14_out4,
       decoder_14_out5, decoder_14_out6, decoder_14_out7, fetch_halt, not_4_out, not_5_out, not_6_out,
       not_7_out, or_1_out, rename_halt, wb_signal, wb_signal_x, wb_signal_y;
  wire [2:0] register_6_q, register_7_q, register_8_q, wb_address, wb_address_x, wb_address_y;
  wire [3:0] adder_3_out, adder_4_out, adder_5_out, register_28_q, register_30_q, register_32_q;
  wire [3:3] register_6_q_2, register_7_q_2, register_8_q_2;
  wire [7:0] adder_1_out, adder_2_out, adr_h_q, adr_l_q, ALU_ROM_data, controlled_buffer_1_out,
       controlled_buffer_2_out, controlled_buffer_3_out, controlled_buffer_4_out, controlled_buffer_5_out,
       controlled_buffer_6_out, controlled_buffer_7_out, controlled_buffer_8_out, controlled_buffer_9_out,
       controlled_buffer_10_out, controlled_buffer_11_out, controlled_buffer_12_out,
       controlled_buffer_13_out, controlled_buffer_14_out, controlled_buffer_15_out,
       controlled_buffer_16_out, controlled_buffer_17_out, controlled_buffer_18_out,
       controlled_buffer_19_out, controlled_buffer_25_out, controlled_buffer_31_out, data_bus, I_O_ROM_data,
       isr_q, MEMORY_ROM_data, register_3_q, register_4_q, register_5_q, register_9_q, register_10_q,
       register_11_q, register_12_q, register_13_q, register_14_q, register_15_q, register_16_q,
       register_17_q, register_18_q, register_19_q, register_20_q, register_21_q, register_22_q,
       register_23_q, register_24_q, register_25_q, register_26_q, register_27_q, register_29_q,
       register_31_q, REGISTER_ROM_data, rom_2_data, wb_data;
  wire [15:0] address_bus, decoder_1_out0, decoder_2_out0, decoder_3_out0, decoder_4_out0, decoder_5_out0,
       decoder_6_out0, decoder_7_out0, decoder_8_out0;
  wire [31:0] rom_1_q, rom_2_q, rom_3_q, rom_4_q;

  ROM #(.addrWidth(16)) rom_1 (.addr(address_bus), .data(data_bus));
  Clock clock_1 (.out(clock_1_out));
  or or_1 (or_1_out, clock_1_out, in_4);
  Adder adder_1 (.a(address_bus[7:0]), .b(rom_2_data), .out(adder_1_out), .cout(adder_1_cout));  // open: cin
  Adder adder_2 (.a(address_bus[15:8]), .b({8{1'b0}}), .out(adder_2_out), .cin(adder_1_cout));  // open: cout
  ROM rom_2 (.addr(data_bus), .data(rom_2_data));
  Register register_1 (.D(adder_1_out), .en(1'b1), .clk(or_1_out), .Q(address_bus[7:0]));  // open: clr
  Register register_2 (.D(adder_2_out), .en(1'b1), .clk(or_1_out), .Q(address_bus[15:8]));  // open: clr
  Register isr (.D(data_bus), .en(fetch_halt), .clk(or_1_out), .Q(isr_q));  // open: clr
  Register adr_l (.D(address_bus[7:0]), .en(fetch_halt), .clk(or_1_out), .Q(adr_l_q));  // open: clr
  Register adr_h (.D(address_bus[15:8]), .en(fetch_halt), .clk(or_1_out), .Q(adr_h_q));  // open: clr
  not not_1 (fetch_halt, in_1);
  not not_2 (decode_halt, in_2);
  not not_3 (rename_halt, in_3);
  ROM I_O_ROM (.addr(isr_q), .data(I_O_ROM_data));
  ROM MEMORY_ROM (.addr(isr_q), .data(MEMORY_ROM_data));
  ROM ALU_ROM (.addr(isr_q), .data(ALU_ROM_data));
  ROM REGISTER_ROM (.addr(isr_q), .data(REGISTER_ROM_data));
  not not_4 (not_4_out, I_O_ROM_data[4]);
  Decoder #(.select(4)) decoder_1 (
    .out0(decoder_1_out0[0]), .out1(decoder_1_out0[1]), .out2(decoder_1_out0[2]), .out3(decoder_1_out0[3]),
    .out4(decoder_1_out0[4]), .out5(decoder_1_out0[5]), .out6(decoder_1_out0[6]), .out7(decoder_1_out0[7]),
    .out8(decoder_1_out0[8]), .out9(decoder_1_out0[9]), .out10(decoder_1_out0[10]),
    .out11(decoder_1_out0[11]), .out12(decoder_1_out0[12]), .out13(decoder_1_out0[13]),
    .out14(decoder_1_out0[14]), .out15(decoder_1_out0[15]), .sel(I_O_ROM_data[3:0]), .en(not_4_out));
  Decoder #(.select(4)) decoder_2 (
    .out0(decoder_2_out0[0]), .out1(decoder_2_out0[1]), .out2(decoder_2_out0[2]), .out3(decoder_2_out0[3]),
    .out4(decoder_2_out0[4]), .out5(decoder_2_out0[5]), .out6(decoder_2_out0[6]), .out7(decoder_2_out0[7]),
    .out8(decoder_2_out0[8]), .out9(decoder_2_out0[9]), .out10(decoder_2_out0[10]),
    .out11(decoder_2_out0[11]), .out12(decoder_2_out0[12]), .out13(decoder_2_out0[13]),
    .out14(decoder_2_out0[14]), .out15(decoder_2_out0[15]), .sel(I_O_ROM_data[3:0]), .en(I_O_ROM_data[4]));
  Decoder #(.select(4)) decoder_3 (
    .out0(decoder_3_out0[0]), .out1(decoder_3_out0[1]), .out2(decoder_3_out0[2]), .out3(decoder_3_out0[3]),
    .out4(decoder_3_out0[4]), .out5(decoder_3_out0[5]), .out6(decoder_3_out0[6]), .out7(decoder_3_out0[7]),
    .out8(decoder_3_out0[8]), .out9(decoder_3_out0[9]), .out10(decoder_3_out0[10]),
    .out11(decoder_3_out0[11]), .out12(decoder_3_out0[12]), .out13(decoder_3_out0[13]),
    .out14(decoder_3_out0[14]), .out15(decoder_3_out0[15]), .sel(MEMORY_ROM_data[3:0]), .en(not_5_out));
  not not_5 (not_5_out, MEMORY_ROM_data[4]);
  Decoder #(.select(4)) decoder_4 (
    .out0(decoder_4_out0[0]), .out1(decoder_4_out0[1]), .out2(decoder_4_out0[2]), .out3(decoder_4_out0[3]),
    .out4(decoder_4_out0[4]), .out5(decoder_4_out0[5]), .out6(decoder_4_out0[6]), .out7(decoder_4_out0[7]),
    .out8(decoder_4_out0[8]), .out9(decoder_4_out0[9]), .out10(decoder_4_out0[10]),
    .out11(decoder_4_out0[11]), .out12(decoder_4_out0[12]), .out13(decoder_4_out0[13]),
    .out14(decoder_4_out0[14]), .out15(decoder_4_out0[15]), .sel(MEMORY_ROM_data[3:0]),
    .en(MEMORY_ROM_data[4]));
  Register #(.width(32)) rom_1_dup2 (
    .D({decoder_2_out0, decoder_1_out0}), .en(decode_halt), .clk(or_1_out), .Q(rom_1_q));  // open: clr
  Register #(.width(32)) rom_2_dup2 (
    .D({decoder_4_out0, decoder_3_out0}), .en(decode_halt), .clk(or_1_out), .Q(rom_2_q));  // open: clr
  not not_6 (not_6_out, ALU_ROM_data[4]);
  not not_7 (not_7_out, REGISTER_ROM_data[4]);
  Decoder #(.select(4)) decoder_5 (
    .out0(decoder_5_out0[0]), .out1(decoder_5_out0[1]), .out2(decoder_5_out0[2]), .out3(decoder_5_out0[3]),
    .out4(decoder_5_out0[4]), .out5(decoder_5_out0[5]), .out6(decoder_5_out0[6]), .out7(decoder_5_out0[7]),
    .out8(decoder_5_out0[8]), .out9(decoder_5_out0[9]), .out10(decoder_5_out0[10]),
    .out11(decoder_5_out0[11]), .out12(decoder_5_out0[12]), .out13(decoder_5_out0[13]),
    .out14(decoder_5_out0[14]), .out15(decoder_5_out0[15]), .sel(ALU_ROM_data[3:0]), .en(not_6_out));
  Decoder #(.select(4)) decoder_6 (
    .out0(decoder_6_out0[0]), .out1(decoder_6_out0[1]), .out2(decoder_6_out0[2]), .out3(decoder_6_out0[3]),
    .out4(decoder_6_out0[4]), .out5(decoder_6_out0[5]), .out6(decoder_6_out0[6]), .out7(decoder_6_out0[7]),
    .out8(decoder_6_out0[8]), .out9(decoder_6_out0[9]), .out10(decoder_6_out0[10]),
    .out11(decoder_6_out0[11]), .out12(decoder_6_out0[12]), .out13(decoder_6_out0[13]),
    .out14(decoder_6_out0[14]), .out15(decoder_6_out0[15]), .sel(ALU_ROM_data[3:0]), .en(ALU_ROM_data[4]));
  Decoder #(.select(4)) decoder_7 (
    .out0(decoder_7_out0[0]), .out1(decoder_7_out0[1]), .out2(decoder_7_out0[2]), .out3(decoder_7_out0[3]),
    .out4(decoder_7_out0[4]), .out5(decoder_7_out0[5]), .out6(decoder_7_out0[6]), .out7(decoder_7_out0[7]),
    .out8(decoder_7_out0[8]), .out9(decoder_7_out0[9]), .out10(decoder_7_out0[10]),
    .out11(decoder_7_out0[11]), .out12(decoder_7_out0[12]), .out13(decoder_7_out0[13]),
    .out14(decoder_7_out0[14]), .out15(decoder_7_out0[15]), .sel(REGISTER_ROM_data[3:0]), .en(not_7_out));
  Decoder #(.select(4)) decoder_8 (
    .out0(decoder_8_out0[0]), .out1(decoder_8_out0[1]), .out2(decoder_8_out0[2]), .out3(decoder_8_out0[3]),
    .out4(decoder_8_out0[4]), .out5(decoder_8_out0[5]), .out6(decoder_8_out0[6]), .out7(decoder_8_out0[7]),
    .out8(decoder_8_out0[8]), .out9(decoder_8_out0[9]), .out10(decoder_8_out0[10]),
    .out11(decoder_8_out0[11]), .out12(decoder_8_out0[12]), .out13(decoder_8_out0[13]),
    .out14(decoder_8_out0[14]), .out15(decoder_8_out0[15]), .sel(REGISTER_ROM_data[3:0]),
    .en(REGISTER_ROM_data[4]));
  Register register_3 (.D(isr_q), .en(decode_halt), .clk(or_1_out), .Q(register_3_q));  // open: clr
  Register register_4 (.D(adr_l_q), .en(decode_halt), .clk(or_1_out), .Q(register_4_q));  // open: clr
  Register register_5 (.D(adr_h_q), .en(decode_halt), .clk(or_1_out), .Q(register_5_q));  // open: clr
  Register #(.width(32)) rom_3 (
    .D({decoder_6_out0, decoder_5_out0}), .en(decode_halt), .clk(or_1_out), .Q(rom_3_q));  // open: clr
  Register #(.width(32)) rom_4 (
    .D({decoder_8_out0, decoder_7_out0}), .en(decode_halt), .clk(or_1_out), .Q(rom_4_q));  // open: clr
  Register #(.width(4)) register_6 (
    .D(adder_3_out), .en(1'b1), .clk(or_1_out), .Q({register_6_q_2[3], register_6_q}));  // open: clr
  Register #(.width(4)) register_7 (
    .D(adder_4_out), .en(1'b1), .clk(or_1_out), .Q({register_7_q_2[3], register_7_q}));  // open: clr
  Register #(.width(4)) register_8 (
    .D(adder_5_out), .en(1'b1), .clk(or_1_out), .Q({register_8_q_2[3], register_8_q}));  // open: clr
  Adder #(.width(4)) adder_3 (
    .a({register_6_q_2[3], register_6_q}), .b(4'b1111), .out(adder_3_out));  // open: cin, cout
  Adder #(.width(4)) adder_4 (
    .a({register_7_q_2[3], register_7_q}), .b(4'b1111), .out(adder_4_out));  // open: cin, cout
  Adder #(.width(4)) adder_5 (
    .a({register_8_q_2[3], register_8_q}), .b(4'b1111), .out(adder_5_out));  // open: cin, cout
  Decoder #(.select(3)) decoder_9 (
    .out2(decoder_9_out2), .out3(decoder_9_out3), .out4(decoder_9_out4), .out5(decoder_9_out5),
    .out6(decoder_9_out6), .out7(decoder_9_out7), .sel(wb_address));  // open: out0, out1, en
  Decoder #(.select(3)) decoder_10 (
    .out2(decoder_10_out2), .out3(decoder_10_out3), .out4(decoder_10_out4), .out5(decoder_10_out5),
    .out6(decoder_10_out6), .out7(decoder_10_out7), .sel(wb_address_x));  // open: out0, out1, en
  Decoder #(.select(3)) decoder_11 (
    .out2(decoder_11_out2), .out3(decoder_11_out3), .out4(decoder_11_out4), .out5(decoder_11_out5),
    .out6(decoder_11_out6), .out7(decoder_11_out7), .sel(wb_address_y));  // open: out0, out1, en
  assign controlled_buffer_1_out = decoder_9_out7 ? wb_data : 8'bz;  // Controlled_Buffer controlled_buffer_1
  assign controlled_buffer_2_out = decoder_9_out6 ? wb_data : 8'bz;  // Controlled_Buffer controlled_buffer_2
  assign controlled_buffer_3_out = decoder_9_out5 ? wb_data : 8'bz;  // Controlled_Buffer controlled_buffer_3
  assign controlled_buffer_4_out = decoder_9_out4 ? wb_data : 8'bz;  // Controlled_Buffer controlled_buffer_4
  assign controlled_buffer_5_out = decoder_9_out3 ? wb_data : 8'bz;  // Controlled_Buffer controlled_buffer_5
  assign controlled_buffer_6_out = decoder_9_out2 ? wb_data : 8'bz;  // Controlled_Buffer controlled_buffer_6
  assign controlled_buffer_7_out = decoder_10_out7 ? wb_data : 8'bz;  // Controlled_Buffer controlled_buffer_7
  assign controlled_buffer_8_out = decoder_10_out6 ? wb_data : 8'bz;  // Controlled_Buffer controlled_buffer_8
  assign controlled_buffer_9_out = decoder_10_out5 ? wb_data : 8'bz;  // Controlled_Buffer controlled_buffer_9
  assign controlled_buffer_10_out = decoder_10_out4 ? wb_data : 8'bz;  // Controlled_Buffer controlled_buffer_10
  assign controlled_buffer_11_out = decoder_10_out3 ? wb_data : 8'bz;  // Controlled_Buffer controlled_buffer_11
  assign controlled_buffer_12_out = decoder_10_out2 ? wb_data : 8'bz;  // Controlled_Buffer controlled_buffer_12
  assign controlled_buffer_13_out = decoder_11_out7 ? wb_data : 8'bz;  // Controlled_Buffer controlled_buffer_13
  assign controlled_buffer_14_out = decoder_11_out6 ? wb_data : 8'bz;  // Controlled_Buffer controlled_buffer_14
  assign controlled_buffer_15_out = decoder_11_out5 ? wb_data : 8'bz;  // Controlled_Buffer controlled_buffer_15
  assign controlled_buffer_16_out = decoder_11_out4 ? wb_data : 8'bz;  // Controlled_Buffer controlled_buffer_16
  assign controlled_buffer_17_out = decoder_11_out3 ? wb_data : 8'bz;  // Controlled_Buffer controlled_buffer_17
  assign controlled_buffer_18_out = decoder_11_out2 ? wb_data : 8'bz;  // Controlled_Buffer controlled_buffer_18
  Register register_9 (.D(controlled_buffer_1_out), .en(wb_signal), .clk(or_1_out), .Q(register_9_q));  // open: clr
  Register register_10 (.D(controlled_buffer_2_out), .en(wb_signal), .clk(or_1_out), .Q(register_10_q));  // open: clr
  Register register_11 (.D(controlled_buffer_3_out), .en(wb_signal), .clk(or_1_out), .Q(register_11_q));  // open: clr
  Register register_12 (.D(controlled_buffer_4_out), .en(wb_signal), .clk(or_1_out), .Q(register_12_q));  // open: clr
  Register register_13 (.D(controlled_buffer_5_out), .en(wb_signal), .clk(or_1_out), .Q(register_13_q));  // open: clr
  Register register_14 (.D(controlled_buffer_6_out), .en(wb_signal), .clk(or_1_out), .Q(register_14_q));  // open: clr
  Register register_15 (.D(controlled_buffer_7_out), .en(wb_signal_x), .clk(or_1_out), .Q(register_15_q));  // open: clr
  Register register_16 (.D(controlled_buffer_8_out), .en(wb_signal_x), .clk(or_1_out), .Q(register_16_q));  // open: clr
  Register register_17 (.D(controlled_buffer_9_out), .en(wb_signal_x), .clk(or_1_out), .Q(register_17_q));  // open: clr
  Register register_18 (
    .D(controlled_buffer_10_out), .en(wb_signal_x), .clk(or_1_out), .Q(register_18_q));  // open: clr
  Register register_19 (
    .D(controlled_buffer_11_out), .en(wb_signal_x), .clk(or_1_out), .Q(register_19_q));  // open: clr
  Register register_20 (
    .D(controlled_buffer_12_out), .en(wb_signal_x), .clk(or_1_out), .Q(register_20_q));  // open: clr
  Register register_21 (
    .D(controlled_buffer_13_out), .en(wb_signal_y), .clk(or_1_out), .Q(register_21_q));  // open: clr
  Register register_22 (
    .D(controlled_buffer_14_out), .en(wb_signal_y), .clk(or_1_out), .Q(register_22_q));  // open: clr
  Register register_23 (
    .D(controlled_buffer_15_out), .en(wb_signal_y), .clk(or_1_out), .Q(register_23_q));  // open: clr
  Register register_24 (
    .D(controlled_buffer_16_out), .en(wb_signal_y), .clk(or_1_out), .Q(register_24_q));  // open: clr
  Register register_25 (
    .D(controlled_buffer_17_out), .en(wb_signal_y), .clk(or_1_out), .Q(register_25_q));  // open: clr
  Register register_26 (
    .D(controlled_buffer_18_out), .en(wb_signal_y), .clk(or_1_out), .Q(register_26_q));  // open: clr
  Decoder #(.select(3)) decoder_12 (
    .out2(decoder_12_out2), .out3(decoder_12_out3), .out4(decoder_12_out4), .out5(decoder_12_out5),
    .out6(decoder_12_out6), .out7(decoder_12_out7), .sel(register_6_q));  // open: out0, out1, en
  assign controlled_buffer_19_out = decoder_12_out7 ? register_9_q : 8'bz;  // Controlled_Buffer controlled_buffer_19
  assign controlled_buffer_19_out = decoder_12_out6 ? register_10_q : 8'bz;  // Controlled_Buffer controlled_buffer_20
  assign controlled_buffer_19_out = decoder_12_out5 ? register_11_q : 8'bz;  // Controlled_Buffer controlled_buffer_21
  assign controlled_buffer_19_out = decoder_12_out4 ? register_12_q : 8'bz;  // Controlled_Buffer controlled_buffer_22
  assign controlled_buffer_19_out = decoder_12_out3 ? register_13_q : 8'bz;  // Controlled_Buffer controlled_buffer_23
  assign controlled_buffer_19_out = decoder_12_out2 ? register_14_q : 8'bz;  // Controlled_Buffer controlled_buffer_24
  Decoder #(.select(3)) decoder_13 (
    .out2(decoder_13_out2), .out3(decoder_13_out3), .out4(decoder_13_out4), .out5(decoder_13_out5),
    .out6(decoder_13_out6), .out7(decoder_13_out7), .sel(register_7_q));  // open: out0, out1, en
  assign controlled_buffer_25_out = decoder_13_out7 ? register_15_q : 8'bz;  // Controlled_Buffer controlled_buffer_25
  assign controlled_buffer_25_out = decoder_13_out6 ? register_16_q : 8'bz;  // Controlled_Buffer controlled_buffer_26
  assign controlled_buffer_25_out = decoder_13_out5 ? register_17_q : 8'bz;  // Controlled_Buffer controlled_buffer_27
  assign controlled_buffer_25_out = decoder_13_out4 ? register_18_q : 8'bz;  // Controlled_Buffer controlled_buffer_28
  assign controlled_buffer_25_out = decoder_13_out3 ? register_19_q : 8'bz;  // Controlled_Buffer controlled_buffer_29
  assign controlled_buffer_25_out = decoder_13_out2 ? register_20_q : 8'bz;  // Controlled_Buffer controlled_buffer_30
  Decoder #(.select(3)) decoder_14 (
    .out2(decoder_14_out2), .out3(decoder_14_out3), .out4(decoder_14_out4), .out5(decoder_14_out5),
    .out6(decoder_14_out6), .out7(decoder_14_out7), .sel(register_8_q));  // open: out0, out1, en
  assign controlled_buffer_31_out = decoder_14_out7 ? register_21_q : 8'bz;  // Controlled_Buffer controlled_buffer_31
  assign controlled_buffer_31_out = decoder_14_out6 ? register_22_q : 8'bz;  // Controlled_Buffer controlled_buffer_32
  assign controlled_buffer_31_out = decoder_14_out5 ? register_23_q : 8'bz;  // Controlled_Buffer controlled_buffer_33
  assign controlled_buffer_31_out = decoder_14_out4 ? register_24_q : 8'bz;  // Controlled_Buffer controlled_buffer_34
  assign controlled_buffer_31_out = decoder_14_out3 ? register_25_q : 8'bz;  // Controlled_Buffer controlled_buffer_35
  assign controlled_buffer_31_out = decoder_14_out2 ? register_26_q : 8'bz;  // Controlled_Buffer controlled_buffer_36
  Register register_27 (.D(controlled_buffer_19_out), .en(1'b1), .clk(or_1_out), .Q(register_27_q));  // open: clr
  Register #(.width(4)) register_28 (
    .D({register_6_q_2[3], register_6_q}), .en(1'b1), .clk(or_1_out), .Q(register_28_q));  // open: clr
  Register register_29 (.D(controlled_buffer_25_out), .en(1'b1), .clk(or_1_out), .Q(register_29_q));  // open: clr
  Register #(.width(4)) register_30 (
    .D({register_7_q_2[3], register_7_q}), .en(1'b1), .clk(or_1_out), .Q(register_30_q));  // open: clr
  Register register_31 (.D(controlled_buffer_31_out), .en(1'b1), .clk(or_1_out), .Q(register_31_q));  // open: clr
  Register #(.width(4)) register_32 (
    .D({register_8_q_2[3], register_8_q}), .en(1'b1), .clk(or_1_out), .Q(register_32_q));  // open: clr
  Register register_33 (.D(register_3_q), .en(rename_halt), .clk(or_1_out));  // open: Q, clr
  Register register_34 (.D(register_4_q), .en(rename_halt));  // open: clk, Q, clr
  Register register_35 (.D(register_5_q), .clk(or_1_out));  // open: en, Q, clr
  Register #(.width(32)) register_36 (.D(rom_1_q), .en(rename_halt), .clk(or_1_out));  // open: Q, clr
  Register #(.width(32)) register_37 (.D(rom_2_q), .en(rename_halt), .clk(or_1_out));  // open: Q, clr
  Register #(.width(32)) register_38 (.D(rom_3_q), .en(rename_halt), .clk(or_1_out));  // open: Q, clr
  Register #(.width(32)) register_39 (.D(rom_4_q), .en(rename_halt), .clk(or_1_out));  // open: Q, clr
endmodule
