// Logisim project corsair.circ as structural Verilog
module main (
);

  cu_parallel_decode cu_parallel_decode_1 ();  // open: flag, instruction, mic_count, mic_reset, clk, rom_3_out, rom_1_out, rom_2_out, c_reg_select, rom_4_out
endmodule

module latch (
  input  a0,
  input  a1,
  input  a2,
  input  a3,
  input  a4,
  input  a5,
  input  a6,
  input  a7,
  input  clk,
  output out_10,
  output out_11,
  output out_12,
  output out_13,
  output out_14,
  output out_15,
  output out_16,
  output out_17
);

  D_Flip_Flop d_ff_1 (.D(a0), .clk(clk), .Q(out_10));  // open: Qn, preset, reset
  D_Flip_Flop d_ff_2 (.D(a1), .clk(clk), .Q(out_11));  // open: Qn, preset, reset
  D_Flip_Flop d_ff_3 (.D(a2), .clk(clk), .Q(out_12));  // open: Qn, preset, reset
  D_Flip_Flop d_ff_4 (.D(a3), .clk(clk), .Q(out_13));  // open: Qn, preset, reset
  D_Flip_Flop d_ff_5 (.D(a4), .clk(clk), .Q(out_14));  // open: Qn, preset, reset
  D_Flip_Flop d_ff_6 (.D(a5), .clk(clk), .Q(out_15));  // open: Qn, preset, reset
  D_Flip_Flop d_ff_7 (.D(a6), .clk(clk), .Q(out_16));  // open: Qn, preset, reset
  D_Flip_Flop d_ff_8 (.D(a7), .clk(clk), .Q(out_17));  // open: Qn, preset, reset
endmodule

module buffer_16 (
  input  in_1,
  input  in_2,
  input  in_3,
  input  in_4,
  input  in_5,
  input  in_6,
  input  in_7,
  input  in_8,
  input  in_9,
  input  in_10,
  input  in_11,
  input  in_12,
  input  in_13,
  input  in_14,
  input  in_15,
  input  in_16,
  output out_17,
  output out_18,
  output out_19,
  output out_20,
  output out_21,
  output out_22,
  output out_23,
  output out_24,
  output out_25,
  output out_26,
  output out_27,
  output out_28,
  output out_29,
  output out_30,
  output out_31,
  output out_32
);

  buf buffer_1 (out_17, in_1);
  buf buffer_2 (out_18, in_2);
  buf buffer_3 (out_19, in_3);
  buf buffer_4 (out_20, in_4);
  buf buffer_5 (out_21, in_5);
  buf buffer_6 (out_22, in_6);
  buf buffer_7 (out_23, in_7);
  buf buffer_8 (out_24, in_8);
  buf buffer_9 (out_25, in_9);
  buf buffer_10 (out_26, in_10);
  buf buffer_11 (out_27, in_11);
  buf buffer_12 (out_28, in_12);
  buf buffer_13 (out_29, in_13);
  buf buffer_14 (out_30, in_14);
  buf buffer_15 (out_31, in_15);
  buf buffer_16 (out_32, in_16);
endmodule

module buffer_8 (
  input  in_1,
  input  in_2,
  input  in_3,
  input  in_4,
  input  in_5,
  input  in_6,
  input  in_7,
  input  in_8,
  output out_9,
  output out_10,
  output out_11,
  output out_12,
  output out_13,
  output out_14,
  output out_15,
  output out_16
);

  buf buffer_1 (out_9, in_1);
  buf buffer_2 (out_10, in_2);
  buf buffer_3 (out_11, in_3);
  buf buffer_4 (out_12, in_4);
  buf buffer_5 (out_13, in_5);
  buf buffer_6 (out_14, in_6);
  buf buffer_7 (out_15, in_7);
  buf buffer_8 (out_16, in_8);
endmodule

module Final_CU_1 (
  input  [7:0] ISR_OUT,
  input  micro_reset,
  input  clock,
  input  cu_flag,
  output [7:0] rom_2_out,
  output [7:0] rom_3_out,
  output [7:0] rom_4_out,
  output [7:0] rom_5_out,
  output [7:0] rom_1_out,
  output [7:0] cu_control_status_out
);

  wire [3:3] counter_1_q;
  wire [11:8] counter_1_q_2;

  Counter #(.max('hf), .width(4)) counter_1 (
    .clr(micro_reset), .load(1'b0), .up(1'b1), .count(1'b1), .clk(clock), .D(4'b0000),
    .Q({counter_1_q[3], counter_1_q_2[10:8]}));  // open: carry
  ROM #(.addrWidth(12)) rom_1 (.addr({counter_1_q_2, ISR_OUT}), .data(rom_1_out));
  or or_1 (counter_1_q_2[11], counter_1_q[3], cu_flag);
  ROM rom_2 (.addr(ISR_OUT), .data(cu_control_status_out));
  ROM #(.addrWidth(12)) rom_3 (.addr({counter_1_q_2, ISR_OUT}), .data(rom_2_out));
  ROM #(.addrWidth(12)) rom_4 (.addr({counter_1_q_2, ISR_OUT}), .data(rom_3_out));
  ROM #(.addrWidth(12)) rom_5 (.addr({counter_1_q_2, ISR_OUT}), .data(rom_4_out));
  ROM #(.addrWidth(12)) rom_6 (.addr({counter_1_q_2, ISR_OUT}), .data(rom_5_out));

  // Notes on the sheet:
  //   MICRO Program Counter
  //   Micro PC: avanzamento step istruzione
  //   ROM_1
  //   special_rom
  //   ROM_2
  //   ROM_3
  //   rom di interfacciamento con il registro delle costanti/di stato
  //   ROM_4
  //   ROM_5
endmodule

module Program_Counter (
  input  PC_reset,
  input  PCH_load,
  input  [7:0] PCH_in,
  input  PCL_load,
  input  count,
  input  [7:0] PCL_in,
  input  clock,
  output [7:0] PCH_OUT,
  output [7:0] PCL_OUT
);

  wire counter_2_carry;

  Counter counter_1 (
    .clr(PC_reset), .load(PCH_load), .up(counter_2_carry), .count(counter_2_carry), .clk(clock), .D(PCH_in),
    .Q(PCH_OUT));  // open: carry
  Counter counter_2 (
    .clr(PC_reset), .load(PCL_load), .up(count), .count(count), .clk(clock), .D(PCL_in),
    .carry(counter_2_carry), .Q(PCL_OUT));
endmodule

module ALU_Zero_Flag_Module (
  input  [7:0] Alu_OP_out,
  output Zero
);

  nand nand_1 (Zero, Alu_OP_out[0], Alu_OP_out[1], Alu_OP_out[2], Alu_OP_out[3], Alu_OP_out[4], Alu_OP_out[5], Alu_OP_out[6], Alu_OP_out[7]);
endmodule

module ALU_summ_subb_unit (
  input  [7:0] A,
  input  [7:0] B,
  input  Subb,
  input  Carry_In,
  output [7:0] summ_subb_out,
  output Carry,
  output Half_carry
);

  wire or_1_out;
  wire [3:0] xor_1_out, xor_5_out;

  xor xor_1 (xor_1_out[0], B[0], Subb);
  xor xor_2 (xor_1_out[1], B[1], Subb);
  xor xor_3 (xor_1_out[2], B[2], Subb);
  xor xor_4 (xor_1_out[3], B[3], Subb);
  xor xor_5 (xor_5_out[0], B[4], Subb);
  xor xor_6 (xor_5_out[1], B[5], Subb);
  xor xor_7 (xor_5_out[2], B[6], Subb);
  xor xor_8 (xor_5_out[3], B[7], Subb);
  or or_1 (or_1_out, Subb, Carry_In);
  Adder #(.width(4)) adder_1 (.a(A[7:4]), .b(xor_5_out), .out(summ_subb_out[7:4]), .cin(or_1_out), .cout(Half_carry));
  Adder #(.width(4)) adder_2 (.a(A[3:0]), .b(xor_1_out), .out(summ_subb_out[3:0]), .cin(Half_carry), .cout(Carry));
endmodule

module ALU_logic_AND (
  input  [7:0] A,
  input  [7:0] B,
  output [7:0] logic_and_out
);

  and and_1 (logic_and_out[0], A[0], B[0]);
  and and_2 (logic_and_out[1], A[1], B[1]);
  and and_3 (logic_and_out[2], A[2], B[2]);
  and and_4 (logic_and_out[3], A[3], B[3]);
  and and_5 (logic_and_out[4], A[4], B[4]);
  and and_6 (logic_and_out[5], A[5], B[5]);
  and and_7 (logic_and_out[6], A[6], B[6]);
  and and_8 (logic_and_out[7], A[7], B[7]);
endmodule

module ALU_logic_OR (
  input  [7:0] A,
  input  [7:0] B,
  output [7:0] logic_or_out
);

  or or_1 (logic_or_out[0], A[0], B[0]);
  or or_2 (logic_or_out[1], A[1], B[1]);
  or or_3 (logic_or_out[2], A[2], B[2]);
  or or_4 (logic_or_out[3], A[3], B[3]);
  or or_5 (logic_or_out[4], A[4], B[4]);
  or or_6 (logic_or_out[5], A[5], B[5]);
  or or_7 (logic_or_out[6], A[6], B[6]);
  or or_8 (logic_or_out[7], A[7], B[7]);
endmodule

module ALU_logic_XOR (
  input  [7:0] A,
  input  [7:0] B,
  output [7:0] logic_xor_out
);

  xor xor_1 (logic_xor_out[0], A[0], B[0]);
  xor xor_2 (logic_xor_out[1], A[1], B[1]);
  xor xor_3 (logic_xor_out[2], A[2], B[2]);
  xor xor_4 (logic_xor_out[3], A[3], B[3]);
  xor xor_5 (logic_xor_out[4], A[4], B[4]);
  xor xor_6 (logic_xor_out[5], A[5], B[5]);
  xor xor_7 (logic_xor_out[6], A[6], B[6]);
  xor xor_8 (logic_xor_out[7], A[7], B[7]);
endmodule

module SP (
  input  SP_reset,
  input  [7:0] sp_data_in,
  input  sp_load,
  input  sp_count,
  input  sp_dec,
  output [7:0] sp_data_out
);

  wire clock_1_out, counter_1_carry;

  Clock clock_1 (.out(clock_1_out));
  Counter counter_1 (
    .clr(SP_reset), .load(sp_load), .up(sp_count), .count(sp_dec), .clk(clock_1_out), .D(sp_data_in),
    .carry(counter_1_carry), .Q(sp_data_out));
  // also tied to GND on the sheet: counter_1_carry
endmodule

module sp_pc_unit (
  input  [3:0] selection_sp_pc,
  input  [7:0] in_buff,
  input  clock,
  output [15:0] address_out
);

  wire decoder_1_out0, decoder_1_out1, decoder_1_out2, decoder_1_out3, decoder_1_out4, decoder_1_out5,
       decoder_1_out8, decoder_1_out9, decoder_1_out10, decoder_1_out12, decoder_1_out13, or_1_out, or_2_out,
       or_3_out, or_4_out, or_5_out;
  wire [3:0] decoder_1_out6;
  wire [7:0] buffer_1_out, buffer_2_out, buffer_3_out, program_counter_1_pch_out, program_counter_1_pcl_out,
       sp_1_sp_data_out;
  wire [15:0] controlled_buffer_1_out;

  Decoder #(.select(4)) decoder_1 (
    .out0(decoder_1_out0), .out1(decoder_1_out1), .out2(decoder_1_out2), .out3(decoder_1_out3),
    .out4(decoder_1_out4), .out5(decoder_1_out5), .out6(decoder_1_out6[0]), .out7(decoder_1_out6[1]),
    .out8(decoder_1_out8), .out9(decoder_1_out9), .out10(decoder_1_out10), .out11(decoder_1_out10),
    .out12(decoder_1_out12), .out13(decoder_1_out13), .out14(decoder_1_out6[2]), .out15(decoder_1_out6[3]),
    .sel(selection_sp_pc));  // open: en
  assign buffer_1_out = in_buff;  // Buffer buffer_1, 8 bits wide
  assign buffer_2_out = in_buff;  // Buffer buffer_2, 8 bits wide
  assign buffer_3_out = in_buff;  // Buffer buffer_3, 8 bits wide
  or or_1 (or_1_out, decoder_1_out5, decoder_1_out4);
  or or_2 (or_2_out, decoder_1_out10, decoder_1_out12);
  or or_3 (or_3_out, decoder_1_out10, decoder_1_out13);
  or or_4 (or_4_out, decoder_1_out12, decoder_1_out13, decoder_1_out8);
  SP sp_1 (
    .SP_reset(decoder_1_out9), .sp_data_in(buffer_1_out), .sp_load(1'b0), .sp_count(or_2_out),
    .sp_dec(or_3_out), .sp_data_out(sp_1_sp_data_out));
  Program_Counter program_counter_1 (
    .PC_reset(decoder_1_out1), .PCH_load(decoder_1_out3), .PCH_in(buffer_2_out), .PCL_load(decoder_1_out2),
    .count(or_1_out), .PCL_in(buffer_3_out), .clock(clock), .PCH_OUT(program_counter_1_pch_out),
    .PCL_OUT(program_counter_1_pcl_out));
  assign controlled_buffer_1_out = or_4_out ? {{8{1'b0}}, sp_1_sp_data_out} : 16'bz;  // Controlled_Buffer controlled_buffer_1
  or or_5 (or_5_out, decoder_1_out0, decoder_1_out5);
  assign controlled_buffer_1_out = or_5_out ? {program_counter_1_pch_out, program_counter_1_pcl_out} : 16'bz;  // Controlled_Buffer controlled_buffer_2
  assign address_out = controlled_buffer_1_out;  // Buffer buffer_4, 16 bits wide
  // also tied to GND on the sheet: {decoder_1_out6[0], decoder_1_out6[1], decoder_1_out6[2], decoder_1_out6[3]}
endmodule

module cu_parallel_decode (
  input  flag,
  input  [7:0] instruction,
  input  mic_count,
  input  mic_reset,
  input  clk,
  output [7:0] rom_3_out,
  output [7:0] rom_1_out,
  output [7:0] rom_2_out,
  output [7:0] c_reg_select,
  output [7:0] rom_4_out
);

  wire d_ff_1_q, d_ff_2_q;
  wire [3:0] counter_1_q;
  wire [3:3] buffer_3_out;
  wire [7:0] buffer_2_out, rom_1_data, rom_2_data, rom_3_data, rom_4_data;
  wire [11:0] or_2_out;
  wire [11:11] or_1_out, or_3_out, or_4_out;

  D_Flip_Flop d_ff_1 (.D(mic_reset), .clk(clk), .Q(d_ff_1_q));  // open: Qn, preset, reset
  Counter #(.max('hf), .width(4)) counter_1 (
    .clr(d_ff_1_q), .load(1'b0), .up(mic_count), .count(mic_count), .clk(clk), .D(4'b0000), .Q(counter_1_q));  // open: carry
  assign or_2_out[7:0] = instruction;  // Buffer buffer_1, 8 bits wide
  D_Flip_Flop d_ff_2 (.D(flag), .clk(clk), .Q(d_ff_2_q));  // open: Qn, preset, reset
  assign buffer_2_out = instruction;  // Buffer buffer_2, 8 bits wide
  or or_1 (or_1_out[11], buffer_3_out[3], d_ff_2_q);
  assign {buffer_3_out[3], or_2_out[10:8]} = counter_1_q;  // Buffer buffer_3, 4 bits wide
  ROM #(.addrWidth(12)) rom_1 (.addr({or_1_out[11], or_2_out[10:0]}), .data(rom_1_data));
  ROM #(.addrWidth(12)) rom_1_dup2 (.addr({1'b0, counter_1_q[2:0], buffer_2_out}), .data(c_reg_select));
  assign rom_1_out = rom_1_data;  // Buffer buffer_4, 8 bits wide
  ROM #(.addrWidth(12)) rom_2 (.addr(or_2_out), .data(rom_2_data));
  or or_2 (or_2_out[11], buffer_3_out[3], d_ff_2_q);
  or or_3 (or_3_out[11], d_ff_2_q, buffer_3_out[3]);
  assign rom_2_out = rom_2_data;  // Buffer buffer_5, 8 bits wide
  or or_4 (or_4_out[11], buffer_3_out[3], d_ff_2_q);
  ROM #(.addrWidth(12)) rom_3 (.addr({or_4_out[11], or_2_out[10:0]}), .data(rom_3_data));
  ROM #(.addrWidth(12)) rom_4 (.addr({or_3_out[11], or_2_out[10:0]}), .data(rom_4_data));
  assign rom_3_out = rom_3_data;  // Buffer buffer_6, 8 bits wide
  assign rom_4_out = rom_4_data;  // Buffer buffer_7, 8 bits wide
endmodule

// VHDL entity counter_3_data, as the project stores it:
--------------------------------------------------------------------------------
-- Project : Conter Versione 3
-- File    :
-- Autor   :
-- Date    :
--
--------------------------------------------------------------------------------
-- Description : Conter a 16 bit, non decrementa correttamente
--

--SIGNAL:

--RESET: reset dei circuiti
--CL : segnale di clock
--ENABLE: attivazione dei chip
--LOAD/COUNT: se il bit è a 0 conta, se è a 1 carica dal buffer in ingresso

--INPUT/OUTPUT

--Buffer_in: buffer a 16 bit di input

--Buffer_out: buffer a 16 bit di output


--------------------------------------------------------------------------------

LIBRARY ieee;
USE ieee.std_logic_1164.all;

ENTITY counter_3_data IS
  PORT (
  ------------------------------------------------------------------------------
  --Insert input ports below
    clock      : IN  std_logic;                    -- input bit example
    val        : IN  std_logic_vector(3 DOWNTO 0); -- input vector example
  ------------------------------------------------------------------------------
  --Insert output ports below
    max        : OUT std_logic;                    -- output bit example
    cpt        : OUT std_logic_vector(3 DOWNTO 0)  -- output vector example
    );
END counter_3_data;

--------------------------------------------------------------------------------
--Complete your VHDL description below
--------------------------------------------------------------------------------

ARCHITECTURE TypeArchitecture OF counter_3_data IS

BEGIN


END TypeArchitecture;

// VHDL entity cu_2_data, as the project stores it:
--------------------------------------------------------------------------------
-- Project :
-- File    :
-- Autor   :
-- Date    :
--
--------------------------------------------------------------------------------
-- Description :
-- Logica di passaggio dati tra le varie sezioni
-- decodifica separata in due sezioni diverse
-- Eseguzione istantanea ad ogni stadio di decodifica


--da fare: unire lo stadio di decodifica in uno solo
--passare il microcode decodificato nello stadio successivo per eseguirlo, passare anche l'istruzione per controllo hazard
--------------------------------------------------------------------------------

LIBRARY ieee;
USE ieee.std_logic_1164.all;

ENTITY cu_2_data IS
  PORT (
  ------------------------------------------------------------------------------
  --Insert input ports below
    clock      : IN  std_logic;                    -- input bit example
    val        : IN  std_logic_vector(3 DOWNTO 0); -- input vector example
  ------------------------------------------------------------------------------
  --Insert output ports below
    max        : OUT std_logic;                    -- output bit example
    cpt        : OUT std_logic_vector(3 DOWNTO 0)  -- output vector example
    );
END cu_2_data;

--------------------------------------------------------------------------------
--Complete your VHDL description below
--------------------------------------------------------------------------------

ARCHITECTURE TypeArchitecture OF cu_2_data IS

BEGIN


END TypeArchitecture;

// VHDL entity cu_3_data, as the project stores it:
--------------------------------------------------------------------------------
-- Project :
-- File    :
-- Autor   :
-- Date    :
--
--------------------------------------------------------------------------------
-- Description :
-- Implementazione separazione stadi pipeline
-- Corretta implementazione trifase e di passaggio


--Passaggio dati da PC a Fetch unit nella CU correttamente funzionante: il dato viene memorizzato nel registro IF/Dec

--Passaggio dati da IF/dec a stadio di decodifica: il dato viene decodificato e mandato in uscita nei registri Dec/Ex

--Passaggio dati da Dec/Ex al buffer per le linee di cotrollo: l'istruzione viene eseguita propagando le linee di controllo


-- Cose da implementare:


--Lettura degli indirizzi di memoria e memorizzarli in un registro per gli indirizzi

--Implementazione di una Hazard Controll Unit ( HCU )
--------------------------------------------------------------------------------

LIBRARY ieee;
USE ieee.std_logic_1164.all;

ENTITY cu_3_data IS
  PORT (
  ------------------------------------------------------------------------------
  --Insert input ports below
    clock      : IN  std_logic;                    -- input bit example
    val        : IN  std_logic_vector(3 DOWNTO 0); -- input vector example
  ------------------------------------------------------------------------------
  --Insert output ports below
    max        : OUT std_logic;                    -- output bit example
    cpt        : OUT std_logic_vector(3 DOWNTO 0)  -- output vector example
    );
END cu_3_data;

--------------------------------------------------------------------------------
--Complete your VHDL description below
--------------------------------------------------------------------------------

ARCHITECTURE TypeArchitecture OF cu_3_data IS

BEGIN


END TypeArchitecture;
