// Logisim project cpu_rebuild.circ as structural Verilog: 11 circuits, main circuit main
module main (
  input  power,
  input  [7:0] buffer_in,
  input  clk,
  input  irq,
  input  nmi,
  input  reset,
  output w_r,
  output [7:0] data_bus_out,
  output [15:0] address_bus
);

  wire adc, address_clc, address_lb_oe, address_oe_alu, and_op, \bit , break_data, break_update,
       brk_flag_for_pc, bus_oe_pch, bus_oe_pcl, carry_data, carry_data_cu, carry_out_for_alu, carry_update,
       carry_update_cu, cmp, cpu_data_in, cpu_data_out, d_bus_oe, dec, decimal_data_cu, decimal_out_for_alu,
       decimapl_update_cu, direct_adr_out, flag_in, hb_latch_we, hb_we, inc, interrupt_data_cu,
       interrupt_logic_1_cu_reset, interrupt_logic_1_irq_detect, interrupt_logic_1_nmi_detect,
       interrupt_logic_1_reset_detect, interrupt_update_cu, irq_detect, irq_operation_mode, isr_we,
       latch_hb_oe_adr, latch_lb_oe_adr, lb_latch_oe, lb_latch_we, lb_we, lh_latch_oe, load_alu_data,
       load_saved_address, lsl, lsr, mic_reset, neg_data, neg_update, not_1_out, oe_a, oe_a_alu, oe_x,
       oe_x_alu, oe_y, oe_y_alu, or_5_out, or_6_out, or_7_out, or_8_out, or_9_out, or_10_out, or_11_out,
       or_12_out, or_13_out, or_op, overflow_data, overflow_data_cu, overflow_update, overflow_update_cu,
       pc_count, pc_direct_load, pc_enable, pc_oe, pcl_pch_load, rol_op, ror_op, save_address, sbc,
       sp_command, sp_dec_pch_bus, sp_dec_pcl_bus, sp_enable, sp_inc_pch_we, sp_inc_pcl_we, sp_oe,
       sp_oe_pch_bus, sp_oe_pcl_bus, sp_we, status_resdet, status_to_bus, status_we, we_a, we_a_alu,
       we_b_alu, we_pch, we_pcl, we_x, we_y, xor_op;
  wire [3:0] status_update_data, status_update_sgn;
  wire [7:0] a_data_for_alu, flag_request, internal_buffer;
  wire [10:0] decoded_rom_4;
  wire [15:0] alu_address_out;
  wire [22:0] decoded_rom_1, decoded_rom_3;
  wire [26:0] decoded_rom2;

  not not_1 (not_1_out, irq_operation_mode);
  and and_1 (irq_detect, irq, not_1_out);
  LedBar ledbar_1 (
    .led0(internal_buffer[7]), .led1(internal_buffer[6]), .led2(internal_buffer[5]),
    .led3(internal_buffer[4]), .led4(internal_buffer[3]), .led5(internal_buffer[2]),
    .led6(internal_buffer[1]), .led7(internal_buffer[0]));
  assign internal_buffer = cpu_data_in ? buffer_in : 8'bz;  // Controlled_Buffer controlled_buffer_1
  cu_sng_adapter cu_sng_adapter_1 (
    .decoded_cl_1(decoded_rom_1), .decoded_cl_2(decoded_rom2), .decoded_cl_3(decoded_rom_3),
    .in_4(decoded_rom_4), .lb_dlatch_we(lb_latch_we), .hb_dlatch_we(hb_latch_we), .lb_dlatch_oe(lb_latch_oe),
    .hb_dlatch_oe(lh_latch_oe), .lb_latch_oe_adr(latch_lb_oe_adr), .dlatch_oe_adr(latch_hb_oe_adr),
    .status_to_bus(status_to_bus), .status_we(status_we), .carry_update(carry_update_cu),
    .interrupt_update(interrupt_update_cu), .decimal_update(decimapl_update_cu),
    .overflow_update(overflow_update_cu), .carry_data(carry_data_cu), .interrupt_data(interrupt_data_cu),
    .decimal_data(decimal_data_cu), .overflow_data(overflow_data_cu), .isr_we(isr_we),
    .cpu_data_in(cpu_data_in), .cpu_data_out(cpu_data_out), .pcl_pch_load(pcl_pch_load), .we_pcl(we_pcl),
    .we_pch(we_pch), .bus_oe_pcl(bus_oe_pcl), .bus_oe_pch(bus_oe_pch), .pc_count(pc_count),
    .pc_enable(pc_enable), .pc_oe(pc_oe), .sp_enable(sp_enable), .sp_oe(sp_oe), .sp_command(sp_command),
    .sp_we(sp_we), .sp_dec_pcl_bus(sp_dec_pcl_bus), .sp_dec_pch_bus(sp_dec_pch_bus),
    .sp_inc_pcl_we(sp_inc_pch_we), .sp_inc_pch_we(sp_inc_pcl_we), .sp_oe_pcl_bus(sp_oe_pch_bus),
    .sp_oe_pch_bus(sp_oe_pcl_bus), .load_alu_address(load_alu_data), .save_address(save_address),
    .load_saved_address(load_saved_address), .adc(adc), .sbc(sbc), .and_op(and_op), .or_op(or_op),
    .xor_op(xor_op), .lsl(lsl), .lsr(lsr), .rol_op(rol_op), .ror_op(ror_op), .\bit (\bit ), .cmp(cmp),
    .inc(inc), .dec(dec), .address_clc(address_clc), .bus_oe(d_bus_oe), .address_oe(address_oe_alu),
    .address_oe_lb(address_lb_oe), .we_a_alu(we_a_alu), .we_b_alu(we_b_alu), .direct_adr_out(direct_adr_out),
    .lb_we(lb_we), .hb_we(hb_we), .oe_x(oe_x), .we_x(we_x), .oe_y(oe_y), .we_y(we_y), .oe_a(oe_a),
    .we_a(we_a), .oe_x_alu(oe_x_alu), .oe_y_alu(oe_y_alu), .oe_a_alu(oe_a_alu), .mic_reset(mic_reset),
    .pc_direct_load(pc_direct_load), .break_update(break_update), .break_data(break_data),
    .status_reset(status_resdet));
  interrupt_logic interrupt_logic_1 (
    .clk(clk), .mic_reset(mic_reset), .irq(irq_detect), .nmi(nmi), .reset(reset), .power(power),
    .irq_detect(interrupt_logic_1_irq_detect), .nmi_detect(interrupt_logic_1_nmi_detect),
    .reset_detect(interrupt_logic_1_reset_detect), .cu_reset(interrupt_logic_1_cu_reset));
  not not_2 (w_r, cpu_data_out);
  assign data_bus_out = cpu_data_out ? internal_buffer : 8'bz;  // Controlled_Buffer controlled_buffer_2
  cu cu_1 (
    .buffer_in(buffer_in), .isr_we(isr_we), .clk(clk), .flag_in(flag_in),
    .cu_reset(interrupt_logic_1_cu_reset), .irq_detect(interrupt_logic_1_irq_detect),
    .nmi_detect(interrupt_logic_1_nmi_detect), .reset_detect(interrupt_logic_1_reset_detect),
    .flag_request_out(flag_request), .mic_reset_out(mic_reset), .decoded_rom_1(decoded_rom_1),
    .decoded_rom_2(decoded_rom2), .decoded_rom_3(decoded_rom_3), .decoded_rom_4(decoded_rom_4));
  tr tr_1 (
    .buffer_in(internal_buffer), .clk(clk), .latch_lb_we(lb_latch_we), .latch_hb_we(hb_latch_we),
    .latch_lb_oe(lb_latch_oe), .latch_hb_oe(lh_latch_oe), .latch_lb_adr_oe(latch_lb_oe_adr),
    .latch_adr_oe(latch_hb_oe_adr), .buffer_out(internal_buffer), .address_out(address_bus));
  or or_1 (carry_update, status_update_sgn[3], carry_update_cu);
  or or_2 (carry_data, status_update_data[3], carry_data_cu);
  register_module register_module_1 (
    .buffer_in(internal_buffer), .clk(clk), .a_we(we_a), .x_we(we_x), .y_we(we_y), .a_oe(oe_a), .x_oe(oe_x),
    .y_oe(oe_y), .x_alu_oe(oe_x_alu), .y_oe_alu(oe_y_alu), .a_oe_alu(oe_a_alu),
    .main_buffer_out(internal_buffer), .alu_a_input_register(a_data_for_alu));
  or or_3 (overflow_update, status_update_sgn[2], overflow_update_cu);
  or or_4 (overflow_data, status_update_data[2], overflow_data_cu);
  or or_5 (or_5_out, sp_dec_pcl_bus, sp_oe_pcl_bus, sp_dec_pch_bus);
  or or_6 (or_6_out, pcl_pch_load, sp_oe_pch_bus, pcl_pch_load);
  or or_7 (or_7_out, sp_dec_pcl_bus, sp_inc_pch_we, sp_dec_pch_bus, sp_oe_pch_bus, sp_inc_pcl_we, sp_oe_pcl_bus);
  or or_8 (or_8_out, or_7_out, sp_oe);
  or or_9 (or_9_out, irq_detect, brk_flag_for_pc);
  or or_10 (or_10_out, sp_inc_pcl_we, we_pcl);
  or or_11 (or_11_out, sp_inc_pch_we, we_pch);
  or or_12 (or_12_out, or_7_out, sp_enable);
  or or_13 (or_13_out, sp_inc_pch_we, sp_inc_pcl_we, 1'b0, sp_command);
  sr sr_1 (
    .register_out(status_to_bus), .register_we(status_we), .buffer_in(internal_buffer), .clk(clk),
    .n_request(flag_request[0]), .o_request(flag_request[1]), .b_request(flag_request[2]),
    .d_request(flag_request[3]), .irq_reset(flag_request[4]), .z_request(flag_request[5]),
    .c_request(flag_request[6]), .n_data(neg_data), .o_data(overflow_data), .b_data(break_data),
    .d_data(decimapl_update_cu), .irq_data(interrupt_update_cu), .z_data(status_update_data[0]),
    .c_data(carry_data), .n_we(neg_update), .o_we(overflow_update), .b_we(break_update),
    .d_we(decimal_data_cu), .irq_we(interrupt_data_cu), .z_we(status_update_sgn[0]), .c_we(carry_update),
    .status_reset(status_resdet), .buffer_out(internal_buffer), .flag_serve_request(flag_in),
    .carry_out(carry_out_for_alu), .bcd_mode(decimal_out_for_alu), .irq_operation(irq_operation_mode),
    .brk_flag(brk_flag_for_pc));
  pc pc_1 (
    .pc_direct_load(pc_direct_load), .irq_sgn(or_9_out), .nmi_sgn(nmi), .reset_sgn(reset),
    .buffer_in(internal_buffer), .pc_reset(1'b0), .pc_oe(pc_oe), .pc_lb_bus_oe(bus_oe_pcl),
    .pc_hb_bus_oe(bus_oe_pch), .mic_reset(mic_reset), .clk(clk), .pc_enable(pc_enable),
    .pc_command(pc_count), .pcl_bus_load(or_10_out), .pch_bus_load(or_11_out), .pcl_to_pc(or_5_out),
    .pch_to_pc(or_6_out), .load_alu(load_alu_data), .save_address(save_address),
    .load_saved_address(load_saved_address), .address_in(alu_address_out), .address_bus(address_bus),
    .buffer_out(internal_buffer));
  sp sp_1 (
    .buffer_in(internal_buffer), .sp_bus_oe(1'b0), .sp_oe(or_8_out), .sp_reset(1'b0), .clk(clk),
    .sp_load(sp_we), .sp_enable(or_12_out), .sp_command(or_13_out), .address_bus(address_bus),
    .buffer_out(internal_buffer));
  alu alu_1 (
    .clk(clk), .carry_in(carry_out_for_alu), .decimal_in(decimal_out_for_alu), .a_in(a_data_for_alu),
    .b_in(internal_buffer), .a_we(we_a_alu), .b_we(we_b_alu), .lb_we(lb_we), .hb_we(hb_we),
    .direct_adr_out(direct_adr_out), .address_bus_lb_oe(address_lb_oe), .address_bus_oe(address_oe_alu),
    .d_bus_oe(d_bus_oe), .adc(adc), .sbc(sbc), .and_op(and_op), .or_op(or_op), .xor_op(xor_op),
    .ror_op(ror_op), .rol_op(rol_op), .lsr(lsr), .lsl(lsl), .inc(inc), .dec(dec), .cmp(cmp), .\bit (\bit ),
    .mic_reset(mic_reset), .buffer_out(internal_buffer), .address_out(alu_address_out),
    .status_update_sgn({status_update_sgn[3:2], neg_update, status_update_sgn[0]}),
    .status_update_data({status_update_data[3:2], neg_data, status_update_data[0]}),
    .direct_address_bus(address_bus));
  // also tied to GND on the sheet: {flag_request[7], internal_buffer[0], internal_buffer[1], internal_buffer[2], internal_buffer[3], internal_buffer[4], internal_buffer[5], internal_buffer[6], internal_buffer[7]}

  // Other names for the same wires on the sheet: address_out[15:0] = address_bus; nmi_detect = nmi;
  //   reset_detect = reset; zero_data = status_update_data[0]; status_update_data[1] = neg_data;
  //   zero_update = status_update_sgn[0]; status_update_sgn[1] = neg_update
endmodule

module register_module (
  input  [7:0] buffer_in,
  input  clk,
  input  a_we,
  input  x_we,
  input  y_we,
  input  a_oe,
  input  x_oe,
  input  y_oe,
  input  x_alu_oe,
  input  y_oe_alu,
  input  a_oe_alu,
  output [7:0] main_buffer_out,
  output [7:0] alu_a_input_register
);

  wire [7:0] register_1_q, register_2_q, register_3_q;

  Register register_1 (.D(buffer_in), .en(a_we), .clk(clk), .Q(register_1_q));  // open: clr
  Register register_2 (.D(buffer_in), .en(x_we), .clk(clk), .Q(register_2_q));  // open: clr
  Register register_3 (.D(buffer_in), .en(y_we), .clk(clk), .Q(register_3_q));  // open: clr
  assign main_buffer_out = a_oe ? register_1_q : 8'bz;  // Controlled_Buffer controlled_buffer_1
  assign main_buffer_out = x_oe ? register_2_q : 8'bz;  // Controlled_Buffer controlled_buffer_2
  assign main_buffer_out = y_oe ? register_3_q : 8'bz;  // Controlled_Buffer controlled_buffer_3
  assign alu_a_input_register = y_oe_alu ? register_3_q : 8'bz;  // Controlled_Buffer controlled_buffer_4
  assign alu_a_input_register = a_oe_alu ? register_1_q : 8'bz;  // Controlled_Buffer controlled_buffer_5
  assign alu_a_input_register = x_alu_oe ? register_2_q : 8'bz;  // Controlled_Buffer controlled_buffer_6

  // Other names for the same wires on the sheet: x_oe_alu = x_alu_oe
endmodule

module sp (
  input  [7:0] buffer_in,
  input  sp_bus_oe,
  input  sp_oe,
  input  sp_reset,
  input  clk,
  input  sp_load,
  input  sp_enable,
  input  sp_command,
  output [15:0] address_bus,
  output [7:0] buffer_out
);

  wire not_1_out;
  wire [7:0] buffer_out_t;

  Counter counter_1 (
    .clr(sp_reset), .load(sp_load), .up(sp_command), .count(sp_enable), .clk(clk), .D(buffer_in),
    .Q(buffer_out_t));  // open: carry
  assign address_bus = not_1_out ? {16{1'b0}} : 16'bz;  // Controlled_Buffer controlled_buffer_1
  not not_1 (not_1_out, sp_oe);
  assign address_bus = sp_oe ? {8'h1, buffer_out_t} : 16'bz;  // Controlled_Buffer controlled_buffer_2
  assign buffer_out = sp_bus_oe ? buffer_out_t : 8'bz;  // Controlled_Buffer controlled_buffer_3
endmodule

module pc (
  input  pc_direct_load,
  input  irq_sgn,
  input  nmi_sgn,
  input  reset_sgn,
  input  [7:0] buffer_in,
  input  pc_reset,
  input  pc_oe,
  input  pc_lb_bus_oe,
  input  pc_hb_bus_oe,
  input  mic_reset,
  input  clk,
  input  pc_enable,
  input  pc_command,
  input  pcl_bus_load,
  input  pch_bus_load,
  input  pcl_to_pc,
  input  pch_to_pc,
  input  load_alu,
  input  save_address,
  input  load_saved_address,
  input  [15:0] address_in,
  output [15:0] address_bus,
  output [7:0] buffer_out
);

  wire and_1_out, and_2_out, and_3_out, counter_1_carry, not_1_out, not_2_out, pc_enable_t, pc_load,
       pch_bus_we, pcl_bus_we;
  wire [7:0] alu_hb_in, alu_lb_in, buffer_in_t, fetch_hight_b, fetch_low_b, hight_b_out, low_b_out, pch_q,
       pch_s_q, pcl_q, pcl_s_q;

  assign {alu_hb_in, alu_lb_in} = load_alu ? address_in : 16'bz;  // Controlled_Buffer controlled_buffer_1
  assign buffer_in_t = not_1_out ? buffer_in : 8'bz;  // Controlled_Buffer controlled_buffer_2
  not not_1 (not_1_out, mic_reset);
  or or_1 (pcl_bus_we, mic_reset, pcl_bus_load);
  or or_2 (pch_bus_we, pch_bus_load, mic_reset);
  or or_3 (pc_load, pcl_to_pc, pch_to_pc, pc_direct_load, load_alu, load_saved_address);
  or or_4 (pc_enable_t, pc_direct_load, pc_enable);
  assign {alu_hb_in, alu_lb_in} = and_1_out ? 16'hfffc : 16'bz;  // Controlled_Buffer controlled_buffer_3
  and and_1 (and_1_out, reset_sgn, pc_direct_load);
  Counter counter_1 (
    .clr(pc_reset), .load(pc_load), .up(pc_command), .count(pc_enable_t), .clk(clk), .D(alu_lb_in),
    .carry(counter_1_carry), .Q(low_b_out));
  Counter counter_2 (
    .clr(pc_reset), .load(pc_load), .up(pc_command), .count(counter_1_carry), .clk(clk), .D(alu_hb_in),
    .Q(hight_b_out));  // open: carry
  assign fetch_low_b = buffer_in_t;  // Buffer buffer_1, 8 bits wide
  assign address_bus = not_2_out ? {16{1'b0}} : 16'bz;  // Controlled_Buffer controlled_buffer_4
  not not_2 (not_2_out, pc_oe);
  assign address_bus = pc_oe ? {hight_b_out, low_b_out} : 16'bz;  // Controlled_Buffer controlled_buffer_5
  Register pcl (.D(fetch_low_b), .en(pcl_bus_we), .clk(clk), .Q(pcl_q));  // open: clr
  Register pcl_s (.D(low_b_out), .en(save_address), .clk(clk), .Q(pcl_s_q));  // open: clr
  assign alu_lb_in = pcl_to_pc ? pcl_q : 8'bz;  // Controlled_Buffer controlled_buffer_6
  assign buffer_out = pc_lb_bus_oe ? pcl_q : 8'bz;  // Controlled_Buffer controlled_buffer_7
  assign alu_lb_in = load_saved_address ? pcl_s_q : 8'bz;  // Controlled_Buffer controlled_buffer_8
  assign fetch_low_b = mic_reset ? low_b_out : 8'bz;  // Controlled_Buffer controlled_buffer_9
  assign fetch_hight_b = mic_reset ? hight_b_out : 8'bz;  // Controlled_Buffer controlled_buffer_10
  assign {alu_hb_in, alu_lb_in} = and_2_out ? 16'hfffa : 16'bz;  // Controlled_Buffer controlled_buffer_11
  and and_2 (and_2_out, irq_sgn, pc_direct_load);
  assign fetch_hight_b = buffer_in_t;  // Buffer buffer_2, 8 bits wide
  Register pch (.D(fetch_hight_b), .en(pch_bus_we), .clk(clk), .Q(pch_q));  // open: clr
  Register pch_s (.D(hight_b_out), .en(save_address), .clk(clk), .Q(pch_s_q));  // open: clr
  assign alu_hb_in = pch_to_pc ? pch_q : 8'bz;  // Controlled_Buffer controlled_buffer_12
  assign alu_hb_in = load_saved_address ? pch_s_q : 8'bz;  // Controlled_Buffer controlled_buffer_13
  assign buffer_out = pc_hb_bus_oe ? pch_q : 8'bz;  // Controlled_Buffer controlled_buffer_14
  assign {alu_hb_in, alu_lb_in} = and_3_out ? 16'hfffe : 16'bz;  // Controlled_Buffer controlled_buffer_15
  and and_3 (and_3_out, nmi_sgn, pc_direct_load);

  // Other names for the same wires on the sheet: low_b_interrupt[7:0] = alu_lb_in; pcl_bus[7:0] = alu_lb_in;
  //   pcl_saved_register[7:0] = alu_lb_in; hight_b_interrupt[7:0] = alu_hb_in; pch_bus[7:0] = alu_hb_in;
  //   pch_saved_register[7:0] = alu_hb_in; irq_signal = irq_sgn; load_alu_address = load_alu;
  //   load_save_address = load_saved_address; nmi_signal = nmi_sgn; pc_save_address = save_address;
  //   reset_signal = reset_sgn
endmodule

module tr (
  input  [7:0] buffer_in,
  input  clk,
  input  latch_lb_we,
  input  latch_hb_we,
  input  latch_lb_oe,
  input  latch_hb_oe,
  input  latch_lb_adr_oe,
  input  latch_adr_oe,
  output [7:0] buffer_out,
  output [15:0] address_out
);

  wire latch_lb_adr_oe_t, not_1_out, not_2_out;
  wire [7:0] register_1_q, register_2_q;

  or or_1 (latch_lb_adr_oe_t, latch_lb_adr_oe, latch_adr_oe);
  Register register_1 (.D(buffer_in), .en(latch_lb_we), .clk(clk), .Q(register_1_q));  // open: clr
  Register register_2 (.D(buffer_in), .en(latch_hb_we), .clk(clk), .Q(register_2_q));  // open: clr
  assign address_out[7:0] = not_1_out ? {8{1'b0}} : 8'bz;  // Controlled_Buffer controlled_buffer_1
  not not_1 (not_1_out, latch_lb_adr_oe_t);
  assign address_out[15:8] = not_2_out ? {8{1'b0}} : 8'bz;  // Controlled_Buffer controlled_buffer_2
  not not_2 (not_2_out, latch_adr_oe);
  assign buffer_out = latch_lb_oe ? register_1_q : 8'bz;  // Controlled_Buffer controlled_buffer_3
  assign address_out[7:0] = latch_lb_adr_oe_t ? register_1_q : 8'bz;  // Controlled_Buffer controlled_buffer_4
  assign buffer_out = latch_hb_oe ? register_2_q : 8'bz;  // Controlled_Buffer controlled_buffer_5
  assign address_out[15:8] = latch_adr_oe ? register_2_q : 8'bz;  // Controlled_Buffer controlled_buffer_6

  // Other names for the same wires on the sheet: latch_lb_buffer[7:0] = address_out[7:0];
  //   latch_hb_buffer[7:0] = address_out[15:8]; latch_hb_adr_oe = latch_adr_oe
endmodule

module interrupt_logic (
  input  clk,
  input  mic_reset,
  input  irq,
  input  nmi,
  input  reset,
  input  power,
  output irq_detect,
  output nmi_detect,
  output reset_detect,
  output cu_reset
);

  wire controlled_buffer_1_out, d_ff_1_q, d_ff_2_q, d_ff_5_q, nand_1_out, not_1_out;

  D_Flip_Flop d_ff_1 (.D(power), .clk(clk), .Q(d_ff_1_q));  // open: Qn, preset, reset
  D_Flip_Flop d_ff_2 (.D(mic_reset), .clk(controlled_buffer_1_out), .Q(d_ff_2_q));  // open: Qn, preset, reset
  assign controlled_buffer_1_out = not_1_out ? clk : 1'bz;  // Controlled_Buffer controlled_buffer_1
  not not_1 (not_1_out, d_ff_2_q);
  D_Flip_Flop d_ff_3 (.D(irq), .clk(clk), .Q(irq_detect), .reset(mic_reset));  // open: Qn, preset
  D_Flip_Flop d_ff_4 (.D(nmi), .clk(clk), .Q(nmi_detect), .reset(mic_reset));  // open: Qn, preset
  D_Flip_Flop d_ff_5 (.D(reset), .clk(clk), .Q(d_ff_5_q), .reset(mic_reset));  // open: Qn, preset
  nand nand_1 (nand_1_out, d_ff_1_q, d_ff_2_q);
  or or_1 (reset_detect, d_ff_5_q, nand_1_out);
  or or_2 (cu_reset, irq, nmi, reset);

  // Other names for the same wires on the sheet: irq_signal = irq; nmi_signal = nmi; reset_signal = reset
endmodule

module cu (
  input  [7:0] buffer_in,
  input  isr_we,
  input  clk,
  input  flag_in,
  input  cu_reset,
  input  irq_detect,
  input  nmi_detect,
  input  reset_detect,
  output [7:0] flag_request_out,
  output mic_reset_out,
  output [22:0] decoded_rom_1,
  output [26:0] decoded_rom_2,
  output [22:0] decoded_rom_3,
  output [10:0] decoded_rom_4
);

  wire d_ff_1_q, decoder_2_out4, decoder_3_out10, decoder_5_out10, decoder_7_out4, not_1_out, not_2_out,
       not_3_out, not_4_out, not_5_out, not_6_out, or_3_out, switch_buffer;
  wire [4:0] rom_1_decode_instruction, rom_3_decode_instruction;
  wire [6:0] rom_4_decode_instruction;
  wire [7:0] custom_buffer, micro_counter_out, rom_2_decode_instruction;
  wire [15:0] cl_address_out;

  or or_1 (switch_buffer, reset_detect, nmi_detect, irq_detect);
  assign cl_address_out[15:8] = {flag_in, {7{1'b0}}} | micro_counter_out;  // OR_Gate or_2, 8 bits wide
  D_Flip_Flop d_ff_1 (.D(or_3_out), .clk(not_1_out), .Q(d_ff_1_q), .reset(d_ff_1_q));  // open: Qn, preset
  or or_3 (or_3_out, cu_reset, decoded_rom_4[10]);
  not not_1 (not_1_out, clk);
  not not_2 (not_2_out, rom_1_decode_instruction[4]);
  Decoder #(.select(4)) decoder_1 (
    .out0(decoded_rom_1[0]), .out1(decoded_rom_1[1]), .out2(decoded_rom_1[2]), .out3(decoded_rom_1[3]),
    .out4(decoded_rom_1[4]), .out5(decoded_rom_1[5]), .out6(decoded_rom_1[6]), .out7(decoded_rom_1[7]),
    .out8(decoded_rom_1[8]), .out9(decoded_rom_1[9]), .out10(decoded_rom_1[10]), .out11(decoded_rom_1[11]),
    .out12(decoded_rom_1[12]), .out13(decoded_rom_1[13]), .out14(decoded_rom_1[14]),
    .out15(decoded_rom_1[15]), .sel(rom_1_decode_instruction[3:0]), .en(not_2_out));
  Decoder #(.select(4)) decoder_2 (
    .out0(decoded_rom_1[16]), .out1(decoded_rom_1[17]), .out2(decoded_rom_1[18]), .out3(decoded_rom_1[19]),
    .out4(decoder_2_out4), .out5(decoder_2_out4), .out6(decoder_2_out4), .out7(decoder_2_out4),
    .out8(decoder_2_out4), .out9(decoder_2_out4), .out10(decoder_2_out4), .out11(decoder_2_out4),
    .out12(decoder_2_out4), .out13(decoder_2_out4), .out14(decoder_2_out4), .out15(decoder_2_out4),
    .sel(rom_1_decode_instruction[3:0]), .en(rom_1_decode_instruction[4]));
  not not_3 (not_3_out, switch_buffer);
  assign custom_buffer = not_3_out ? buffer_in : 8'bz;  // Controlled_Buffer controlled_buffer_1
  ROM cond_out (.addr(cl_address_out[7:0]), .data(flag_request_out));
  not not_4 (not_4_out, rom_4_decode_instruction[4]);
  Decoder #(.select(4)) decoder_3 (
    .out0(decoded_rom_4[0]), .out1(decoded_rom_4[1]), .out2(decoded_rom_4[2]), .out3(decoded_rom_4[3]),
    .out4(decoded_rom_4[4]), .out5(decoded_rom_4[5]), .out6(decoded_rom_4[6]), .out7(decoded_rom_4[7]),
    .out8(decoded_rom_4[8]), .out9(decoded_rom_4[9]), .out10(decoder_3_out10), .out11(decoder_3_out10),
    .out12(decoder_3_out10), .out13(decoder_3_out10), .out14(decoder_3_out10), .out15(decoder_3_out10),
    .sel(rom_4_decode_instruction[3:0]), .en(not_4_out));
  Register isr (.D(custom_buffer), .en(isr_we), .clk(clk), .Q(cl_address_out[7:0]));  // open: clr
  assign custom_buffer = reset_detect ? 8'hef : 8'bz;  // Controlled_Buffer reset
  assign custom_buffer = nmi_detect ? 8'hdf : 8'bz;  // Controlled_Buffer nmi
  assign custom_buffer = irq_detect ? {8{1'b1}} : 8'bz;  // Controlled_Buffer irq
  Counter counter_1 (
    .clr(d_ff_1_q), .load(1'b0), .up(1'b1), .count(1'b1), .clk(clk), .D({8{1'b0}}), .Q(micro_counter_out));  // open: carry
  not not_5 (not_5_out, rom_2_decode_instruction[4]);
  Decoder #(.select(4)) decoder_4 (
    .out0(decoded_rom_2[0]), .out1(decoded_rom_2[1]), .out2(decoded_rom_2[2]), .out3(decoded_rom_2[3]),
    .out4(decoded_rom_2[4]), .out5(decoded_rom_2[5]), .out6(decoded_rom_2[6]), .out7(decoded_rom_2[7]),
    .out8(decoded_rom_2[8]), .out9(decoded_rom_2[9]), .out10(decoded_rom_2[10]), .out11(decoded_rom_2[11]),
    .out12(decoded_rom_2[12]), .out13(decoded_rom_2[13]), .out14(decoded_rom_2[14]),
    .out15(decoded_rom_2[15]), .sel(rom_2_decode_instruction[3:0]), .en(not_5_out));
  Decoder #(.select(4)) decoder_5 (
    .out0(decoded_rom_2[16]), .out1(decoded_rom_2[17]), .out2(decoded_rom_2[18]), .out3(decoded_rom_2[19]),
    .out4(decoded_rom_2[20]), .out5(decoded_rom_2[21]), .out6(decoded_rom_2[22]), .out7(decoded_rom_2[23]),
    .out8(decoded_rom_2[24]), .out9(decoded_rom_2[25]), .out10(decoder_5_out10), .out11(decoder_5_out10),
    .out12(decoder_5_out10), .out13(decoder_5_out10), .out14(decoder_5_out10), .out15(decoder_5_out10),
    .sel(rom_2_decode_instruction[3:0]), .en(rom_2_decode_instruction[4]));
  ROM #(.addrWidth(16)) rom_1 (.addr(cl_address_out), .data({decoded_rom_1[22:20], rom_1_decode_instruction}));
  ROM #(.addrWidth(16)) rom_2 (
    .addr(cl_address_out),
    .data({{2{rom_2_decode_instruction[7]}}, decoded_rom_2[26], rom_2_decode_instruction[4:0]}));
  ROM #(.addrWidth(16)) rom_3 (.addr(cl_address_out), .data({decoded_rom_3[22:20], rom_3_decode_instruction}));
  ROM #(.addrWidth(16)) rom_4 (
    .addr(cl_address_out),
    .data({decoded_rom_4[10], {2{rom_4_decode_instruction[6]}}, rom_4_decode_instruction[4:0]}));
  not not_6 (not_6_out, rom_3_decode_instruction[4]);
  Decoder #(.select(4)) decoder_6 (
    .out0(decoded_rom_3[0]), .out1(decoded_rom_3[1]), .out2(decoded_rom_3[2]), .out3(decoded_rom_3[3]),
    .out4(decoded_rom_3[4]), .out5(decoded_rom_3[5]), .out6(decoded_rom_3[6]), .out7(decoded_rom_3[7]),
    .out8(decoded_rom_3[8]), .out9(decoded_rom_3[9]), .out10(decoded_rom_3[10]), .out11(decoded_rom_3[11]),
    .out12(decoded_rom_3[12]), .out13(decoded_rom_3[13]), .out14(decoded_rom_3[14]),
    .out15(decoded_rom_3[15]), .sel(rom_3_decode_instruction[3:0]), .en(not_6_out));
  Decoder #(.select(4)) decoder_7 (
    .out0(decoded_rom_3[16]), .out1(decoded_rom_3[17]), .out2(decoded_rom_3[18]), .out3(decoded_rom_3[19]),
    .out4(decoder_7_out4), .out5(decoder_7_out4), .out6(decoder_7_out4), .out7(decoder_7_out4),
    .out8(decoder_7_out4), .out9(decoder_7_out4), .out10(decoder_7_out4), .out11(decoder_7_out4),
    .out12(decoder_7_out4), .out13(decoder_7_out4), .out14(decoder_7_out4), .out15(decoder_7_out4),
    .sel(rom_3_decode_instruction[3:0]), .en(rom_3_decode_instruction[4]));

  assign mic_reset_out = decoded_rom_4[10];
  // also tied to GND on the sheet: {decoder_2_out4, decoder_3_out10, decoder_5_out10, decoder_7_out4, rom_2_decode_instruction[7], rom_4_decode_instruction[6]}

  // Other names for the same wires on the sheet: instruction_out[7:0] = cl_address_out[7:0];
  //   rom_1_decode_instruction[7:5] = decoded_rom_1[22:20];
  //   rom_2_decode_instruction[6:5] = {rom_2_decode_instruction[7], decoded_rom_2[26]};
  //   rom_3_decode_instruction[7:5] = decoded_rom_3[22:20]; mic_reset_rignal = decoded_rom_4[10];
  //   rom_4_decode_instruction (some bits) = {decoded_rom_4[10], rom_4_decode_instruction[6]}
endmodule

module sr (
  input  register_out,
  input  register_we,
  input  [7:0] buffer_in,
  input  clk,
  input  n_request,
  input  o_request,
  input  b_request,
  input  d_request,
  input  irq_reset,
  input  z_request,
  input  c_request,
  input  n_data,
  input  o_data,
  input  b_data,
  input  d_data,
  input  irq_data,
  input  z_data,
  input  c_data,
  input  n_we,
  input  o_we,
  input  b_we,
  input  d_we,
  input  irq_we,
  input  z_we,
  input  c_we,
  input  status_reset,
  output [7:0] buffer_out,
  output flag_serve_request,
  output carry_out,
  output bcd_mode,
  output irq_operation,
  output brk_flag
);

  wire and_1_out, and_2_out, and_6_out, or_1_out, or_2_out, or_3_out, or_4_out, or_5_out, or_6_out, or_7_out,
       or_8_out, or_9_out, or_10_out, or_11_out, or_12_out, or_13_out, or_14_out;
  wire [6:0] register_1_q;

  Register #(.width(1)) register_1 (.D(or_1_out), .en(or_2_out), .clk(clk), .Q(register_1_q[0]), .clr(status_reset));
  or or_1 (or_1_out, n_data, buffer_in[0]);
  or or_2 (or_2_out, n_we, register_we);
  Register #(.width(1)) register_2 (.D(or_3_out), .en(or_4_out), .clk(clk), .Q(register_1_q[1]), .clr(status_reset));
  or or_3 (or_3_out, o_data, buffer_in[1]);
  or or_4 (or_4_out, o_we, register_we);
  Register #(.width(1)) register_3 (.D(or_5_out), .en(or_6_out), .clk(clk), .Q(register_1_q[2]), .clr(status_reset));
  or or_5 (or_5_out, b_data, buffer_in[2]);
  or or_6 (or_6_out, b_we, register_we);
  Register #(.width(1)) register_4 (.D(or_7_out), .en(or_8_out), .clk(clk), .Q(register_1_q[3]), .clr(status_reset));
  or or_7 (or_7_out, d_data, buffer_in[3]);
  or or_8 (or_8_out, d_we, register_we);
  Register #(.width(1)) register_5 (.D(or_9_out), .en(or_10_out), .clk(clk), .Q(register_1_q[4]), .clr(status_reset));
  or or_9 (or_9_out, irq_data, buffer_in[4]);
  or or_10 (or_10_out, irq_we, register_we);
  Register #(.width(1)) register_6 (.D(or_11_out), .en(or_12_out), .clk(clk), .Q(register_1_q[5]), .clr(status_reset));
  or or_11 (or_11_out, z_data, buffer_in[5]);
  or or_12 (or_12_out, z_we, register_we);
  Register #(.width(1)) register_7 (.D(or_13_out), .en(or_14_out), .clk(clk), .Q(register_1_q[6]), .clr(status_reset));
  or or_13 (or_13_out, c_data, buffer_in[6]);
  or or_14 (or_14_out, c_we, register_we);
  assign buffer_out = register_out ? {1'b0, register_1_q} : 8'bz;  // Controlled_Buffer controlled_buffer_1
  and and_1 (and_1_out, register_1_q[0], n_request);
  and and_2 (and_2_out, register_1_q[1], o_request);
  and and_3 (brk_flag, register_1_q[2], b_request);
  and and_4 (bcd_mode, register_1_q[3], d_request);
  and and_5 (irq_operation, register_1_q[4], irq_reset);
  and and_6 (and_6_out, register_1_q[5], z_request);
  and and_7 (carry_out, register_1_q[6], c_request);
  or or_15 (flag_serve_request, and_1_out, and_2_out, brk_flag, bcd_mode, irq_operation, and_6_out, carry_out);
  // also tied to GND on the sheet: buffer_in[7]

  // Other names for the same wires on the sheet: irq_request = irq_reset
endmodule

module alu (
  input  clk,
  input  carry_in,
  input  decimal_in,
  input  [7:0] a_in,
  input  [7:0] b_in,
  input  a_we,
  input  b_we,
  input  lb_we,
  input  hb_we,
  input  direct_adr_out,
  input  address_bus_lb_oe,
  input  address_bus_oe,
  input  d_bus_oe,
  input  adc,
  input  sbc,
  input  and_op,
  input  or_op,
  input  xor_op,
  input  ror_op,
  input  rol_op,
  input  lsr,
  input  lsl,
  input  inc,
  input  dec,
  input  cmp,
  input  \bit ,
  input  mic_reset,
  output [7:0] buffer_out,
  output [15:0] address_out,
  output [3:0] status_update_sgn,
  output [3:0] status_update_data,
  output [15:0] direct_address_bus
);

  wire adder_1_cout, adder_2_cout, adder_3_cout, and_1_out, and_6_out, and_7_out, no_op_selected, not_1_out,
       not_2_out, not_3_out, not_4_out, not_5_out, not_6_out, not_7_out, not_8_out, not_9_out, not_10_out,
       not_11_out, not_12_out, not_13_out, not_14_out, not_15_out, not_16_out, not_17_out, not_18_out,
       not_19_out, not_20_out, not_21_out, not_22_out, not_23_out, or_1_out, or_2_out, or_4_out,
       subtractor_1_bout, subtractor_2_bout, subtractor_3_bout;
  wire [7:0] a_register, adder_1_out, adder_2_out, adder_3_out, and_5_out, b_register,
       controlled_buffer_1_out, controlled_buffer_2_out, controlled_buffer_4_out, controlled_buffer_5_out,
       controlled_buffer_6_out, controlled_buffer_7_out, controlled_buffer_16_out, controlled_buffer_17_out,
       controlled_buffer_18_out, controlled_buffer_19_out, controlled_buffer_20_out,
       controlled_buffer_21_out, controlled_buffer_22_out, controlled_buffer_23_out,
       controlled_buffer_24_out, controlled_buffer_25_out, controlled_buffer_26_out, hb_register, hb_resoult,
       lb_register, lb_resoult, or_3_out, register_1_q, resoult, result_register_q, subtractor_1_out,
       subtractor_2_out, subtractor_3_out, xor_1_out;

  Register a (.D(a_in), .en(a_we), .clk(clk), .Q(a_register), .clr(mic_reset));
  Register b (.D(b_in), .en(b_we), .clk(clk), .Q(b_register), .clr(mic_reset));
  assign controlled_buffer_1_out = ror_op ? a_register : 8'bz;  // Controlled_Buffer controlled_buffer_1
  and and_1 (and_1_out, adc, carry_in);
  assign controlled_buffer_2_out = inc ? 8'h1 : 8'bz;  // Controlled_Buffer controlled_buffer_2
  assign controlled_buffer_2_out = adc ? a_register : 8'bz;  // Controlled_Buffer controlled_buffer_3
  assign controlled_buffer_4_out = or_2_out ? b_register : 8'bz;  // Controlled_Buffer controlled_buffer_4
  and and_2 (status_update_data[3], adc, adder_1_cout);
  assign controlled_buffer_5_out = sbc ? a_register : 8'bz;  // Controlled_Buffer controlled_buffer_5
  assign controlled_buffer_6_out = sbc ? b_register : 8'bz;  // Controlled_Buffer controlled_buffer_6
  and and_3 (status_update_data[3], sbc, subtractor_1_bout);
  assign controlled_buffer_7_out = rol_op ? a_register : 8'bz;  // Controlled_Buffer controlled_buffer_7
  assign resoult = or_2_out ? adder_1_out : 8'bz;  // Controlled_Buffer controlled_buffer_8
  Adder adder_1 (
    .a(controlled_buffer_2_out), .b(controlled_buffer_4_out), .out(adder_1_out), .cin(and_1_out),
    .cout(adder_1_cout));
  assign resoult = sbc ? subtractor_1_out : 8'bz;  // Controlled_Buffer controlled_buffer_9
  Subtractor subtractor_1 (
    .a(controlled_buffer_5_out), .b(controlled_buffer_6_out), .out(subtractor_1_out), .bin(carry_in),
    .bout(subtractor_1_bout));
  assign lb_resoult = or_1_out ? adder_2_out : 8'bz;  // Controlled_Buffer controlled_buffer_10
  Adder adder_2 (.a(lb_register), .b(a_register), .out(adder_2_out), .cin(1'b0), .cout(adder_2_cout));
  or or_1 (or_1_out, address_bus_oe, address_bus_lb_oe);
  assign hb_resoult = address_bus_oe ? adder_3_out : 8'bz;  // Controlled_Buffer controlled_buffer_11
  Adder adder_3 (.a(hb_register), .b({8{1'b0}}), .out(adder_3_out), .cin(adder_2_cout), .cout(adder_3_cout));
  assign hb_resoult = address_bus_lb_oe ? {8{1'b0}} : 8'bz;  // Controlled_Buffer controlled_buffer_12
  Subtractor subtractor_2 (
    .a(a_register), .b(b_register), .out(subtractor_2_out), .bin(1'b0), .bout(subtractor_2_bout));
  or or_2 (or_2_out, adc, inc);
  assign resoult = ror_op ? {controlled_buffer_1_out[0], controlled_buffer_1_out[7:1]} : 8'bz;  // Controlled_Buffer controlled_buffer_13
  assign resoult = rol_op ? {controlled_buffer_7_out[6:0], controlled_buffer_7_out[7]} : 8'bz;  // Controlled_Buffer controlled_buffer_14
  assign resoult = cmp ? subtractor_2_out : 8'bz;  // Controlled_Buffer controlled_buffer_15
  Register lb (.D(b_in), .en(lb_we), .clk(clk), .Q(lb_register), .clr(mic_reset));
  Register hb (.D(b_in), .en(hb_we), .clk(clk), .Q(hb_register), .clr(mic_reset));
  Register register_1 (.D(resoult), .en(not_1_out), .clk(not_2_out), .Q(register_1_q));  // open: clr
  not not_1 (not_1_out, no_op_selected);
  not not_2 (not_2_out, clk);
  assign controlled_buffer_16_out = lsr ? a_register : 8'bz;  // Controlled_Buffer controlled_buffer_16
  assign controlled_buffer_17_out = lsl ? a_register : 8'bz;  // Controlled_Buffer controlled_buffer_17
  assign controlled_buffer_18_out = and_op ? a_register : 8'bz;  // Controlled_Buffer controlled_buffer_18
  assign controlled_buffer_19_out = and_op ? b_register : 8'bz;  // Controlled_Buffer controlled_buffer_19
  assign controlled_buffer_20_out = or_op ? a_register : 8'bz;  // Controlled_Buffer controlled_buffer_20
  assign controlled_buffer_21_out = or_op ? b_register : 8'bz;  // Controlled_Buffer controlled_buffer_21
  assign controlled_buffer_22_out = xor_op ? a_register : 8'bz;  // Controlled_Buffer controlled_buffer_22
  assign controlled_buffer_23_out = xor_op ? b_register : 8'bz;  // Controlled_Buffer controlled_buffer_23
  and and_4 (status_update_data[3], lsl, controlled_buffer_17_out[7]);
  assign controlled_buffer_24_out = dec ? a_register : 8'bz;  // Controlled_Buffer controlled_buffer_24
  assign controlled_buffer_25_out = dec ? 8'h1 : 8'bz;  // Controlled_Buffer controlled_buffer_25
  assign controlled_buffer_26_out = d_bus_oe ? register_1_q : 8'bz;  // Controlled_Buffer controlled_buffer_26
  assign and_5_out = controlled_buffer_18_out & controlled_buffer_19_out;  // AND_Gate and_5, 8 bits wide
  assign resoult = and_op ? and_5_out : 8'bz;  // Controlled_Buffer controlled_buffer_27
  assign or_3_out = controlled_buffer_20_out | controlled_buffer_21_out;  // OR_Gate or_3, 8 bits wide
  assign resoult = or_op ? or_3_out : 8'bz;  // Controlled_Buffer controlled_buffer_28
  assign xor_1_out = controlled_buffer_22_out ^ controlled_buffer_23_out;  // XOR_Gate xor_1, 8 bits wide
  assign resoult = xor_op ? xor_1_out : 8'bz;  // Controlled_Buffer controlled_buffer_29
  Subtractor subtractor_3 (
    .a(controlled_buffer_24_out), .b(controlled_buffer_25_out), .out(subtractor_3_out), .bin(1'b0),
    .bout(subtractor_3_bout));
  not not_3 (not_3_out, controlled_buffer_26_out[0]);
  not not_4 (not_4_out, controlled_buffer_26_out[1]);
  not not_5 (not_5_out, controlled_buffer_26_out[2]);
  not not_6 (not_6_out, controlled_buffer_26_out[3]);
  not not_7 (not_7_out, controlled_buffer_26_out[4]);
  not not_8 (not_8_out, controlled_buffer_26_out[5]);
  not not_9 (not_9_out, controlled_buffer_26_out[6]);
  not not_10 (not_10_out, controlled_buffer_26_out[7]);
  assign resoult = lsr ? {1'b0, controlled_buffer_16_out[7:1]} : 8'bz;  // Controlled_Buffer controlled_buffer_30
  assign resoult = lsl ? {controlled_buffer_17_out[6:0], 1'b0} : 8'bz;  // Controlled_Buffer controlled_buffer_31
  assign resoult = dec ? subtractor_3_out : 8'bz;  // Controlled_Buffer controlled_buffer_32
  and and_6 (and_6_out, not_6_out, not_3_out, not_4_out, not_5_out, not_7_out, not_8_out, not_9_out, not_10_out);
  and and_7 (and_7_out, controlled_buffer_26_out[0], controlled_buffer_26_out[1], controlled_buffer_26_out[2], controlled_buffer_26_out[3], controlled_buffer_26_out[4], controlled_buffer_26_out[5], controlled_buffer_26_out[6], controlled_buffer_26_out[7]);
  and and_8 (status_update_data[1], controlled_buffer_26_out[7], 1'b0);
  and and_9 (status_update_data[0], and_6_out, 1'b0);
  and and_10 (status_update_data[2], 1'b0, and_7_out);
  Register result_register (.D(resoult), .en(not_11_out), .clk(not_12_out), .Q(result_register_q));  // open: clr
  not not_11 (not_11_out, no_op_selected);
  not not_12 (not_12_out, clk);
  or or_4 (or_4_out, address_bus_lb_oe, address_bus_oe);
  not not_13 (not_13_out, adc);
  not not_14 (not_14_out, sbc);
  not not_15 (not_15_out, and_op);
  not not_16 (not_16_out, or_op);
  not not_17 (not_17_out, xor_op);
  not not_18 (not_18_out, ror_op);
  not not_19 (not_19_out, rol_op);
  not not_20 (not_20_out, lsr);
  not not_21 (not_21_out, lsl);
  not not_22 (not_22_out, inc);
  not not_23 (not_23_out, dec);
  assign buffer_out = d_bus_oe ? result_register_q : 8'bz;  // Controlled_Buffer controlled_buffer_33
  assign address_out = or_4_out ? {hb_resoult, lb_resoult} : 16'bz;  // Controlled_Buffer controlled_buffer_34
  assign direct_address_bus = direct_adr_out ? {hb_resoult, lb_resoult} : 16'bz;  // Controlled_Buffer controlled_buffer_35
  and and_11 (no_op_selected, not_23_out, not_13_out, not_14_out, not_15_out, not_16_out, not_21_out, not_17_out, not_18_out, not_19_out, not_20_out, not_22_out);

  assign status_update_sgn = status_update_data;
  // also tied to GND on the sheet: {adder_3_cout, subtractor_2_bout, controlled_buffer_16_out[0], subtractor_3_bout}

  // Other names for the same wires on the sheet: adc_op = adc; bit_op = \bit ; cmp_op = cmp; dec_op = dec;
  //   inc_op = inc; hb_in[7:0] = b_in; lb_in[7:0] = b_in; lsl_op = lsl; lsr_op = lsr; sbc_op = sbc;
  //   status_data[3:0] = status_update_data; status_update[3:0] = status_update_data;
  //   zero_flag = status_update_data[0]; zero_update = status_update_data[0]; negative = status_update_data[1];
  //   negative_update = status_update_data[1]; overflow = status_update_data[2];
  //   overflow_update = status_update_data[2]; carry_out = status_update_data[3];
  //   carry_update = status_update_data[3]
endmodule

module cu_sng_adapter (
  input  [22:0] decoded_cl_1,
  input  [26:0] decoded_cl_2,
  input  [22:0] decoded_cl_3,
  input  [10:0] in_4,
  output lb_dlatch_we,
  output hb_dlatch_we,
  output lb_dlatch_oe,
  output hb_dlatch_oe,
  output lb_latch_oe_adr,
  output dlatch_oe_adr,
  output status_to_bus,
  output status_we,
  output carry_update,
  output interrupt_update,
  output decimal_update,
  output overflow_update,
  output carry_data,
  output interrupt_data,
  output decimal_data,
  output overflow_data,
  output isr_we,
  output cpu_data_in,
  output cpu_data_out,
  output pcl_pch_load,
  output we_pcl,
  output we_pch,
  output bus_oe_pcl,
  output bus_oe_pch,
  output pc_count,
  output pc_enable,
  output pc_oe,
  output sp_enable,
  output sp_oe,
  output sp_command,
  output sp_we,
  output sp_dec_pcl_bus,
  output sp_dec_pch_bus,
  output sp_inc_pcl_we,
  output sp_inc_pch_we,
  output sp_oe_pcl_bus,
  output sp_oe_pch_bus,
  output load_alu_address,
  output save_address,
  output load_saved_address,
  output adc,
  output sbc,
  output and_op,
  output or_op,
  output xor_op,
  output lsl,
  output lsr,
  output rol_op,
  output ror_op,
  output \bit ,
  output cmp,
  output inc,
  output dec,
  output address_clc,
  output bus_oe,
  output address_oe,
  output address_oe_lb,
  output we_a_alu,
  output we_b_alu,
  output direct_adr_out,
  output lb_we,
  output hb_we,
  output oe_x,
  output we_x,
  output oe_y,
  output we_y,
  output oe_a,
  output we_a,
  output oe_x_alu,
  output oe_y_alu,
  output oe_a_alu,
  output mic_reset,
  output pc_direct_load,
  output break_update,
  output break_data,
  output status_reset
);

  or or_1 (pc_count, decoded_cl_2[24], decoded_cl_2[6], decoded_cl_2[25], decoded_cl_2[21], decoded_cl_2[26]);
  or or_2 (carry_update, decoded_cl_1[9], decoded_cl_1[13]);
  or or_3 (interrupt_update, decoded_cl_1[10], decoded_cl_1[14]);
  or or_4 (decimal_update, decoded_cl_1[11], decoded_cl_1[15]);
  or or_5 (overflow_update, decoded_cl_1[12], decoded_cl_1[16]);
  or or_6 (carry_data, decoded_cl_1[9], 1'b0);
  or or_7 (interrupt_data, decoded_cl_1[10], 1'b0);
  or or_8 (decimal_data, decoded_cl_1[11], 1'b0);
  or or_9 (overflow_data, decoded_cl_1[12], 1'b0);
  or or_10 (we_pcl, decoded_cl_2[2], decoded_cl_2[21]);
  or or_11 (we_pch, decoded_cl_2[3], decoded_cl_2[26], decoded_cl_2[22]);
  or or_12 (bus_oe_pcl, decoded_cl_2[4], decoded_cl_2[24]);
  or or_13 (bus_oe_pch, decoded_cl_2[5], decoded_cl_2[25]);
  or or_14 (pc_oe, pc_count, decoded_cl_2[22], decoded_cl_2[7]);
  or or_15 (sp_enable, decoded_cl_2[10], decoded_cl_2[9]);
  or or_16 (break_update, decoded_cl_1[17], decoded_cl_1[18]);
  or or_17 (break_data, decoded_cl_1[17], 1'b0);
  or or_18 (sp_command, decoded_cl_2[9], 1'b0);

  assign adc = decoded_cl_3[1];
  assign address_clc = decoded_cl_3[14];
  assign address_oe = decoded_cl_3[16];
  assign address_oe_lb = decoded_cl_3[17];
  assign and_op = decoded_cl_3[3];
  assign \bit  = decoded_cl_3[10];
  assign bus_oe = decoded_cl_3[15];
  assign cmp = decoded_cl_3[11];
  assign cpu_data_in = decoded_cl_1[21];
  assign cpu_data_out = decoded_cl_1[22];
  assign dec = decoded_cl_3[13];
  assign direct_adr_out = decoded_cl_3[22];
  assign dlatch_oe_adr = decoded_cl_1[6];
  assign hb_dlatch_oe = decoded_cl_1[4];
  assign hb_dlatch_we = decoded_cl_1[2];
  assign hb_we = decoded_cl_3[19];
  assign inc = decoded_cl_3[12];
  assign isr_we = decoded_cl_1[20];
  assign lb_dlatch_oe = decoded_cl_1[3];
  assign lb_dlatch_we = decoded_cl_1[1];
  assign lb_latch_oe_adr = decoded_cl_1[5];
  assign lb_we = decoded_cl_3[18];
  assign load_alu_address = decoded_cl_2[18];
  assign load_saved_address = decoded_cl_2[20];
  assign lsl = decoded_cl_3[6];
  assign lsr = decoded_cl_3[7];
  assign mic_reset = in_4[10];
  assign oe_a = in_4[5];
  assign oe_a_alu = in_4[9];
  assign oe_x = in_4[1];
  assign oe_x_alu = in_4[7];
  assign oe_y = in_4[3];
  assign oe_y_alu = in_4[8];
  assign or_op = decoded_cl_3[4];
  assign pc_direct_load = decoded_cl_2[23];
  assign pc_enable = pc_count;
  assign pcl_pch_load = decoded_cl_2[1];
  assign rol_op = decoded_cl_3[8];
  assign ror_op = decoded_cl_3[9];
  assign save_address = decoded_cl_2[19];
  assign sbc = decoded_cl_3[2];
  assign sp_dec_pch_bus = decoded_cl_2[13];
  assign sp_dec_pcl_bus = decoded_cl_2[12];
  assign sp_inc_pch_we = decoded_cl_2[15];
  assign sp_inc_pcl_we = decoded_cl_2[14];
  assign sp_oe = decoded_cl_2[8];
  assign sp_oe_pch_bus = decoded_cl_2[17];
  assign sp_oe_pcl_bus = decoded_cl_2[16];
  assign sp_we = decoded_cl_2[11];
  assign status_reset = decoded_cl_1[19];
  assign status_to_bus = decoded_cl_1[7];
  assign status_we = decoded_cl_1[8];
  assign we_a = in_4[6];
  assign we_a_alu = decoded_cl_3[20];
  assign we_b_alu = decoded_cl_3[21];
  assign we_x = in_4[2];
  assign we_y = in_4[4];
  assign xor_op = decoded_cl_3[5];
  // also tied to GND on the sheet: {decoded_cl_1[0], decoded_cl_2[0], decoded_cl_3[0], in_4[0]}

  // Other names for the same wires on the sheet: lb_dlatch_adr = decoded_cl_1[5]; dlatch_adr = decoded_cl_1[6];
  //   carry_set = decoded_cl_1[9]; interrupt_set = decoded_cl_1[10]; decimal_set = decoded_cl_1[11];
  //   overflow_set = decoded_cl_1[12]; carry_clear = decoded_cl_1[13]; interrupt_clear = decoded_cl_1[14];
  //   decimal_clear = decoded_cl_1[15]; overflow_clear = decoded_cl_1[16]; break_set = decoded_cl_1[17];
  //   break_clear = decoded_cl_1[18]; pcl_load = decoded_cl_2[1]; we_pcl_t = decoded_cl_2[2];
  //   we_pch_t = decoded_cl_2[3]; bus_oe_pcl_t = decoded_cl_2[4]; bus_oe_pch_t = decoded_cl_2[5];
  //   pc_count_t = decoded_cl_2[6]; pc_oe_t = decoded_cl_2[7]; sp_inc = decoded_cl_2[9]; sp_dec = decoded_cl_2[10];
  //   sp_inc_pch_we_t = decoded_cl_2[14]; sp_inc_pcl_we_t = decoded_cl_2[15]; sp_oe_pch_bus_t = decoded_cl_2[16];
  //   sp_oe_pcl_bus_t = decoded_cl_2[17]; pc_count_pcl_load = decoded_cl_2[21]; pc_oe_pch_load = decoded_cl_2[22];
  //   pc_count_pcl_oe = decoded_cl_2[24]; pc_count_pch_oe = decoded_cl_2[25]; pc_count_pch_load = decoded_cl_2[26];
  //   sbs = decoded_cl_3[2]
endmodule

module test (
  input  power,
  input  irq,
  input  nmi,
  input  reset
);

  wire and_2_out, clk, not_1_out, not_2_out, not_3_out, not_4_out, w_r;
  wire [7:0] controlled_buffer_1_out, main_1_data_bus_out, ram_1_dout, rom_1_data;
  wire [15:0] main_1_address_bus;

  Clock clock_1 (.out(clk));
  main main_1 (
    .power(power), .buffer_in(controlled_buffer_1_out), .clk(clk), .irq(irq), .nmi(nmi), .reset(reset),
    .w_r(w_r), .data_bus_out(main_1_data_bus_out), .address_bus(main_1_address_bus));
  not not_1 (not_1_out, main_1_address_bus[15]);
  // AND_Gate and_1 has open pins: in0=not_1_out, in1=main_1_address_bus[14], out=open
  not not_2 (not_2_out, main_1_address_bus[14]);
  not not_3 (not_3_out, main_1_address_bus[15]);
  and and_2 (and_2_out, not_2_out, not_3_out);
  ROM #(.addrWidth(16)) rom_1 (.addr(main_1_address_bus), .data(rom_1_data));
  assign controlled_buffer_1_out = main_1_address_bus[15] ? rom_1_data : 8'bz;  // Controlled_Buffer controlled_buffer_1
  RAM #(.addrWidth(16), .enables("line")) ram_1 (
    .addr(main_1_address_bus), .we(not_4_out), .clk(clk), .din(main_1_data_bus_out), .dout(ram_1_dout));
  not not_4 (not_4_out, w_r);
  assign controlled_buffer_1_out = and_2_out ? ram_1_dout : 8'bz;  // Controlled_Buffer controlled_buffer_2
endmodule
